// Logisim project minirv.circ as structural Verilog: 1 circuit, main circuit main
module main (
  input  [9:0] in_1,
  input  Enable,
  input  [9:0] in_3,
  input  [31:0] in_4,
  input  RESET,
  input  [31:0] in_6
);

  wire and_1_out, clock_1_out, comparator_1_eq, comparator_2_eq, decoder_1_out0, decoder_1_out1,
       decoder_1_out2, decoder_1_out3, decoder_1_out4, decoder_1_out5, decoder_1_out6, decoder_1_out7,
       decoder_1_out8, decoder_1_out9, decoder_1_out10, decoder_1_out11, decoder_1_out12, decoder_1_out13,
       decoder_1_out14, decoder_1_out15, not_1_out, or_1_out;
  wire [0:0] adder_3_out;
  wire [31:0] adder_1_out, adder_2_out, bit_extender_1_out, multiplexer_1_out, multiplexer_2_out,
       multiplexer_3_out, multiplexer_4_out, register_1_q, register_2_q, register_3_q, register_4_q,
       register_5_q, register_6_q, register_7_q, register_8_q, register_9_q, register_10_q, register_11_q,
       register_12_q, register_13_q, register_14_q, register_15_q, register_16_q, register_17_q, rom_1_data;
  wire [31:1] adder_3_out_2;

  Multiplexer #(.width(32)) multiplexer_1 (
    .in0(adder_1_out), .in1(multiplexer_3_out), .out(multiplexer_1_out), .sel(comparator_1_eq), .en(Enable));
  Clock clock_1 (.out(clock_1_out));
  Register #(.width(32)) register_1 (
    .D(multiplexer_1_out), .en(Enable), .Q(register_1_q), .clk(clock_1_out), .clr(RESET));
  Adder #(.width(32)) adder_1 (.a(register_1_q), .b(in_4), .out(adder_1_out), .cin(1'b0));  // open: cout
  Adder #(.width(32)) adder_2 (.a(register_1_q), .b(in_6), .out(adder_2_out), .cin(1'b0));  // open: cout
  ROM #(.addrWidth(4), .dataWidth(32)) rom_1 (.addr(register_1_q[5:2]), .data(rom_1_data), .sel(1'b1));
  Decoder #(.select(5)) decoder_1 (
    .out0(decoder_1_out0), .out1(decoder_1_out1), .out2(decoder_1_out2), .out3(decoder_1_out3),
    .out4(decoder_1_out4), .out5(decoder_1_out5), .out6(decoder_1_out6), .out7(decoder_1_out7),
    .out8(decoder_1_out8), .out9(decoder_1_out9), .out10(decoder_1_out10), .out11(decoder_1_out11),
    .out12(decoder_1_out12), .out13(decoder_1_out13), .out14(decoder_1_out14), .out15(decoder_1_out15),
    .sel(rom_1_data[11:7]), .en(or_1_out));  // open: out16, out17, out18, out19, out20, out21, out22, out23, out24, out25, out26, out27, out28, out29, out30, out31
  assign bit_extender_1_out = {{20{1'b0}}, rom_1_data[31:20]};  // Bit_Extender bit_extender_1
  Comparator #(.width(10)) comparator_1 (
    .a({rom_1_data[14:12], rom_1_data[6:0]}), .b(in_1), .eq(comparator_1_eq));  // open: gt, lt
  Comparator #(.width(10)) comparator_2 (
    .a({rom_1_data[14:12], rom_1_data[6:0]}), .b(in_3), .eq(comparator_2_eq));  // open: gt, lt
  not not_1 (not_1_out, comparator_1_eq);
  and and_1 (and_1_out, comparator_2_eq, not_1_out);
  Multiplexer #(.width(32), .enable("false")) multiplexer_2 (
    .in0(adder_2_out), .in1({adder_3_out_2, adder_3_out[0]}), .out(multiplexer_2_out), .sel(and_1_out));
  Register #(.width(32)) register_2 (.en(decoder_1_out0), .Q(register_2_q), .clr(RESET));  // open: D, clk
  Register #(.width(32)) register_3 (
    .D(multiplexer_2_out), .en(decoder_1_out1), .Q(register_3_q), .clk(clock_1_out), .clr(RESET));
  Register #(.width(32)) register_4 (
    .D(multiplexer_2_out), .en(decoder_1_out2), .Q(register_4_q), .clk(clock_1_out), .clr(RESET));
  Register #(.width(32)) register_5 (
    .D(multiplexer_2_out), .en(decoder_1_out3), .Q(register_5_q), .clk(clock_1_out), .clr(RESET));
  Register #(.width(32)) register_6 (
    .D(multiplexer_2_out), .en(decoder_1_out4), .Q(register_6_q), .clk(clock_1_out), .clr(RESET));
  Register #(.width(32)) register_7 (
    .D(multiplexer_2_out), .en(decoder_1_out5), .Q(register_7_q), .clk(clock_1_out), .clr(RESET));
  Register #(.width(32)) register_8 (
    .D(multiplexer_2_out), .en(decoder_1_out6), .Q(register_8_q), .clk(clock_1_out), .clr(RESET));
  Register #(.width(32)) register_9 (
    .D(multiplexer_2_out), .en(decoder_1_out7), .Q(register_9_q), .clk(clock_1_out), .clr(RESET));
  Register #(.width(32)) register_10 (
    .D(multiplexer_2_out), .en(decoder_1_out8), .Q(register_10_q), .clk(clock_1_out), .clr(RESET));
  Register #(.width(32)) register_11 (
    .D(multiplexer_2_out), .en(decoder_1_out9), .Q(register_11_q), .clk(clock_1_out), .clr(RESET));
  Register #(.width(32)) register_12 (
    .D(multiplexer_2_out), .en(decoder_1_out10), .Q(register_12_q), .clk(clock_1_out), .clr(RESET));
  Register #(.width(32)) register_13 (
    .D(multiplexer_2_out), .en(decoder_1_out11), .Q(register_13_q), .clk(clock_1_out), .clr(RESET));
  Register #(.width(32)) register_14 (
    .D(multiplexer_2_out), .en(decoder_1_out12), .Q(register_14_q), .clk(clock_1_out), .clr(RESET));
  Register #(.width(32)) register_15 (
    .D(multiplexer_2_out), .en(decoder_1_out13), .Q(register_15_q), .clk(clock_1_out), .clr(RESET));
  Register #(.width(32)) register_16 (
    .D(multiplexer_2_out), .en(decoder_1_out14), .Q(register_16_q), .clk(clock_1_out), .clr(RESET));
  Register #(.width(32)) register_17 (
    .D(multiplexer_2_out), .en(decoder_1_out15), .Q(register_17_q), .clk(clock_1_out), .clr(RESET));
  Multiplexer #(.width(32)) multiplexer_3 (
    .in0({adder_3_out_2, 1'b0}), .in1(multiplexer_4_out), .out(multiplexer_3_out), .sel(register_1_q[5]),
    .en(comparator_1_eq));
  or or_1 (or_1_out, comparator_1_eq, comparator_2_eq);
  // Probe on register_3_q
  // Probe on register_4_q
  Multiplexer #(.select(5), .width(32)) multiplexer_4 (
    .in0(register_2_q), .in1(register_3_q), .in2(register_4_q), .in3(register_5_q), .in4(register_6_q),
    .in5(register_7_q), .in6(register_8_q), .in7(register_9_q), .in8(register_10_q), .in9(register_11_q),
    .in10(register_12_q), .in11(register_13_q), .in12(register_14_q), .in13(register_15_q),
    .in14(register_16_q), .in15(register_17_q), .out(multiplexer_4_out), .sel(rom_1_data[19:15]),
    .en(or_1_out));  // open: in16, in17, in18, in19, in20, in21, in22, in23, in24, in25, in26, in27, in28, in29, in30, in31
  Adder #(.width(32)) adder_3 (
    .a(bit_extender_1_out), .b(multiplexer_4_out), .out({adder_3_out_2, adder_3_out[0]}), .cin(1'b0));  // open: cout

  // Notes on the sheet:
  //   PC
  //   contents of rom_1 (hex, n*v repeats v):
  //   1400513 10000e7 c000e7 c00067 a50513 8067
  //   rd
  //   rs1
  //   JALR
  //   ADDI
endmodule
