// Logisim project minirv_new.circ as structural Verilog: 7 circuits, main circuit two_instructions
module two_instructions (
  input  ENABLE,
  input  [31:0] in_2,
  input  [15:0] ADDI,
  input  RESET,
  input  [15:0] in_5,
  input  [31:0] in_6
);

  wire and_1_out, clock_1_out, comparator_1_eq, comparator_2_eq, decoder_1_out0, decoder_1_out1,
       decoder_1_out2, decoder_1_out3, decoder_1_out4, decoder_1_out5, decoder_1_out6, decoder_1_out7,
       decoder_1_out8, decoder_1_out9, decoder_1_out10, decoder_1_out11, decoder_1_out12, decoder_1_out13,
       decoder_1_out14, decoder_1_out15, not_1_out, or_1_out;
  wire [31:0] add_signed_1_out1, adder_1_out, adder_2_out, multiplexer_1_out, multiplexer_2_out,
       multiplexer_3_out, multiplexer_4_out, register_1_q, register_2_q, register_3_q, register_4_q,
       register_5_q, register_6_q, register_7_q, register_8_q, register_9_q, register_10_q, register_11_q,
       register_12_q, register_13_q, register_14_q, register_15_q, register_16_q, register_17_q, rom_1_data;

  Multiplexer #(.enable("true"), .width(32)) multiplexer_1 (
    .in0(adder_2_out), .in1(multiplexer_3_out), .out(multiplexer_1_out), .sel(comparator_1_eq), .en(ENABLE));
  Clock clock_1 (.out(clock_1_out));
  Register #(.width(32)) register_1 (
    .D(multiplexer_1_out), .en(ENABLE), .clk(clock_1_out), .Q(register_1_q), .clr(RESET));
  ROM #(.addrWidth(4), .dataWidth(32)) rom_1 (.addr(register_1_q[5:2]), .data(rom_1_data));
  Adder #(.width(32)) adder_1 (.a(register_1_q), .b(in_6), .out(adder_1_out), .cin(1'b0));  // open: cout
  Adder #(.width(32)) adder_2 (.a(register_1_q), .b(in_2), .out(adder_2_out), .cin(1'b0));  // open: cout
  Decoder #(.select(5)) decoder_1 (
    .out0(decoder_1_out0), .out1(decoder_1_out1), .out2(decoder_1_out2), .out3(decoder_1_out3),
    .out4(decoder_1_out4), .out5(decoder_1_out5), .out6(decoder_1_out6), .out7(decoder_1_out7),
    .out8(decoder_1_out8), .out9(decoder_1_out9), .out10(decoder_1_out10), .out11(decoder_1_out11),
    .out12(decoder_1_out12), .out13(decoder_1_out13), .out14(decoder_1_out14), .out15(decoder_1_out15),
    .sel(rom_1_data[11:7]), .en(or_1_out));  // open: out16, out17, out18, out19, out20, out21, out22, out23, out24, out25, out26, out27, out28, out29, out30, out31
  Comparator #(.width(16)) comparator_1 (
    .a({{6{1'b0}}, rom_1_data[14:12], rom_1_data[6:0]}), .b(ADDI), .eq(comparator_1_eq));  // open: gt, lt
  Comparator #(.width(16)) comparator_2 (
    .a({{6{1'b0}}, rom_1_data[14:12], rom_1_data[6:0]}), .b(in_5), .eq(comparator_2_eq));  // open: gt, lt
  and and_1 (and_1_out, comparator_2_eq, not_1_out);
  not not_1 (not_1_out, comparator_1_eq);
  Multiplexer #(.width(32)) multiplexer_2 (
    .in0(adder_1_out), .in1(add_signed_1_out1), .out(multiplexer_2_out), .sel(and_1_out));
  Register #(.width(32)) register_2 (
    .D({32{1'b0}}), .en(decoder_1_out0), .clk(clock_1_out), .Q(register_2_q), .clr(RESET));
  Register #(.width(32)) register_3 (
    .D(multiplexer_2_out), .en(decoder_1_out1), .clk(clock_1_out), .Q(register_3_q), .clr(RESET));
  Register #(.width(32)) register_4 (
    .D(multiplexer_2_out), .en(decoder_1_out2), .clk(clock_1_out), .Q(register_4_q), .clr(RESET));
  Register #(.width(32)) register_5 (
    .D(multiplexer_2_out), .en(decoder_1_out3), .clk(clock_1_out), .Q(register_5_q), .clr(RESET));
  Register #(.width(32)) register_6 (
    .D(multiplexer_2_out), .en(decoder_1_out4), .clk(clock_1_out), .Q(register_6_q), .clr(RESET));
  Register #(.width(32)) register_7 (
    .D(multiplexer_2_out), .en(decoder_1_out5), .clk(clock_1_out), .Q(register_7_q), .clr(RESET));
  Register #(.width(32)) register_8 (
    .D(multiplexer_2_out), .en(decoder_1_out6), .clk(clock_1_out), .Q(register_8_q), .clr(RESET));
  Register #(.width(32)) register_9 (
    .D(multiplexer_2_out), .en(decoder_1_out7), .clk(clock_1_out), .Q(register_9_q), .clr(RESET));
  Register #(.width(32)) register_10 (
    .D(multiplexer_2_out), .en(decoder_1_out8), .clk(clock_1_out), .Q(register_10_q), .clr(RESET));
  Register #(.width(32)) register_11 (
    .D(multiplexer_2_out), .en(decoder_1_out9), .clk(clock_1_out), .Q(register_11_q), .clr(RESET));
  Register #(.width(32)) register_12 (
    .D(multiplexer_2_out), .en(decoder_1_out10), .clk(clock_1_out), .Q(register_12_q), .clr(RESET));
  Register #(.width(32)) register_13 (
    .D(multiplexer_2_out), .en(decoder_1_out11), .clk(clock_1_out), .Q(register_13_q), .clr(RESET));
  Register #(.width(32)) register_14 (
    .D(multiplexer_2_out), .en(decoder_1_out12), .clk(clock_1_out), .Q(register_14_q), .clr(RESET));
  Register #(.width(32)) register_15 (
    .D(multiplexer_2_out), .en(decoder_1_out13), .clk(clock_1_out), .Q(register_15_q), .clr(RESET));
  Register #(.width(32)) register_16 (
    .D(multiplexer_2_out), .en(decoder_1_out14), .clk(clock_1_out), .Q(register_16_q), .clr(RESET));
  Register #(.width(32)) register_17 (
    .D(multiplexer_2_out), .en(decoder_1_out15), .clk(clock_1_out), .Q(register_17_q), .clr(RESET));
  or or_1 (or_1_out, comparator_1_eq, comparator_2_eq);
  Multiplexer #(.enable("true"), .width(32)) multiplexer_3 (
    .in0({add_signed_1_out1[31:1], 1'b0}), .in1(multiplexer_4_out), .out(multiplexer_3_out),
    .sel(register_1_q[5]), .en(comparator_1_eq));
  Multiplexer #(.enable("true"), .select(5), .width(32)) multiplexer_4 (
    .in0(register_2_q), .in1(register_3_q), .in2(register_4_q), .in3(register_5_q), .in4(register_6_q),
    .in5(register_7_q), .in6(register_8_q), .in7(register_9_q), .in8(register_10_q), .in9(register_11_q),
    .in10(register_12_q), .in11(register_13_q), .in12(register_14_q), .in13(register_15_q),
    .in14(register_16_q), .in15(register_17_q), .out(multiplexer_4_out), .sel(rom_1_data[19:15]),
    .en(or_1_out));  // open: in16, in17, in18, in19, in20, in21, in22, in23, in24, in25, in26, in27, in28, in29, in30, in31
  // Probe on {rom_1_data[31], {20{1'b0}}, rom_1_data[30:20]}
  add_signed add_signed_1 (
    .IN1({rom_1_data[31], {20{1'b0}}, rom_1_data[30:20]}), .IN2(multiplexer_4_out), .OUT1(add_signed_1_out1));

  // Notes on the sheet:
  //   contents of rom_1 (hex, n*v repeats v):
  //   81400513 10000e7 c000e7 c00067 a50513 8067
  //   rd
  //   rs1
  //   JALR
endmodule

module plus_add_lui (
  input  ENABLE,
  input  RESET,
  input  [31:0] in_3
);

  wire clk_out, comparator_1_eq, comparator_2_eq, comparator_3_eq, comparator_4_eq, undriven_2;
  wire [4:0] decode_inst_1_rd, decode_inst_1_rs1;
  wire [15:0] decode_inst_1_instruction;
  wire [31:0] adder_1_out, decode_inst_1_lui_eimm20, multiplexer_1_out, pc_1_q, pc_1_q_plus4, rom_1_data,
       undriven;

  Clock clk (.out(clk_out));
  Multiplexer #(.enable("true"), .width(32)) multiplexer_1 (
    .in0(pc_1_q_plus4), .in1(undriven), .out(multiplexer_1_out), .sel(undriven_2), .en(ENABLE));
  PC pc_1 (.D(multiplexer_1_out), .ENABLE(ENABLE), .clk(clk_out), .Reset(RESET), .Q_plus4(pc_1_q_plus4), .Q(pc_1_q));
  ROM #(.addrWidth(4), .dataWidth(32)) rom_1 (.addr(pc_1_q[5:2]), .data(rom_1_data));
  Adder #(.width(32)) adder_1 (.a(pc_1_q), .b(in_3), .out(adder_1_out), .cin(1'b0));  // open: cout
  Decode_Inst decode_inst_1 (
    .in_1(rom_1_data), .instruction(decode_inst_1_instruction), .lui_Eimm20(decode_inst_1_lui_eimm20),
    .rd(decode_inst_1_rd), .rs1(decode_inst_1_rs1));  // open: rs2, lw_Eimm12, lbu_Eimm12, jalr_Eimm12, addi_Eimm12, sw_Eimm12, sb_Eimm12
  Comparator #(.width(16)) comparator_1 (
    .a(decode_inst_1_instruction), .b({16{1'b1}}), .eq(comparator_1_eq));  // open: gt, lt
  Comparator #(.width(16)) comparator_2 (
    .a(decode_inst_1_instruction), .b({16{1'b1}}), .eq(comparator_2_eq));  // open: gt, lt
  Comparator #(.width(16)) comparator_3 (
    .a(decode_inst_1_instruction), .b({16{1'b1}}), .eq(comparator_3_eq));  // open: gt, lt
  Comparator #(.width(16)) comparator_4 (
    .a(decode_inst_1_instruction), .b({16{1'b1}}), .eq(comparator_4_eq));  // open: gt, lt
  Register16 register16_1 (
    .Reset(RESET), .clk(clk_out));  // open: WData, WEnable, WSelect, Out_Enable, Out_Reg, Out_Data

  // Notes on the sheet:
  //   contents of rom_1 (hex, n*v repeats v):
  //   1400513 10000e7 c000e7 c00067 a50513 8067
  //   ADD
  //   JALR
  //   ADDI
  //   LUI
endmodule

module add_signed (
  input  [31:0] IN1,
  input  [31:0] IN2,
  output [31:0] OUT1
);

  wire [30:0] not_1_out, not_32_out, not_63_out;
  wire [31:0] adder_1_out, adder_2_out, adder_3_out, adder_4_out, multiplexer_1_out, multiplexer_2_out;

  not not_1 (not_1_out[0], IN1[0]);
  not not_2 (not_1_out[1], IN1[1]);
  not not_3 (not_1_out[2], IN1[2]);
  not not_4 (not_1_out[3], IN1[3]);
  not not_5 (not_1_out[4], IN1[4]);
  not not_6 (not_1_out[5], IN1[5]);
  not not_7 (not_1_out[6], IN1[6]);
  not not_8 (not_1_out[7], IN1[7]);
  not not_9 (not_1_out[8], IN1[8]);
  not not_10 (not_1_out[9], IN1[9]);
  not not_11 (not_1_out[10], IN1[10]);
  not not_12 (not_1_out[11], IN1[11]);
  not not_13 (not_1_out[12], IN1[12]);
  not not_14 (not_1_out[13], IN1[13]);
  not not_15 (not_1_out[14], IN1[14]);
  not not_16 (not_1_out[15], IN1[15]);
  not not_17 (not_1_out[16], IN1[16]);
  not not_18 (not_1_out[17], IN1[17]);
  not not_19 (not_1_out[18], IN1[18]);
  not not_20 (not_1_out[19], IN1[19]);
  not not_21 (not_1_out[20], IN1[20]);
  not not_22 (not_1_out[21], IN1[21]);
  not not_23 (not_1_out[22], IN1[22]);
  not not_24 (not_1_out[23], IN1[23]);
  not not_25 (not_1_out[24], IN1[24]);
  not not_26 (not_1_out[25], IN1[25]);
  not not_27 (not_1_out[26], IN1[26]);
  not not_28 (not_1_out[27], IN1[27]);
  not not_29 (not_1_out[28], IN1[28]);
  not not_30 (not_1_out[29], IN1[29]);
  not not_31 (not_1_out[30], IN1[30]);
  not not_32 (not_32_out[0], IN2[0]);
  not not_33 (not_32_out[1], IN2[1]);
  not not_34 (not_32_out[2], IN2[2]);
  not not_35 (not_32_out[3], IN2[3]);
  not not_36 (not_32_out[4], IN2[4]);
  not not_37 (not_32_out[5], IN2[5]);
  not not_38 (not_32_out[6], IN2[6]);
  not not_39 (not_32_out[7], IN2[7]);
  not not_40 (not_32_out[8], IN2[8]);
  not not_41 (not_32_out[9], IN2[9]);
  not not_42 (not_32_out[10], IN2[10]);
  not not_43 (not_32_out[11], IN2[11]);
  not not_44 (not_32_out[12], IN2[12]);
  not not_45 (not_32_out[13], IN2[13]);
  not not_46 (not_32_out[14], IN2[14]);
  not not_47 (not_32_out[15], IN2[15]);
  not not_48 (not_32_out[16], IN2[16]);
  not not_49 (not_32_out[17], IN2[17]);
  not not_50 (not_32_out[18], IN2[18]);
  not not_51 (not_32_out[19], IN2[19]);
  not not_52 (not_32_out[20], IN2[20]);
  not not_53 (not_32_out[21], IN2[21]);
  not not_54 (not_32_out[22], IN2[22]);
  not not_55 (not_32_out[23], IN2[23]);
  not not_56 (not_32_out[24], IN2[24]);
  not not_57 (not_32_out[25], IN2[25]);
  not not_58 (not_32_out[26], IN2[26]);
  not not_59 (not_32_out[27], IN2[27]);
  not not_60 (not_32_out[28], IN2[28]);
  not not_61 (not_32_out[29], IN2[29]);
  not not_62 (not_32_out[30], IN2[30]);
  Adder #(.width(32)) adder_1 (.a({32{1'b0}}), .b({IN1[31], not_1_out}), .out(adder_1_out), .cin(1'b1));  // open: cout
  Adder #(.width(32)) adder_2 (.a({32{1'b0}}), .b({IN2[31], not_32_out}), .out(adder_2_out), .cin(1'b1));  // open: cout
  Multiplexer #(.width(32)) multiplexer_1 (.in0(IN1), .in1(adder_1_out), .out(multiplexer_1_out), .sel(IN1[31]));
  Multiplexer #(.width(32)) multiplexer_2 (.in0(IN2), .in1(adder_2_out), .out(multiplexer_2_out), .sel(IN2[31]));
  // Probe on multiplexer_1_out
  // Probe on multiplexer_2_out
  Adder #(.width(32)) adder_3 (.a(multiplexer_1_out), .b(multiplexer_2_out), .out(adder_3_out));  // open: cin, cout
  not not_63 (not_63_out[0], adder_3_out[0]);
  not not_64 (not_63_out[1], adder_3_out[1]);
  not not_65 (not_63_out[2], adder_3_out[2]);
  not not_66 (not_63_out[3], adder_3_out[3]);
  not not_67 (not_63_out[4], adder_3_out[4]);
  not not_68 (not_63_out[5], adder_3_out[5]);
  not not_69 (not_63_out[6], adder_3_out[6]);
  not not_70 (not_63_out[7], adder_3_out[7]);
  not not_71 (not_63_out[8], adder_3_out[8]);
  not not_72 (not_63_out[9], adder_3_out[9]);
  not not_73 (not_63_out[10], adder_3_out[10]);
  not not_74 (not_63_out[11], adder_3_out[11]);
  not not_75 (not_63_out[12], adder_3_out[12]);
  not not_76 (not_63_out[13], adder_3_out[13]);
  not not_77 (not_63_out[14], adder_3_out[14]);
  not not_78 (not_63_out[15], adder_3_out[15]);
  not not_79 (not_63_out[16], adder_3_out[16]);
  not not_80 (not_63_out[17], adder_3_out[17]);
  not not_81 (not_63_out[18], adder_3_out[18]);
  not not_82 (not_63_out[19], adder_3_out[19]);
  not not_83 (not_63_out[20], adder_3_out[20]);
  not not_84 (not_63_out[21], adder_3_out[21]);
  not not_85 (not_63_out[22], adder_3_out[22]);
  not not_86 (not_63_out[23], adder_3_out[23]);
  not not_87 (not_63_out[24], adder_3_out[24]);
  not not_88 (not_63_out[25], adder_3_out[25]);
  not not_89 (not_63_out[26], adder_3_out[26]);
  not not_90 (not_63_out[27], adder_3_out[27]);
  not not_91 (not_63_out[28], adder_3_out[28]);
  not not_92 (not_63_out[29], adder_3_out[29]);
  not not_93 (not_63_out[30], adder_3_out[30]);
  Adder #(.width(32)) adder_4 (
    .a({32{1'b0}}), .b({adder_3_out[31], not_63_out}), .out(adder_4_out), .cin(1'b1));  // open: cout
  Multiplexer #(.width(32)) multiplexer_3 (.in0(adder_3_out), .in1(adder_4_out), .out(OUT1), .sel(adder_3_out[31]));
endmodule

module main (
);

  PC pc_1 ();  // open: D, ENABLE, clk, Reset, Q_plus4, Q
  ROM #(.dataWidth(32)) rom_1 ();  // open: addr, data
  RAM #(.asyncread("true"), .byteenables("byteEnables"), .dataWidth(32), .\type ("nonvolatile")) ram_1 ();  // open: addr, we, oe, clk, din, dout, be3, be2, be1, be0
  Decode_Inst decode_inst_1 ();  // open: in_1, instruction, lui_Eimm20, rd, rs1, rs2, lw_Eimm12, lbu_Eimm12, jalr_Eimm12, addi_Eimm12, sw_Eimm12, sb_Eimm12
endmodule

module PC (
  input  [31:0] D,
  input  ENABLE,
  input  clk,
  input  Reset,
  output [31:0] Q_plus4,
  output [31:0] Q
);

  Clock clock_1 (.out(clk));
  Register #(.width(32)) register_1 (.D(D), .en(ENABLE), .clk(clk), .Q(Q), .clr(Reset));
  Adder #(.width(32)) adder_1 (.a(Q), .b(32'h4), .out(Q_plus4), .cin(1'b0));  // open: cout
endmodule

module Decode_Inst (
  input  [31:0] in_1,
  output [15:0] instruction,
  output [31:0] lui_Eimm20,
  output [4:0] rd,
  output [4:0] rs1,
  output [4:0] rs2,
  output [31:0] lw_Eimm12,
  output [31:0] lbu_Eimm12,
  output [31:0] jalr_Eimm12,
  output [31:0] addi_Eimm12,
  output [31:0] sw_Eimm12,
  output [31:0] sb_Eimm12
);


  assign addi_Eimm12 = {{20{1'b0}}, in_1[31:20]};
  assign instruction = {{6{1'b0}}, in_1[14:12], in_1[6:0]};
  assign jalr_Eimm12 = {{20{1'b0}}, in_1[31:20]};
  assign lbu_Eimm12 = {{20{1'b0}}, in_1[31:20]};
  assign lui_Eimm20 = {in_1[31:12], {12{1'b0}}};
  assign lw_Eimm12 = {{20{1'b0}}, in_1[31:20]};
  assign rd = in_1[11:7];
  assign rs1 = in_1[19:15];
  assign rs2 = in_1[24:20];
  assign sb_Eimm12 = {{20{1'b0}}, in_1[31:25], in_1[11:7]};
  assign sw_Eimm12 = {{20{1'b0}}, in_1[31:25], in_1[11:7]};
endmodule

module Register16 (
  input  [31:0] WData,
  input  WEnable,
  input  [4:0] WSelect,
  input  Out_Enable,
  input  [4:0] Out_Reg,
  input  Reset,
  input  clk,
  output [31:0] Out_Data
);

  wire decoder_1_out1, decoder_1_out2, decoder_1_out3, decoder_1_out4, decoder_1_out5, decoder_1_out6,
       decoder_1_out7, decoder_1_out8, decoder_1_out9, decoder_1_out10, decoder_1_out11, decoder_1_out12,
       decoder_1_out13, decoder_1_out14, decoder_1_out15;
  wire [31:0] register_1_q, register_2_q, register_3_q, register_4_q, register_5_q, register_6_q,
       register_7_q, register_8_q, register_9_q, register_10_q, register_11_q, register_12_q, register_13_q,
       register_14_q, register_15_q, register_16_q;

  Decoder #(.select(5)) decoder_1 (
    .out1(decoder_1_out1), .out2(decoder_1_out2), .out3(decoder_1_out3), .out4(decoder_1_out4),
    .out5(decoder_1_out5), .out6(decoder_1_out6), .out7(decoder_1_out7), .out8(decoder_1_out8),
    .out9(decoder_1_out9), .out10(decoder_1_out10), .out11(decoder_1_out11), .out12(decoder_1_out12),
    .out13(decoder_1_out13), .out14(decoder_1_out14), .out15(decoder_1_out15), .sel(WSelect), .en(WEnable));  // open: out0, out16, out17, out18, out19, out20, out21, out22, out23, out24, out25, out26, out27, out28, out29, out30, out31
  Clock clock_1 (.out(clk));
  Register #(.width(32)) register_1 (.D({32{1'b0}}), .en(1'b0), .clk(clk), .Q(register_1_q), .clr(Reset));
  Register #(.width(32)) register_2 (.D(WData), .en(decoder_1_out1), .clk(clk), .Q(register_2_q), .clr(Reset));
  Register #(.width(32)) register_3 (.D(WData), .en(decoder_1_out2), .clk(clk), .Q(register_3_q), .clr(Reset));
  Register #(.width(32)) register_4 (.D(WData), .en(decoder_1_out3), .clk(clk), .Q(register_4_q), .clr(Reset));
  Register #(.width(32)) register_5 (.D(WData), .en(decoder_1_out4), .clk(clk), .Q(register_5_q), .clr(Reset));
  Register #(.width(32)) register_6 (.D(WData), .en(decoder_1_out5), .clk(clk), .Q(register_6_q), .clr(Reset));
  Register #(.width(32)) register_7 (.D(WData), .en(decoder_1_out6), .clk(clk), .Q(register_7_q), .clr(Reset));
  Register #(.width(32)) register_8 (.D(WData), .en(decoder_1_out7), .clk(clk), .Q(register_8_q), .clr(Reset));
  Register #(.width(32)) register_9 (.D(WData), .en(decoder_1_out8), .clk(clk), .Q(register_9_q), .clr(Reset));
  Register #(.width(32)) register_10 (.D(WData), .en(decoder_1_out9), .clk(clk), .Q(register_10_q), .clr(Reset));
  Register #(.width(32)) register_11 (.D(WData), .en(decoder_1_out10), .clk(clk), .Q(register_11_q), .clr(Reset));
  Register #(.width(32)) register_12 (.D(WData), .en(decoder_1_out11), .clk(clk), .Q(register_12_q), .clr(Reset));
  Register #(.width(32)) register_13 (.D(WData), .en(decoder_1_out12), .clk(clk), .Q(register_13_q), .clr(Reset));
  Register #(.width(32)) register_14 (.D(WData), .en(decoder_1_out13), .clk(clk), .Q(register_14_q), .clr(Reset));
  Register #(.width(32)) register_15 (.D(WData), .en(decoder_1_out14), .clk(clk), .Q(register_15_q), .clr(Reset));
  Register #(.width(32)) register_16 (.D(WData), .en(decoder_1_out15), .clk(clk), .Q(register_16_q), .clr(Reset));
  Multiplexer #(.enable("true"), .select(5), .width(32)) multiplexer_1 (
    .in0(register_1_q), .in1(register_2_q), .in2(register_3_q), .in3(register_4_q), .in4(register_5_q),
    .in5(register_6_q), .in6(register_7_q), .in7(register_8_q), .in8(register_9_q), .in9(register_10_q),
    .in10(register_11_q), .in11(register_12_q), .in12(register_13_q), .in13(register_14_q),
    .in14(register_15_q), .in15(register_16_q), .out(Out_Data), .sel(Out_Reg), .en(Out_Enable));  // open: in16, in17, in18, in19, in20, in21, in22, in23, in24, in25, in26, in27, in28, in29, in30, in31
endmodule
