// Logisim project 减法器.circ as structural Verilog: 5 circuits, main circuit 4位原码减法器
module \_4位原码减法器  (
  input  in_1,
  input  [3:0] in_2,
  input  in_3,
  input  [3:0] in_4,
  output out_5,
  output [3:0] out_6
);

  wire adder_1_cout, adder_1_out, adder_2_cout, adder_2_out, adder_3_cout, adder_3_out, adder_4_out,
       and_1_out, and_2_out, and_3_out, comparator_1_gt, comparator_1_lt, multiplexer_1_out,
       multiplexer_2_out, multiplexer_3_out, multiplexer_4_out, multiplexer_5_out, multiplexer_6_out,
       multiplexer_7_out, multiplexer_8_out, not_1_out, not_2_out, not_3_out, not_4_out, subtractor_1_bout,
       subtractor_1_out, subtractor_2_bout, subtractor_2_out, subtractor_3_bout, subtractor_3_out,
       subtractor_4_out, xor_1_out;
  wire [3:0] and_4_out, and_8_out;

  Hex_Digit_Display hex_digit_display_1 (.value(in_2));  // open: dp
  Hex_Digit_Display hex_digit_display_2 (.value(in_4));  // open: dp
  not not_1 (not_1_out, in_3);
  Comparator #(.width(4)) comparator_1 (.a(in_2), .b(in_4), .gt(comparator_1_gt), .lt(comparator_1_lt));  // open: eq
  not not_2 (not_2_out, in_3);
  not not_3 (not_3_out, in_1);
  Adder #(.width(1)) adder_1 (.a(in_2[0]), .b(in_4[0]), .out(adder_1_out), .cin(1'b0), .cout(adder_1_cout));
  Adder #(.width(1)) adder_2 (.a(in_2[1]), .b(in_4[1]), .out(adder_2_out), .cin(adder_1_cout), .cout(adder_2_cout));
  Adder #(.width(1)) adder_3 (.a(in_2[2]), .b(in_4[2]), .out(adder_3_out), .cin(adder_2_cout), .cout(adder_3_cout));
  Adder #(.width(1)) adder_4 (.a(in_2[3]), .b(in_4[3]), .out(adder_4_out), .cin(adder_3_cout));  // open: cout
  Multiplexer #(.enable("false")) multiplexer_1 (
    .in0(in_2[0]), .in1(in_4[0]), .out(multiplexer_1_out), .sel(comparator_1_lt));
  Multiplexer #(.enable("false")) multiplexer_2 (
    .in0(in_4[0]), .in1(in_2[0]), .out(multiplexer_2_out), .sel(comparator_1_lt));
  Multiplexer #(.enable("false")) multiplexer_3 (
    .in0(in_2[1]), .in1(in_4[1]), .out(multiplexer_3_out), .sel(comparator_1_lt));
  Multiplexer #(.enable("false")) multiplexer_4 (
    .in0(in_4[1]), .in1(in_2[1]), .out(multiplexer_4_out), .sel(comparator_1_lt));
  Multiplexer #(.enable("false")) multiplexer_5 (
    .in0(in_2[2]), .in1(in_4[2]), .out(multiplexer_5_out), .sel(comparator_1_lt));
  Multiplexer #(.enable("false")) multiplexer_6 (
    .in0(in_4[2]), .in1(in_2[2]), .out(multiplexer_6_out), .sel(comparator_1_lt));
  Multiplexer #(.enable("false")) multiplexer_7 (
    .in0(in_2[3]), .in1(in_4[3]), .out(multiplexer_7_out), .sel(comparator_1_lt));
  Multiplexer #(.enable("false")) multiplexer_8 (
    .in0(in_4[3]), .in1(in_2[3]), .out(multiplexer_8_out), .sel(comparator_1_lt));
  and and_1 (and_1_out, not_1_out, in_1);
  and and_2 (and_2_out, in_1, in_3, comparator_1_gt);
  and and_3 (and_3_out, comparator_1_lt, not_2_out, not_3_out);
  xor xor_1 (xor_1_out, in_1, in_3);
  not not_4 (not_4_out, xor_1_out);
  Subtractor #(.width(1)) subtractor_1 (
    .a(multiplexer_1_out), .b(multiplexer_2_out), .out(subtractor_1_out), .bout(subtractor_1_bout));  // open: bin
  Subtractor #(.width(1)) subtractor_2 (
    .a(multiplexer_3_out), .b(multiplexer_4_out), .out(subtractor_2_out), .bin(subtractor_1_bout),
    .bout(subtractor_2_bout));
  Subtractor #(.width(1)) subtractor_3 (
    .a(multiplexer_5_out), .b(multiplexer_6_out), .out(subtractor_3_out), .bin(subtractor_2_bout),
    .bout(subtractor_3_bout));
  Subtractor #(.width(1)) subtractor_4 (
    .a(multiplexer_7_out), .b(multiplexer_8_out), .out(subtractor_4_out), .bin(subtractor_3_bout));  // open: bout
  or or_1 (out_5, and_1_out, and_2_out, and_3_out);
  _7_Segment_Display u_7_segment_display_1 (.g(out_5));  // open: f, a, b, e, d, c, dp
  and and_4 (and_4_out[0], xor_1_out, adder_1_out);
  and and_5 (and_4_out[1], xor_1_out, adder_2_out);
  and and_6 (and_4_out[2], xor_1_out, adder_3_out);
  and and_7 (and_4_out[3], xor_1_out, adder_4_out);
  and and_8 (and_8_out[0], not_4_out, subtractor_1_out);
  and and_9 (and_8_out[1], not_4_out, subtractor_2_out);
  and and_10 (and_8_out[2], not_4_out, subtractor_3_out);
  and and_11 (and_8_out[3], not_4_out, subtractor_4_out);
  Hex_Digit_Display hex_digit_display_3 (.value(out_6));  // open: dp
  Multiplexer #(.width(4), .enable("false")) multiplexer_9 (
    .in0(and_8_out), .in1(and_4_out), .out(out_6), .sel(xor_1_out));
endmodule

module \_4位原码加法器  (
  input  in_1,
  input  [3:0] in_2,
  input  in_3,
  input  [3:0] in_4,
  output out_5,
  output [3:0] out_6
);

  wire adder_1_cout, adder_1_out, adder_2_cout, adder_2_out, adder_3_cout, adder_3_out, adder_4_out,
       and_1_out, and_2_out, and_3_out, comparator_1_gt, comparator_1_lt, multiplexer_1_out,
       multiplexer_2_out, multiplexer_3_out, multiplexer_4_out, multiplexer_5_out, multiplexer_6_out,
       multiplexer_7_out, multiplexer_8_out, not_1_out, subtractor_1_bout, subtractor_1_out,
       subtractor_2_bout, subtractor_2_out, subtractor_3_bout, subtractor_3_out, subtractor_4_out, xnor_1_out;
  wire [3:0] and_4_out, and_8_out;

  Hex_Digit_Display hex_digit_display_1 (.value(in_2));  // open: dp
  Hex_Digit_Display hex_digit_display_2 (.value(in_4));  // open: dp
  Comparator #(.width(4), .mode("unsigned")) comparator_1 (
    .a(in_2), .b(in_4), .gt(comparator_1_gt), .lt(comparator_1_lt));  // open: eq
  Adder #(.width(1)) adder_1 (.a(in_2[0]), .b(in_4[0]), .out(adder_1_out), .cin(1'b0), .cout(adder_1_cout));
  Adder #(.width(1)) adder_2 (.a(in_2[1]), .b(in_4[1]), .out(adder_2_out), .cin(adder_1_cout), .cout(adder_2_cout));
  Adder #(.width(1)) adder_3 (.a(in_2[2]), .b(in_4[2]), .out(adder_3_out), .cin(adder_2_cout), .cout(adder_3_cout));
  Adder #(.width(1)) adder_4 (.a(in_2[3]), .b(in_4[3]), .out(adder_4_out), .cin(adder_3_cout));  // open: cout
  Multiplexer #(.enable("false")) multiplexer_1 (
    .in0(in_2[0]), .in1(in_4[0]), .out(multiplexer_1_out), .sel(comparator_1_lt));
  Multiplexer #(.enable("false")) multiplexer_2 (
    .in0(in_4[0]), .in1(in_2[0]), .out(multiplexer_2_out), .sel(comparator_1_lt));
  Multiplexer #(.enable("false")) multiplexer_3 (
    .in0(in_2[1]), .in1(in_4[1]), .out(multiplexer_3_out), .sel(comparator_1_lt));
  Multiplexer #(.enable("false")) multiplexer_4 (
    .in0(in_4[1]), .in1(in_2[1]), .out(multiplexer_4_out), .sel(comparator_1_lt));
  Multiplexer #(.enable("false")) multiplexer_5 (
    .in0(in_2[2]), .in1(in_4[2]), .out(multiplexer_5_out), .sel(comparator_1_lt));
  Multiplexer #(.enable("false")) multiplexer_6 (
    .in0(in_4[2]), .in1(in_2[2]), .out(multiplexer_6_out), .sel(comparator_1_lt));
  Multiplexer #(.enable("false")) multiplexer_7 (
    .in0(in_2[3]), .in1(in_4[3]), .out(multiplexer_7_out), .sel(comparator_1_lt));
  Multiplexer #(.enable("false")) multiplexer_8 (
    .in0(in_4[3]), .in1(in_2[3]), .out(multiplexer_8_out), .sel(comparator_1_lt));
  and and_1 (and_1_out, in_3, in_1);
  and and_2 (and_2_out, in_1, comparator_1_gt);
  and and_3 (and_3_out, comparator_1_lt, in_3);
  xnor xnor_1 (xnor_1_out, in_1, in_3);
  not not_1 (not_1_out, xnor_1_out);
  Subtractor #(.width(1)) subtractor_1 (
    .a(multiplexer_1_out), .b(multiplexer_2_out), .out(subtractor_1_out), .bout(subtractor_1_bout));  // open: bin
  Subtractor #(.width(1)) subtractor_2 (
    .a(multiplexer_3_out), .b(multiplexer_4_out), .out(subtractor_2_out), .bin(subtractor_1_bout),
    .bout(subtractor_2_bout));
  Subtractor #(.width(1)) subtractor_3 (
    .a(multiplexer_5_out), .b(multiplexer_6_out), .out(subtractor_3_out), .bin(subtractor_2_bout),
    .bout(subtractor_3_bout));
  Subtractor #(.width(1)) subtractor_4 (
    .a(multiplexer_7_out), .b(multiplexer_8_out), .out(subtractor_4_out), .bin(subtractor_3_bout));  // open: bout
  or or_1 (out_5, and_1_out, and_2_out, and_3_out);
  _7_Segment_Display u_7_segment_display_1 (.g(out_5));  // open: f, a, b, e, d, c, dp
  and and_4 (and_4_out[0], xnor_1_out, adder_1_out);
  and and_5 (and_4_out[1], xnor_1_out, adder_2_out);
  and and_6 (and_4_out[2], xnor_1_out, adder_3_out);
  and and_7 (and_4_out[3], xnor_1_out, adder_4_out);
  and and_8 (and_8_out[0], not_1_out, subtractor_1_out);
  and and_9 (and_8_out[1], not_1_out, subtractor_2_out);
  and and_10 (and_8_out[2], not_1_out, subtractor_3_out);
  and and_11 (and_8_out[3], not_1_out, subtractor_4_out);
  Hex_Digit_Display hex_digit_display_3 (.value(out_6));  // open: dp
  Multiplexer #(.width(4), .enable("false")) multiplexer_9 (
    .in0(and_8_out), .in1(and_4_out), .out(out_6), .sel(xnor_1_out));
endmodule

module \_4位反码加法器  (
  input  in_1,
  input  [3:0] in_2,
  input  in_3,
  input  [3:0] in_4
);

  wire and_1_out, and_2_out, multiplexer_11_out, multiplexer_12_out, \n4位原码加法器_1_out_5 , not_1_out,
       not_2_out, not_3_out, not_4_out, not_5_out, not_6_out, not_7_out, not_8_out, not_9_out, not_10_out;
  wire [3:0] multiplexer_1_out, multiplexer_2_out, multiplexer_6_out, multiplexer_7_out, multiplexer_13_out,
       multiplexer_14_out, \n4位原码加法器_1_out_6 ;

  _7_Segment_Display u_7_segment_display_1 (.g(multiplexer_11_out));  // open: f, a, b, e, d, c, dp
  Hex_Digit_Display hex_digit_display_1 (.value(multiplexer_1_out));  // open: dp
  _7_Segment_Display u_7_segment_display_2 (.g(multiplexer_12_out));  // open: f, a, b, e, d, c, dp
  Hex_Digit_Display hex_digit_display_2 (.value(multiplexer_6_out));  // open: dp
  not not_1 (not_1_out, in_2[0]);
  not not_2 (not_2_out, in_2[1]);
  not not_3 (not_3_out, in_2[2]);
  not not_4 (not_4_out, in_2[3]);
  not not_5 (not_5_out, in_4[0]);
  not not_6 (not_6_out, in_4[1]);
  not not_7 (not_7_out, in_4[2]);
  not not_8 (not_8_out, in_4[3]);
  Multiplexer #(.width(4), .enable("false")) multiplexer_1 (
    .in0(in_2), .in1(multiplexer_13_out), .out(multiplexer_1_out), .sel(in_1));
  Multiplexer #(.enable("false")) multiplexer_2 (
    .in0(in_2[0]), .in1(not_1_out), .out(multiplexer_2_out[0]), .sel(in_1));
  Multiplexer #(.enable("false")) multiplexer_3 (
    .in0(in_2[1]), .in1(not_2_out), .out(multiplexer_2_out[1]), .sel(in_1));
  Multiplexer #(.enable("false")) multiplexer_4 (
    .in0(in_2[2]), .in1(not_3_out), .out(multiplexer_2_out[2]), .sel(in_1));
  Multiplexer #(.enable("false")) multiplexer_5 (
    .in0(in_2[3]), .in1(not_4_out), .out(multiplexer_2_out[3]), .sel(in_1));
  Multiplexer #(.width(4), .enable("false")) multiplexer_6 (
    .in0(in_4), .in1(multiplexer_14_out), .out(multiplexer_6_out), .sel(in_3));
  Multiplexer #(.enable("false")) multiplexer_7 (
    .in0(in_4[0]), .in1(not_5_out), .out(multiplexer_7_out[0]), .sel(in_3));
  Multiplexer #(.enable("false")) multiplexer_8 (
    .in0(in_4[1]), .in1(not_6_out), .out(multiplexer_7_out[1]), .sel(in_3));
  Multiplexer #(.enable("false")) multiplexer_9 (
    .in0(in_4[2]), .in1(not_7_out), .out(multiplexer_7_out[2]), .sel(in_3));
  Multiplexer #(.enable("false")) multiplexer_10 (
    .in0(in_4[3]), .in1(not_8_out), .out(multiplexer_7_out[3]), .sel(in_3));
  and and_1 (and_1_out, in_1, not_1_out, not_2_out, not_3_out, not_4_out);
  and and_2 (and_2_out, in_3, not_5_out, not_6_out, not_7_out, not_8_out);
  Multiplexer #(.enable("false")) multiplexer_11 (
    .in0(in_1), .in1(not_9_out), .out(multiplexer_11_out), .sel(and_1_out));
  not not_9 (not_9_out, in_1);
  Multiplexer #(.enable("false")) multiplexer_12 (
    .in0(in_3), .in1(not_10_out), .out(multiplexer_12_out), .sel(and_2_out));
  not not_10 (not_10_out, in_3);
  Multiplexer #(.width(4), .enable("false")) multiplexer_13 (
    .in0(multiplexer_2_out), .in1(in_2), .out(multiplexer_13_out), .sel(and_1_out));
  Multiplexer #(.width(4), .enable("false")) multiplexer_14 (
    .in0(multiplexer_7_out), .in1(in_4), .out(multiplexer_14_out), .sel(and_2_out));
  \_4位原码加法器  \u_4位原码加法器_1  (
    .in_1(multiplexer_11_out), .in_2(multiplexer_13_out), .in_3(multiplexer_12_out),
    .in_4(multiplexer_14_out), .out_5(\n4位原码加法器_1_out_5 ), .out_6(\n4位原码加法器_1_out_6 ));
  _7_Segment_Display u_7_segment_display_3 (.g(\n4位原码加法器_1_out_5 ));  // open: f, a, b, e, d, c, dp
  Hex_Digit_Display hex_digit_display_3 (.value(\n4位原码加法器_1_out_6 ));  // open: dp
endmodule

module \_4位反码加法器_simple_version  (
  input  in_1,
  input  [3:0] in_2,
  input  in_3,
  input  [3:0] in_4
);

  wire adder_1_cout, adder_1_out, adder_2_cout, adder_3_cout, adder_4_cout, adder_5_cout, and_1_out,
       and_2_out, multiplexer_1_out, multiplexer_3_out, not_1_out, not_2_out;
  wire [3:0] adder_2_out, multiplexer_2_out, multiplexer_4_out, multiplexer_5_out, multiplexer_6_out,
       multiplexer_7_out, not_3_out, not_7_out, not_11_out;

  _7_Segment_Display u_7_segment_display_1 (.g(multiplexer_1_out));  // open: f, a, b, e, d, c, dp
  _7_Segment_Display u_7_segment_display_2 (.g(multiplexer_3_out));  // open: f, a, b, e, d, c, dp
  Hex_Digit_Display hex_digit_display_1 (.value(multiplexer_5_out));  // open: dp
  Hex_Digit_Display hex_digit_display_2 (.value(multiplexer_6_out));  // open: dp
  not not_1 (not_1_out, in_1);
  not not_2 (not_2_out, in_3);
  not not_3 (not_3_out[0], in_2[0]);
  not not_4 (not_3_out[1], in_2[1]);
  not not_5 (not_3_out[2], in_2[2]);
  not not_6 (not_3_out[3], in_2[3]);
  not not_7 (not_7_out[0], in_4[0]);
  not not_8 (not_7_out[1], in_4[1]);
  not not_9 (not_7_out[2], in_4[2]);
  not not_10 (not_7_out[3], in_4[3]);
  and and_1 (and_1_out, in_1, not_3_out[0], not_3_out[1], not_3_out[2], not_3_out[3]);
  and and_2 (and_2_out, in_3, not_7_out[0], not_7_out[1], not_7_out[2], not_7_out[3]);
  Multiplexer #(.enable("false")) multiplexer_1 (.in0(in_1), .in1(not_1_out), .out(multiplexer_1_out), .sel(and_1_out));
  Multiplexer #(.width(4), .enable("false")) multiplexer_2 (
    .in0(in_2), .in1(not_3_out), .out(multiplexer_2_out), .sel(in_1));
  Multiplexer #(.enable("false")) multiplexer_3 (.in0(in_3), .in1(not_2_out), .out(multiplexer_3_out), .sel(and_2_out));
  Multiplexer #(.width(4), .enable("false")) multiplexer_4 (
    .in0(in_4), .in1(not_7_out), .out(multiplexer_4_out), .sel(in_3));
  Multiplexer #(.width(4), .enable("false")) multiplexer_5 (
    .in0(multiplexer_2_out), .in1(in_2), .out(multiplexer_5_out), .sel(and_1_out));
  Multiplexer #(.width(4), .enable("false")) multiplexer_6 (
    .in0(multiplexer_4_out), .in1(in_4), .out(multiplexer_6_out), .sel(and_2_out));
  Adder #(.width(1)) adder_1 (.a(in_1), .b(in_3), .out(adder_1_out), .cin(adder_5_cout), .cout(adder_1_cout));
  Adder #(.width(1)) adder_2 (.a(in_2[0]), .b(in_4[0]), .out(adder_2_out[0]), .cin(adder_1_cout), .cout(adder_2_cout));
  Adder #(.width(1)) adder_3 (.a(in_2[1]), .b(in_4[1]), .out(adder_2_out[1]), .cin(adder_2_cout), .cout(adder_3_cout));
  Adder #(.width(1)) adder_4 (.a(in_2[2]), .b(in_4[2]), .out(adder_2_out[2]), .cin(adder_3_cout), .cout(adder_4_cout));
  Adder #(.width(1)) adder_5 (.a(in_2[3]), .b(in_4[3]), .out(adder_2_out[3]), .cin(adder_4_cout), .cout(adder_5_cout));
  not not_11 (not_11_out[0], adder_2_out[0]);
  not not_12 (not_11_out[1], adder_2_out[1]);
  not not_13 (not_11_out[2], adder_2_out[2]);
  not not_14 (not_11_out[3], adder_2_out[3]);
  Multiplexer #(.width(4), .enable("false")) multiplexer_7 (
    .in0(adder_2_out), .in1(not_11_out), .out(multiplexer_7_out), .sel(adder_1_out));
  _7_Segment_Display u_7_segment_display_3 (.g(adder_1_out));  // open: f, a, b, e, d, c, dp
  Hex_Digit_Display hex_digit_display_3 (.value(multiplexer_7_out));  // open: dp

  // Notes on the sheet:
  //   这部分电路是为了输入
  //   显示用的，方便调试
  //   主电路
  //   这部分电路是为了输出
  //   显示用的，方便调试
endmodule

module \溢出判断  (
  input  [3:0] in_1,
  input  [3:0] in_2,
  output out_3,
  output out_4,
  output out_5,
  output out_6
);

  wire adder_1_cout, adder_2_cout, adder_3_cout, adder_4_cout, and_1_out, and_2_out, and_3_out, and_4_out,
       and_5_out, and_6_out, and_7_out, and_8_out, not_1_out, not_2_out, not_3_out, not_4_out, not_5_out,
       not_6_out, not_7_out, not_8_out, not_9_out, not_10_out, not_11_out, not_12_out, or_1_out, or_2_out,
       or_3_out, or_4_out;

  Adder #(.width(1)) adder_1 (.a(in_1[0]), .b(in_2[0]), .out(out_3), .cin(1'b0), .cout(adder_1_cout));
  Adder #(.width(1)) adder_2 (.a(in_1[1]), .b(in_2[1]), .out(out_4), .cin(adder_1_cout), .cout(adder_2_cout));
  Adder #(.width(1)) adder_3 (.a(in_2[2]), .b(in_1[2]), .out(out_5), .cin(adder_2_cout), .cout(adder_3_cout));
  Adder #(.width(1)) adder_4 (.a(in_1[3]), .b(in_2[3]), .out(out_6), .cin(adder_3_cout), .cout(adder_4_cout));
  not not_1 (not_1_out, 1'b0);
  not not_2 (not_2_out, in_1[0]);
  not not_3 (not_3_out, in_2[0]);
  not not_4 (not_4_out, adder_1_cout);
  not not_5 (not_5_out, in_1[1]);
  not not_6 (not_6_out, in_2[1]);
  not not_7 (not_7_out, adder_2_cout);
  not not_8 (not_8_out, in_2[2]);
  not not_9 (not_9_out, in_1[2]);
  not not_10 (not_10_out, adder_3_cout);
  not not_11 (not_11_out, in_1[3]);
  not not_12 (not_12_out, in_2[3]);
  and and_1 (and_1_out, not_1_out, in_2[0], in_1[0]);
  and and_2 (and_2_out, 1'b0, not_2_out, not_3_out);
  and and_3 (and_3_out, not_4_out, in_2[1], in_1[1]);
  and and_4 (and_4_out, adder_1_cout, not_5_out, not_6_out);
  and and_5 (and_5_out, not_7_out, in_1[2], in_2[2]);
  and and_6 (and_6_out, adder_2_cout, not_8_out, not_9_out);
  and and_7 (and_7_out, not_10_out, in_2[3], in_1[3]);
  and and_8 (and_8_out, adder_3_cout, not_11_out, not_12_out);
  LED led_1 (.in(or_1_out));
  or or_1 (or_1_out, and_1_out, and_2_out);
  LED led_2 (.in(or_2_out));
  or or_2 (or_2_out, and_3_out, and_4_out);
  or or_3 (or_3_out, and_5_out, and_6_out);
  LED led_3 (.in(or_3_out));
  or or_4 (or_4_out, and_7_out, and_8_out);
  LED led_4 (.in(or_4_out));
endmodule
