// Logisim project 加法器.circ as structural Verilog: 4 circuits, main circuit 全加器
module \全加器  (
  input  _0,
  input  _1,
  input  Cin,
  output C,
  output S
);

  wire and_1_out, or_1_out, or_2_out, or_3_out, xor_1_out, xor_2_out;

  or or_1 (or_1_out, _0, Cin);
  or or_2 (or_2_out, _1, Cin);
  and and_1 (and_1_out, _0, _1, Cin);
  xor xor_1 (xor_1_out, _0, _1);
  or or_3 (or_3_out, _0, _1);
  xor xor_2 (xor_2_out, xor_1_out, Cin);
  and and_2 (C, or_3_out, or_1_out, or_2_out);
  or or_4 (S, and_1_out, xor_2_out);
endmodule

module \半加器  (
  input  in_1,
  input  in_2,
  output C,
  output S
);

  and and_1 (C, in_1, in_2);
  xor xor_1 (S, in_2, in_1);
endmodule

module \全加器_based_on半加器  (
  input  in_1,
  input  in_2,
  input  in_3,
  output C,
  output S
);

  wire \半加器_1_c , \半加器_1_s , \半加器_3_c ;

  \半加器  \u_半加器_1  (.in_1(in_1), .in_2(in_2), .C(\半加器_1_c ), .S(\半加器_1_s ));
  \半加器  \u_半加器_2  (.in_1(\半加器_1_c ), .in_2(\半加器_3_c ), .S(C));  // open: C
  \半加器  \u_半加器_3  (.in_1(\半加器_1_s ), .in_2(in_3), .C(\半加器_3_c ), .S(S));
endmodule

module \四位加法器  (
  input  in_1,
  input  in_2,
  input  in_3,
  input  in_4,
  input  in_5,
  input  in_6,
  input  in_7,
  input  in_8,
  output S1,
  output S2,
  output S3,
  output S4
);

  wire \全加器_1_c , \全加器_2_c , \全加器_3_c , \全加器_4_c ;

  \全加器  \u_全加器_1  (._0(in_1), ._1(in_5), .Cin(1'b0), .C(\全加器_1_c ), .S(S1));
  \全加器  \u_全加器_2  (._0(in_2), ._1(in_6), .Cin(\全加器_1_c ), .C(\全加器_2_c ), .S(S2));
  LED led_1 (.in(\全加器_1_c ));
  LED led_2 (.in(\全加器_2_c ));
  \全加器  \u_全加器_3  (._0(in_3), ._1(in_7), .Cin(\全加器_2_c ), .C(\全加器_3_c ), .S(S3));
  LED led_3 (.in(\全加器_3_c ));
  \全加器  \u_全加器_4  (._0(in_4), ._1(in_8), .Cin(\全加器_3_c ), .C(\全加器_4_c ), .S(S4));
  LED led_4 (.in(\全加器_4_c ));
endmodule
