// Logisim project 同或门.circ as structural Verilog: 2 circuits, main circuit main
module main (
  input  in_1,
  input  in_2,
  output out_3
);

  wire and_1_out, and_2_out, not_1_out, or_1_out;

  or or_1 (or_1_out, in_1, in_2);
  and and_1 (and_1_out, in_1, in_2);
  not not_1 (not_1_out, and_1_out);
  and and_2 (and_2_out, or_1_out, not_1_out);
  not not_2 (out_3, and_2_out);
endmodule

module transistor (
  input  in_1,
  input  in_2,
  input  in_3,
  input  in_4,
  input  in_5,
  output out_6,
  output out_7
);

  wire transistor_1_out, transistor_3_out, transistor_7_out, undriven;

  Transistor transistor_1 (.in(1'b1), .out(transistor_1_out), .gate(in_1));
  Transistor #(.\type ("n")) transistor_2 (.in(1'b0), .out(transistor_1_out), .gate(in_1));
  Transistor transistor_3 (.in(1'b1), .out(transistor_3_out), .gate(in_4));
  Transistor #(.\type ("n")) transistor_4 (.in(1'b0), .out(transistor_3_out), .gate(in_4));
  Transistor transistor_5 (.in(in_1), .out(out_6), .gate(in_2));
  Transistor #(.\type ("n")) transistor_6 (.in(transistor_1_out), .out(out_6), .gate(in_2));
  Transistor transistor_7 (.in(in_4), .out(transistor_7_out), .gate(in_5));
  Transistor #(.\type ("n")) transistor_8 (.in(transistor_3_out), .out(transistor_7_out), .gate(in_5));
  Transistor transistor_9 (.in(undriven), .out(out_6), .gate(in_1));
  Transistor #(.\type ("n"), .gate("br")) transistor_10 (.in(undriven), .out(out_6), .gate(transistor_1_out));
  Transistor transistor_11 (.in(1'b1), .out(out_7), .gate(transistor_7_out));
  Transistor #(.\type ("n")) transistor_12 (.in(1'b0), .out(out_7), .gate(transistor_7_out));

  // Notes on the sheet:
  //   异或
  //   同或
endmodule
