// Logisim project 多路选择器.circ as structural Verilog: 3 circuits, main circuit 1位2选1选择器
module \_1位2选1选择器  (
  input  D1,
  input  S,
  input  D2,
  output out_4
);

  wire and_1_out, and_2_out, not_1_out;

  not not_1 (not_1_out, S);
  and and_1 (and_1_out, D1, not_1_out);
  and and_2 (and_2_out, S, D2);
  or or_1 (out_4, and_1_out, and_2_out);
endmodule

module \_3位4选1选择器  (
  input  [2:0] in_1,
  input  [2:0] in_2,
  input  [1:0] in_3,
  input  [2:0] in_4,
  input  [2:0] in_5,
  output _0,
  output _1,
  output _2
);

  wire and_1_out, and_2_out, and_3_out, and_4_out, and_5_out, and_6_out, and_7_out, and_8_out, and_9_out,
       and_10_out, and_11_out, and_12_out, decoder_1_out0, decoder_1_out1, decoder_1_out2, decoder_1_out3;

  Decoder #(.select(2), .enable("false")) decoder_1 (
    .out0(decoder_1_out0), .out1(decoder_1_out1), .out2(decoder_1_out2), .out3(decoder_1_out3), .sel(in_3));
  and and_1 (and_1_out, in_1[0], decoder_1_out0);
  and and_2 (and_2_out, in_2[0], decoder_1_out1);
  and and_3 (and_3_out, in_4[0], decoder_1_out2);
  and and_4 (and_4_out, in_5[0], decoder_1_out3);
  and and_5 (and_5_out, in_1[1], decoder_1_out0);
  and and_6 (and_6_out, in_2[1], decoder_1_out1);
  and and_7 (and_7_out, in_4[1], decoder_1_out2);
  and and_8 (and_8_out, in_1[2], decoder_1_out3);
  and and_9 (and_9_out, in_5[1], decoder_1_out0);
  and and_10 (and_10_out, in_2[2], decoder_1_out1);
  and and_11 (and_11_out, in_4[2], decoder_1_out2);
  and and_12 (and_12_out, in_5[2], decoder_1_out3);
  or or_1 (_0, and_1_out, and_2_out, and_3_out, and_4_out);
  or or_2 (_1, and_5_out, and_6_out, and_7_out, and_8_out);
  or or_3 (_2, and_9_out, and_10_out, and_11_out, and_12_out);
endmodule

module \可切换进位计数制  (
  input  in_1,
  input  [3:0] in_2
);

  wire and_1_out, and_2_out, and_3_out, and_4_out, and_5_out, and_6_out, and_7_out, and_8_out, and_9_out,
       and_10_out, and_11_out, and_12_out, and_13_out, and_14_out, decoder_1_out0, decoder_1_out1,
       decoder_1_out2, decoder_1_out3, decoder_1_out4, decoder_1_out5, decoder_1_out6, decoder_1_out7,
       decoder_1_out8, decoder_1_out9, decoder_1_out10, decoder_1_out11, decoder_1_out12, decoder_1_out13,
       decoder_1_out14, decoder_1_out15, not_1_out, or_1_out;

  Decoder #(.select(4), .enable("false")) decoder_1 (
    .out0(decoder_1_out0), .out1(decoder_1_out1), .out2(decoder_1_out2), .out3(decoder_1_out3),
    .out4(decoder_1_out4), .out5(decoder_1_out5), .out6(decoder_1_out6), .out7(decoder_1_out7),
    .out8(decoder_1_out8), .out9(decoder_1_out9), .out10(decoder_1_out10), .out11(decoder_1_out11),
    .out12(decoder_1_out12), .out13(decoder_1_out13), .out14(decoder_1_out14), .out15(decoder_1_out15),
    .sel(in_2));
  or or_1 (or_1_out, decoder_1_out10, decoder_1_out11, decoder_1_out12, decoder_1_out13, decoder_1_out14, decoder_1_out15);
  not not_1 (not_1_out, in_1);
  and and_1 (and_1_out, or_1_out, not_1_out);
  and and_2 (and_2_out, in_1, or_1_out);
  and and_3 (and_3_out, and_2_out, decoder_1_out10);
  and and_4 (and_4_out, and_2_out, decoder_1_out11);
  and and_5 (and_5_out, and_2_out, decoder_1_out12);
  and and_6 (and_6_out, and_2_out, decoder_1_out13);
  and and_7 (and_7_out, and_2_out, decoder_1_out14);
  and and_8 (and_8_out, and_2_out, decoder_1_out15);
  and and_9 (and_9_out, and_1_out, decoder_1_out10);
  and and_10 (and_10_out, and_1_out, decoder_1_out11);
  and and_11 (and_11_out, and_1_out, decoder_1_out12);
  and and_12 (and_12_out, and_1_out, decoder_1_out13);
  and and_13 (and_13_out, and_1_out, decoder_1_out14);
  and and_14 (and_14_out, and_1_out, decoder_1_out15);
  _7_Segment_Display u_7_segment_display_1 ();  // open: g, f, a, b, e, d, c, dp

  // Notes on the sheet:
  //   0-9七段数码管逻辑电路
  //   十六进制的逻辑电路
  //   十进制的逻辑电路
endmodule
