// Logisim project 支持数列求和的简单处理器.circ as structural Verilog: 5 circuits, main circuit ROM
module ROM (
  input  RESET,
  input  EN
);

  wire adder_1_cout, adder_1_out, adder_2_cout, adder_2_out, adder_3_out, and_1_out, and_2_out, and_3_out,
       and_4_out, and_5_out, and_6_out, and_7_out, and_8_out, and_9_out, and_10_out, and_11_out, and_12_out,
       and_13_out, and_14_out, and_15_out, and_16_out, and_17_out, and_18_out, and_19_out, and_20_out,
       and_21_out, and_22_out, and_23_out, and_24_out, and_25_out, and_26_out, and_27_out, and_28_out,
       and_29_out, and_30_out, and_31_out, and_32_out, and_33_out, and_34_out, and_35_out, and_36_out,
       and_37_out, and_38_out, and_39_out, and_40_out, and_41_out, and_42_out, and_43_out, and_44_out,
       and_45_out, and_46_out, and_47_out, and_48_out, and_49_out, and_50_out, and_51_out, and_52_out,
       and_53_out, and_54_out, and_55_out, and_56_out, and_57_out, and_58_out, and_59_out, and_60_out,
       and_61_out, and_62_out, and_63_out, and_64_out, clk_out, decoder_1_out0, decoder_1_out1,
       decoder_1_out2, decoder_1_out3, decoder_1_out4, decoder_1_out5, decoder_1_out6, decoder_1_out7,
       \n4位寄存器_1_q_0 , or_1_out, or_2_out, undriven, undriven_2, undriven_3, undriven_4, undriven_5,
       undriven_6, undriven_7, undriven_8, undriven_9, undriven_10, undriven_11, undriven_12, undriven_13,
       undriven_14, undriven_15, undriven_16, undriven_17, undriven_18, undriven_19, undriven_20,
       undriven_21, undriven_22, undriven_23, undriven_24, undriven_25, undriven_26, undriven_27,
       undriven_28, undriven_29, undriven_30, undriven_31, undriven_32, undriven_33, undriven_34,
       undriven_35, undriven_36, undriven_37, undriven_38, undriven_39, undriven_40, undriven_41,
       undriven_42, undriven_43, undriven_44, undriven_45, undriven_46, undriven_47, undriven_48,
       undriven_49, undriven_50, undriven_51, undriven_52, undriven_53, undriven_54, undriven_55, undriven_56;
  wire [2:0] \n4位寄存器_1_q_3 , register_1_q;

  \_4位寄存器  \u_4位寄存器_1  (
    .EN(EN), .RESET(RESET), .clk(clk_out), .D_0(\n4位寄存器_1_q_0 ), .D_1(adder_3_out), .D_2(adder_2_out),
    .D_3(adder_1_out), .Q_0(\n4位寄存器_1_q_0 ), .Q_1(\n4位寄存器_1_q_3 [2]), .Q_2(\n4位寄存器_1_q_3 [1]),
    .Q_3(\n4位寄存器_1_q_3 [0]));
  Clock clk (.out(clk_out));
  Adder #(.width(1)) adder_1 (.a(\n4位寄存器_1_q_3 [0]), .b(1'b1), .out(adder_1_out), .cin(1'b0), .cout(adder_1_cout));
  Adder #(.width(1)) adder_2 (
    .a(\n4位寄存器_1_q_3 [1]), .b(1'b0), .out(adder_2_out), .cin(adder_1_cout), .cout(adder_2_cout));
  Adder #(.width(1)) adder_3 (.a(\n4位寄存器_1_q_3 [2]), .b(1'b0), .out(adder_3_out), .cin(adder_2_cout));  // open: cout
  Register #(.width(3)) register_1 (.D(\n4位寄存器_1_q_3 ), .en(EN), .Q(register_1_q), .clk(clk_out), .clr(RESET));
  Decoder #(.select(3), .enable("false")) decoder_1 (
    .out0(decoder_1_out0), .out1(decoder_1_out1), .out2(decoder_1_out2), .out3(decoder_1_out3),
    .out4(decoder_1_out4), .out5(decoder_1_out5), .out6(decoder_1_out6), .out7(decoder_1_out7),
    .sel(register_1_q));
  buf and_1 (and_1_out, decoder_1_out0);  // AND_Gate
  buf and_2 (and_2_out, decoder_1_out1);  // AND_Gate
  buf and_3 (and_3_out, decoder_1_out2);  // AND_Gate
  buf and_4 (and_4_out, decoder_1_out3);  // AND_Gate
  buf and_5 (and_5_out, decoder_1_out4);  // AND_Gate
  buf and_6 (and_6_out, decoder_1_out5);  // AND_Gate
  buf and_7 (and_7_out, decoder_1_out6);  // AND_Gate
  buf and_8 (and_8_out, decoder_1_out7);  // AND_Gate
  or or_1 (or_1_out, and_8_out, and_7_out, and_6_out, and_5_out, and_4_out, and_3_out, and_2_out, and_1_out);
  and and_9 (and_9_out, decoder_1_out0, undriven);
  and and_10 (and_10_out, decoder_1_out1, undriven_2);
  and and_11 (and_11_out, decoder_1_out2, undriven_3);
  and and_12 (and_12_out, decoder_1_out3, undriven_4);
  and and_13 (and_13_out, decoder_1_out4, undriven_5);
  and and_14 (and_14_out, decoder_1_out5, undriven_6);
  and and_15 (and_15_out, decoder_1_out6, undriven_7);
  and and_16 (and_16_out, decoder_1_out7, undriven_8);
  or or_2 (or_2_out, and_16_out, and_15_out, and_14_out, and_13_out, and_12_out, and_11_out, and_10_out, and_9_out);
  and and_17 (and_17_out, decoder_1_out0, undriven_9);
  and and_18 (and_18_out, decoder_1_out1, undriven_10);
  and and_19 (and_19_out, decoder_1_out2, undriven_11);
  and and_20 (and_20_out, decoder_1_out3, undriven_12);
  and and_21 (and_21_out, decoder_1_out4, undriven_13);
  and and_22 (and_22_out, decoder_1_out5, undriven_14);
  and and_23 (and_23_out, decoder_1_out6, undriven_15);
  and and_24 (and_24_out, decoder_1_out7, undriven_16);
  // OR_Gate or_3 has open pins: in0=and_24_out, in1=and_23_out, in2=and_22_out, in3=and_21_out, in4=and_20_out, in5=and_19_out, in6=and_18_out, in7=and_17_out, out=open
  and and_25 (and_25_out, decoder_1_out0, undriven_17);
  and and_26 (and_26_out, decoder_1_out1, undriven_18);
  and and_27 (and_27_out, decoder_1_out2, undriven_19);
  and and_28 (and_28_out, decoder_1_out3, undriven_20);
  and and_29 (and_29_out, decoder_1_out4, undriven_21);
  and and_30 (and_30_out, decoder_1_out5, undriven_22);
  and and_31 (and_31_out, decoder_1_out6, undriven_23);
  and and_32 (and_32_out, decoder_1_out7, undriven_24);
  // OR_Gate or_4 has open pins: in0=and_32_out, in1=and_31_out, in2=and_30_out, in3=and_29_out, in4=and_28_out, in5=and_27_out, in6=and_26_out, in7=and_25_out, out=open
  and and_33 (and_33_out, decoder_1_out0, undriven_25);
  and and_34 (and_34_out, decoder_1_out1, undriven_26);
  and and_35 (and_35_out, decoder_1_out2, undriven_27);
  and and_36 (and_36_out, decoder_1_out3, undriven_28);
  and and_37 (and_37_out, decoder_1_out4, undriven_29);
  and and_38 (and_38_out, decoder_1_out5, undriven_30);
  and and_39 (and_39_out, decoder_1_out6, undriven_31);
  and and_40 (and_40_out, decoder_1_out7, undriven_32);
  // OR_Gate or_5 has open pins: in0=and_40_out, in1=and_39_out, in2=and_38_out, in3=and_37_out, in4=and_36_out, in5=and_35_out, in6=and_34_out, in7=and_33_out, out=open
  and and_41 (and_41_out, decoder_1_out0, undriven_33);
  and and_42 (and_42_out, decoder_1_out1, undriven_34);
  and and_43 (and_43_out, decoder_1_out2, undriven_35);
  and and_44 (and_44_out, decoder_1_out3, undriven_36);
  and and_45 (and_45_out, decoder_1_out4, undriven_37);
  and and_46 (and_46_out, decoder_1_out5, undriven_38);
  and and_47 (and_47_out, decoder_1_out6, undriven_39);
  and and_48 (and_48_out, decoder_1_out7, undriven_40);
  // OR_Gate or_6 has open pins: in0=and_48_out, in1=and_47_out, in2=and_46_out, in3=and_45_out, in4=and_44_out, in5=and_43_out, in6=and_42_out, in7=and_41_out, out=open
  and and_49 (and_49_out, decoder_1_out0, undriven_41);
  and and_50 (and_50_out, decoder_1_out1, undriven_42);
  and and_51 (and_51_out, decoder_1_out2, undriven_43);
  and and_52 (and_52_out, decoder_1_out3, undriven_44);
  and and_53 (and_53_out, decoder_1_out4, undriven_45);
  and and_54 (and_54_out, decoder_1_out5, undriven_46);
  and and_55 (and_55_out, decoder_1_out6, undriven_47);
  and and_56 (and_56_out, decoder_1_out7, undriven_48);
  // OR_Gate or_7 has open pins: in0=and_56_out, in1=and_55_out, in2=and_54_out, in3=and_53_out, in4=and_52_out, in5=and_51_out, in6=and_50_out, in7=and_49_out, out=open
  and and_57 (and_57_out, decoder_1_out0, undriven_49);
  and and_58 (and_58_out, decoder_1_out1, undriven_50);
  and and_59 (and_59_out, decoder_1_out2, undriven_51);
  and and_60 (and_60_out, decoder_1_out3, undriven_52);
  and and_61 (and_61_out, decoder_1_out4, undriven_53);
  and and_62 (and_62_out, decoder_1_out5, undriven_54);
  and and_63 (and_63_out, decoder_1_out6, undriven_55);
  and and_64 (and_64_out, decoder_1_out7, undriven_56);
  // OR_Gate or_8 has open pins: in0=and_64_out, in1=and_63_out, in2=and_62_out, in3=and_61_out, in4=and_60_out, in5=and_59_out, in6=and_58_out, in7=and_57_out, out=open
endmodule

module RAM (
  input  RESET,
  input  D_7,
  input  D_6,
  input  D_5,
  input  D_4,
  input  D_3,
  input  D_2,
  input  D_1,
  input  D_0,
  input  EN_CHANGE,
  input  EN
);

  wire adder_1_cout, adder_1_out, adder_2_cout, adder_2_out, adder_3_out, and_1_out, and_2_out, and_3_out,
       and_4_out, and_5_out, and_6_out, and_7_out, and_8_out, and_9_out, and_10_out, and_11_out, and_12_out,
       and_13_out, and_14_out, and_15_out, and_16_out, and_17_out, and_18_out, and_19_out, and_20_out,
       and_21_out, and_22_out, and_23_out, and_24_out, and_25_out, and_26_out, and_27_out, and_28_out,
       and_29_out, and_30_out, and_31_out, and_32_out, and_33_out, and_34_out, and_35_out, and_36_out,
       and_37_out, and_38_out, and_39_out, and_40_out, and_41_out, and_42_out, and_43_out, and_44_out,
       and_45_out, and_46_out, and_47_out, and_48_out, and_49_out, and_50_out, and_51_out, and_52_out,
       and_53_out, and_54_out, and_55_out, and_56_out, and_57_out, and_58_out, and_59_out, and_60_out,
       and_61_out, and_62_out, and_63_out, and_64_out, and_65_out, and_66_out, and_67_out, and_68_out,
       and_69_out, and_70_out, and_71_out, and_72_out, clk_out, decoder_1_out0, decoder_1_out1,
       decoder_1_out2, decoder_1_out3, decoder_1_out4, decoder_1_out5, decoder_1_out6, decoder_1_out7,
       \d触发器_带使能端_1_q , \d触发器_带使能端_2_q , \d触发器_带使能端_3_q , \d触发器_带使能端_4_q , \d触发器_带使能端_5_q , \d触发器_带使能端_6_q ,
       \d触发器_带使能端_7_q , \d触发器_带使能端_8_q , \d触发器_带使能端_9_q , \d触发器_带使能端_10_q , \d触发器_带使能端_11_q ,
       \d触发器_带使能端_12_q , \d触发器_带使能端_13_q , \d触发器_带使能端_14_q , \d触发器_带使能端_15_q , \d触发器_带使能端_16_q ,
       \d触发器_带使能端_17_q , \d触发器_带使能端_18_q , \d触发器_带使能端_19_q , \d触发器_带使能端_20_q , \d触发器_带使能端_21_q ,
       \d触发器_带使能端_22_q , \d触发器_带使能端_23_q , \d触发器_带使能端_24_q , \d触发器_带使能端_25_q , \d触发器_带使能端_26_q ,
       \d触发器_带使能端_27_q , \d触发器_带使能端_28_q , \d触发器_带使能端_29_q , \d触发器_带使能端_30_q , \d触发器_带使能端_31_q ,
       \d触发器_带使能端_32_q , \d触发器_带使能端_33_q , \d触发器_带使能端_34_q , \d触发器_带使能端_35_q , \d触发器_带使能端_36_q ,
       \d触发器_带使能端_37_q , \d触发器_带使能端_38_q , \d触发器_带使能端_39_q , \d触发器_带使能端_40_q , \d触发器_带使能端_41_q ,
       \d触发器_带使能端_42_q , \d触发器_带使能端_43_q , \d触发器_带使能端_44_q , \d触发器_带使能端_45_q , \d触发器_带使能端_46_q ,
       \d触发器_带使能端_47_q , \d触发器_带使能端_48_q , \d触发器_带使能端_49_q , \d触发器_带使能端_50_q , \d触发器_带使能端_51_q ,
       \d触发器_带使能端_52_q , \d触发器_带使能端_53_q , \d触发器_带使能端_54_q , \d触发器_带使能端_55_q , \d触发器_带使能端_56_q ,
       \d触发器_带使能端_57_q , \d触发器_带使能端_58_q , \d触发器_带使能端_59_q , \d触发器_带使能端_60_q , \d触发器_带使能端_61_q ,
       \d触发器_带使能端_62_q , \d触发器_带使能端_63_q , \d触发器_带使能端_64_q , \n4位寄存器_1_q_0 , or_1_out, or_2_out, or_3_out,
       or_4_out, or_5_out, or_6_out, or_7_out, or_8_out;
  wire [2:0] \n4位寄存器_1_q_3 , register_1_q;

  \_4位寄存器  \u_4位寄存器_1  (
    .EN(EN), .RESET(RESET), .clk(clk_out), .D_0(\n4位寄存器_1_q_0 ), .D_1(adder_3_out), .D_2(adder_2_out),
    .D_3(adder_1_out), .Q_0(\n4位寄存器_1_q_0 ), .Q_1(\n4位寄存器_1_q_3 [2]), .Q_2(\n4位寄存器_1_q_3 [1]),
    .Q_3(\n4位寄存器_1_q_3 [0]));
  Clock clk (.out(clk_out));
  Adder #(.width(1)) adder_1 (.a(\n4位寄存器_1_q_3 [0]), .b(1'b1), .out(adder_1_out), .cin(1'b0), .cout(adder_1_cout));
  Adder #(.width(1)) adder_2 (
    .a(\n4位寄存器_1_q_3 [1]), .b(1'b0), .out(adder_2_out), .cin(adder_1_cout), .cout(adder_2_cout));
  Adder #(.width(1)) adder_3 (.a(\n4位寄存器_1_q_3 [2]), .b(1'b0), .out(adder_3_out), .cin(adder_2_cout));  // open: cout
  Register #(.width(3)) register_1 (.D(\n4位寄存器_1_q_3 ), .en(EN), .Q(register_1_q), .clk(clk_out), .clr(RESET));
  Decoder #(.select(3), .enable("false")) decoder_1 (
    .out0(decoder_1_out0), .out1(decoder_1_out1), .out2(decoder_1_out2), .out3(decoder_1_out3),
    .out4(decoder_1_out4), .out5(decoder_1_out5), .out6(decoder_1_out6), .out7(decoder_1_out7),
    .sel(register_1_q));
  and and_1 (and_1_out, decoder_1_out0, EN_CHANGE);
  and and_2 (and_2_out, decoder_1_out1, EN_CHANGE);
  and and_3 (and_3_out, decoder_1_out2, EN_CHANGE);
  and and_4 (and_4_out, decoder_1_out3, EN_CHANGE);
  and and_5 (and_5_out, decoder_1_out4, EN_CHANGE);
  and and_6 (and_6_out, decoder_1_out5, EN_CHANGE);
  and and_7 (and_7_out, decoder_1_out6, EN_CHANGE);
  and and_8 (and_8_out, decoder_1_out7, EN_CHANGE);
  \D触发器_带使能端  \d触发器_带使能端_1  (.EN(and_1_out), .RESET(RESET), .clk(clk_out), .D(D_7), .Q(\d触发器_带使能端_1_q ));
  \D触发器_带使能端  \d触发器_带使能端_2  (.EN(and_2_out), .RESET(RESET), .clk(clk_out), .D(D_7), .Q(\d触发器_带使能端_2_q ));
  \D触发器_带使能端  \d触发器_带使能端_3  (.EN(and_3_out), .RESET(RESET), .clk(clk_out), .D(D_7), .Q(\d触发器_带使能端_3_q ));
  \D触发器_带使能端  \d触发器_带使能端_4  (.EN(and_4_out), .RESET(RESET), .clk(clk_out), .D(D_7), .Q(\d触发器_带使能端_4_q ));
  \D触发器_带使能端  \d触发器_带使能端_5  (.EN(and_5_out), .RESET(RESET), .clk(clk_out), .D(D_7), .Q(\d触发器_带使能端_5_q ));
  \D触发器_带使能端  \d触发器_带使能端_6  (.EN(and_6_out), .RESET(RESET), .clk(clk_out), .D(D_7), .Q(\d触发器_带使能端_6_q ));
  \D触发器_带使能端  \d触发器_带使能端_7  (.EN(and_7_out), .RESET(RESET), .clk(clk_out), .D(D_7), .Q(\d触发器_带使能端_7_q ));
  \D触发器_带使能端  \d触发器_带使能端_8  (.EN(and_8_out), .RESET(RESET), .clk(clk_out), .D(D_7), .Q(\d触发器_带使能端_8_q ));
  and and_9 (and_9_out, decoder_1_out0, \d触发器_带使能端_1_q );
  and and_10 (and_10_out, decoder_1_out1, \d触发器_带使能端_2_q );
  and and_11 (and_11_out, decoder_1_out2, \d触发器_带使能端_3_q );
  and and_12 (and_12_out, decoder_1_out3, \d触发器_带使能端_4_q );
  and and_13 (and_13_out, decoder_1_out4, \d触发器_带使能端_5_q );
  and and_14 (and_14_out, decoder_1_out5, \d触发器_带使能端_6_q );
  and and_15 (and_15_out, decoder_1_out6, \d触发器_带使能端_7_q );
  and and_16 (and_16_out, decoder_1_out7, \d触发器_带使能端_8_q );
  or or_1 (or_1_out, and_16_out, and_15_out, and_14_out, and_13_out, and_12_out, and_11_out, and_10_out, and_9_out);
  and and_17 (and_17_out, decoder_1_out0, \d触发器_带使能端_9_q );
  \D触发器_带使能端  \d触发器_带使能端_9  (.EN(and_1_out), .RESET(RESET), .clk(clk_out), .D(D_6), .Q(\d触发器_带使能端_9_q ));
  and and_18 (and_18_out, decoder_1_out1, \d触发器_带使能端_10_q );
  \D触发器_带使能端  \d触发器_带使能端_10  (.EN(and_2_out), .RESET(RESET), .clk(clk_out), .D(D_6), .Q(\d触发器_带使能端_10_q ));
  and and_19 (and_19_out, decoder_1_out2, \d触发器_带使能端_11_q );
  \D触发器_带使能端  \d触发器_带使能端_11  (.EN(and_3_out), .RESET(RESET), .clk(clk_out), .D(D_6), .Q(\d触发器_带使能端_11_q ));
  and and_20 (and_20_out, decoder_1_out3, \d触发器_带使能端_12_q );
  \D触发器_带使能端  \d触发器_带使能端_12  (.EN(and_4_out), .RESET(RESET), .clk(clk_out), .D(D_6), .Q(\d触发器_带使能端_12_q ));
  and and_21 (and_21_out, decoder_1_out4, \d触发器_带使能端_13_q );
  \D触发器_带使能端  \d触发器_带使能端_13  (.EN(and_5_out), .RESET(RESET), .clk(clk_out), .D(D_6), .Q(\d触发器_带使能端_13_q ));
  and and_22 (and_22_out, decoder_1_out5, \d触发器_带使能端_14_q );
  \D触发器_带使能端  \d触发器_带使能端_14  (.EN(and_6_out), .RESET(RESET), .clk(clk_out), .D(D_6), .Q(\d触发器_带使能端_14_q ));
  and and_23 (and_23_out, decoder_1_out6, \d触发器_带使能端_15_q );
  \D触发器_带使能端  \d触发器_带使能端_15  (.EN(and_7_out), .RESET(RESET), .clk(clk_out), .D(D_6), .Q(\d触发器_带使能端_15_q ));
  and and_24 (and_24_out, decoder_1_out7, \d触发器_带使能端_16_q );
  \D触发器_带使能端  \d触发器_带使能端_16  (.EN(and_8_out), .RESET(RESET), .clk(clk_out), .D(D_6), .Q(\d触发器_带使能端_16_q ));
  or or_2 (or_2_out, and_24_out, and_23_out, and_22_out, and_21_out, and_20_out, and_19_out, and_18_out, and_17_out);
  and and_25 (and_25_out, decoder_1_out0, \d触发器_带使能端_17_q );
  \D触发器_带使能端  \d触发器_带使能端_17  (.EN(and_1_out), .RESET(RESET), .clk(clk_out), .D(D_5), .Q(\d触发器_带使能端_17_q ));
  and and_26 (and_26_out, decoder_1_out1, \d触发器_带使能端_18_q );
  \D触发器_带使能端  \d触发器_带使能端_18  (.EN(and_2_out), .RESET(RESET), .clk(clk_out), .D(D_5), .Q(\d触发器_带使能端_18_q ));
  and and_27 (and_27_out, decoder_1_out2, \d触发器_带使能端_19_q );
  \D触发器_带使能端  \d触发器_带使能端_19  (.EN(and_3_out), .RESET(RESET), .clk(clk_out), .D(D_5), .Q(\d触发器_带使能端_19_q ));
  and and_28 (and_28_out, decoder_1_out3, \d触发器_带使能端_20_q );
  \D触发器_带使能端  \d触发器_带使能端_20  (.EN(and_4_out), .RESET(RESET), .clk(clk_out), .D(D_5), .Q(\d触发器_带使能端_20_q ));
  and and_29 (and_29_out, decoder_1_out4, \d触发器_带使能端_21_q );
  \D触发器_带使能端  \d触发器_带使能端_21  (.EN(and_5_out), .RESET(RESET), .clk(clk_out), .D(D_5), .Q(\d触发器_带使能端_21_q ));
  and and_30 (and_30_out, decoder_1_out5, \d触发器_带使能端_22_q );
  \D触发器_带使能端  \d触发器_带使能端_22  (.EN(and_6_out), .RESET(RESET), .clk(clk_out), .D(D_5), .Q(\d触发器_带使能端_22_q ));
  and and_31 (and_31_out, decoder_1_out6, \d触发器_带使能端_23_q );
  \D触发器_带使能端  \d触发器_带使能端_23  (.EN(and_7_out), .RESET(RESET), .clk(clk_out), .D(D_5), .Q(\d触发器_带使能端_23_q ));
  and and_32 (and_32_out, decoder_1_out7, \d触发器_带使能端_24_q );
  \D触发器_带使能端  \d触发器_带使能端_24  (.EN(and_8_out), .RESET(RESET), .clk(clk_out), .D(D_5), .Q(\d触发器_带使能端_24_q ));
  or or_3 (or_3_out, and_32_out, and_31_out, and_30_out, and_29_out, and_28_out, and_27_out, and_26_out, and_25_out);
  \D触发器_带使能端  \d触发器_带使能端_25  (.EN(and_1_out), .RESET(RESET), .clk(clk_out), .D(D_4), .Q(\d触发器_带使能端_25_q ));
  \D触发器_带使能端  \d触发器_带使能端_26  (.EN(and_2_out), .RESET(RESET), .clk(clk_out), .D(D_4), .Q(\d触发器_带使能端_26_q ));
  \D触发器_带使能端  \d触发器_带使能端_27  (.EN(and_3_out), .RESET(RESET), .clk(clk_out), .D(D_4), .Q(\d触发器_带使能端_27_q ));
  \D触发器_带使能端  \d触发器_带使能端_28  (.EN(and_4_out), .RESET(RESET), .clk(clk_out), .D(D_4), .Q(\d触发器_带使能端_28_q ));
  \D触发器_带使能端  \d触发器_带使能端_29  (.EN(and_5_out), .RESET(RESET), .clk(clk_out), .D(D_4), .Q(\d触发器_带使能端_29_q ));
  \D触发器_带使能端  \d触发器_带使能端_30  (.EN(and_6_out), .RESET(RESET), .clk(clk_out), .D(D_4), .Q(\d触发器_带使能端_30_q ));
  \D触发器_带使能端  \d触发器_带使能端_31  (.EN(and_7_out), .RESET(RESET), .clk(clk_out), .D(D_4), .Q(\d触发器_带使能端_31_q ));
  \D触发器_带使能端  \d触发器_带使能端_32  (.EN(and_8_out), .RESET(RESET), .clk(clk_out), .D(D_4), .Q(\d触发器_带使能端_32_q ));
  and and_33 (and_33_out, decoder_1_out0, \d触发器_带使能端_25_q );
  and and_34 (and_34_out, decoder_1_out1, \d触发器_带使能端_26_q );
  and and_35 (and_35_out, decoder_1_out2, \d触发器_带使能端_27_q );
  and and_36 (and_36_out, decoder_1_out3, \d触发器_带使能端_28_q );
  and and_37 (and_37_out, decoder_1_out4, \d触发器_带使能端_29_q );
  and and_38 (and_38_out, decoder_1_out5, \d触发器_带使能端_30_q );
  and and_39 (and_39_out, decoder_1_out6, \d触发器_带使能端_31_q );
  and and_40 (and_40_out, decoder_1_out7, \d触发器_带使能端_32_q );
  or or_4 (or_4_out, and_40_out, and_39_out, and_38_out, and_37_out, and_36_out, and_35_out, and_34_out, and_33_out);
  \D触发器_带使能端  \d触发器_带使能端_33  (.EN(and_1_out), .RESET(RESET), .clk(clk_out), .D(D_3), .Q(\d触发器_带使能端_33_q ));
  \D触发器_带使能端  \d触发器_带使能端_34  (.EN(and_2_out), .RESET(RESET), .clk(clk_out), .D(D_3), .Q(\d触发器_带使能端_34_q ));
  \D触发器_带使能端  \d触发器_带使能端_35  (.EN(and_3_out), .RESET(RESET), .clk(clk_out), .D(D_3), .Q(\d触发器_带使能端_35_q ));
  \D触发器_带使能端  \d触发器_带使能端_36  (.EN(and_4_out), .RESET(RESET), .clk(clk_out), .D(D_3), .Q(\d触发器_带使能端_36_q ));
  \D触发器_带使能端  \d触发器_带使能端_37  (.EN(and_5_out), .RESET(RESET), .clk(clk_out), .D(D_3), .Q(\d触发器_带使能端_37_q ));
  \D触发器_带使能端  \d触发器_带使能端_38  (.EN(and_6_out), .RESET(RESET), .clk(clk_out), .D(D_3), .Q(\d触发器_带使能端_38_q ));
  \D触发器_带使能端  \d触发器_带使能端_39  (.EN(and_7_out), .RESET(RESET), .clk(clk_out), .D(D_3), .Q(\d触发器_带使能端_39_q ));
  \D触发器_带使能端  \d触发器_带使能端_40  (.EN(and_8_out), .RESET(RESET), .clk(clk_out), .D(D_3), .Q(\d触发器_带使能端_40_q ));
  and and_41 (and_41_out, decoder_1_out0, \d触发器_带使能端_33_q );
  and and_42 (and_42_out, decoder_1_out1, \d触发器_带使能端_34_q );
  and and_43 (and_43_out, decoder_1_out2, \d触发器_带使能端_35_q );
  and and_44 (and_44_out, decoder_1_out3, \d触发器_带使能端_36_q );
  and and_45 (and_45_out, decoder_1_out4, \d触发器_带使能端_37_q );
  and and_46 (and_46_out, decoder_1_out5, \d触发器_带使能端_38_q );
  and and_47 (and_47_out, decoder_1_out6, \d触发器_带使能端_39_q );
  and and_48 (and_48_out, decoder_1_out7, \d触发器_带使能端_40_q );
  or or_5 (or_5_out, and_48_out, and_47_out, and_46_out, and_45_out, and_44_out, and_43_out, and_42_out, and_41_out);
  \D触发器_带使能端  \d触发器_带使能端_41  (.EN(and_1_out), .RESET(RESET), .clk(clk_out), .D(D_2), .Q(\d触发器_带使能端_41_q ));
  \D触发器_带使能端  \d触发器_带使能端_42  (.EN(and_2_out), .RESET(RESET), .clk(clk_out), .D(D_2), .Q(\d触发器_带使能端_42_q ));
  \D触发器_带使能端  \d触发器_带使能端_43  (.EN(and_3_out), .RESET(RESET), .clk(clk_out), .D(D_2), .Q(\d触发器_带使能端_43_q ));
  \D触发器_带使能端  \d触发器_带使能端_44  (.EN(and_4_out), .RESET(RESET), .clk(clk_out), .D(D_2), .Q(\d触发器_带使能端_44_q ));
  \D触发器_带使能端  \d触发器_带使能端_45  (.EN(and_5_out), .RESET(RESET), .clk(clk_out), .D(D_2), .Q(\d触发器_带使能端_45_q ));
  \D触发器_带使能端  \d触发器_带使能端_46  (.EN(and_6_out), .RESET(RESET), .clk(clk_out), .D(D_2), .Q(\d触发器_带使能端_46_q ));
  \D触发器_带使能端  \d触发器_带使能端_47  (.EN(and_7_out), .RESET(RESET), .clk(clk_out), .D(D_2), .Q(\d触发器_带使能端_47_q ));
  \D触发器_带使能端  \d触发器_带使能端_48  (.EN(decoder_1_out7), .RESET(RESET), .clk(clk_out), .D(D_2), .Q(\d触发器_带使能端_48_q ));
  and and_49 (and_49_out, decoder_1_out0, \d触发器_带使能端_41_q );
  and and_50 (and_50_out, decoder_1_out1, \d触发器_带使能端_42_q );
  and and_51 (and_51_out, decoder_1_out2, \d触发器_带使能端_43_q );
  and and_52 (and_52_out, decoder_1_out3, \d触发器_带使能端_44_q );
  and and_53 (and_53_out, decoder_1_out4, \d触发器_带使能端_45_q );
  and and_54 (and_54_out, decoder_1_out5, \d触发器_带使能端_46_q );
  and and_55 (and_55_out, decoder_1_out6, \d触发器_带使能端_47_q );
  and and_56 (and_56_out, decoder_1_out7, \d触发器_带使能端_48_q );
  or or_6 (or_6_out, and_56_out, and_55_out, and_54_out, and_53_out, and_52_out, and_51_out, and_50_out, and_49_out);
  \D触发器_带使能端  \d触发器_带使能端_49  (.EN(and_1_out), .RESET(RESET), .clk(clk_out), .D(D_1), .Q(\d触发器_带使能端_49_q ));
  \D触发器_带使能端  \d触发器_带使能端_50  (.EN(and_2_out), .RESET(RESET), .clk(clk_out), .D(D_1), .Q(\d触发器_带使能端_50_q ));
  \D触发器_带使能端  \d触发器_带使能端_51  (.EN(and_3_out), .RESET(RESET), .clk(clk_out), .D(D_1), .Q(\d触发器_带使能端_51_q ));
  \D触发器_带使能端  \d触发器_带使能端_52  (.EN(and_4_out), .RESET(RESET), .clk(clk_out), .D(D_1), .Q(\d触发器_带使能端_52_q ));
  \D触发器_带使能端  \d触发器_带使能端_53  (.EN(and_5_out), .RESET(RESET), .clk(clk_out), .D(D_1), .Q(\d触发器_带使能端_53_q ));
  \D触发器_带使能端  \d触发器_带使能端_54  (.EN(and_6_out), .RESET(RESET), .clk(clk_out), .D(D_1), .Q(\d触发器_带使能端_54_q ));
  \D触发器_带使能端  \d触发器_带使能端_55  (.EN(and_7_out), .RESET(RESET), .clk(clk_out), .D(D_1), .Q(\d触发器_带使能端_55_q ));
  \D触发器_带使能端  \d触发器_带使能端_56  (.EN(and_8_out), .RESET(RESET), .clk(clk_out), .D(D_1), .Q(\d触发器_带使能端_56_q ));
  and and_57 (and_57_out, decoder_1_out0, \d触发器_带使能端_49_q );
  and and_58 (and_58_out, decoder_1_out1, \d触发器_带使能端_50_q );
  and and_59 (and_59_out, decoder_1_out2, \d触发器_带使能端_51_q );
  and and_60 (and_60_out, decoder_1_out3, \d触发器_带使能端_52_q );
  and and_61 (and_61_out, decoder_1_out4, \d触发器_带使能端_53_q );
  and and_62 (and_62_out, decoder_1_out5, \d触发器_带使能端_54_q );
  and and_63 (and_63_out, decoder_1_out6, \d触发器_带使能端_55_q );
  and and_64 (and_64_out, decoder_1_out7, \d触发器_带使能端_56_q );
  or or_7 (or_7_out, and_64_out, and_63_out, and_62_out, and_61_out, and_60_out, and_59_out, and_58_out, and_57_out);
  \D触发器_带使能端  \d触发器_带使能端_57  (.EN(and_1_out), .RESET(RESET), .clk(clk_out), .D(D_0), .Q(\d触发器_带使能端_57_q ));
  \D触发器_带使能端  \d触发器_带使能端_58  (.EN(and_2_out), .RESET(RESET), .clk(clk_out), .D(D_0), .Q(\d触发器_带使能端_58_q ));
  \D触发器_带使能端  \d触发器_带使能端_59  (.EN(and_3_out), .RESET(RESET), .clk(clk_out), .D(D_0), .Q(\d触发器_带使能端_59_q ));
  \D触发器_带使能端  \d触发器_带使能端_60  (.EN(and_4_out), .RESET(RESET), .clk(clk_out), .D(D_0), .Q(\d触发器_带使能端_60_q ));
  \D触发器_带使能端  \d触发器_带使能端_61  (.EN(and_5_out), .RESET(RESET), .clk(clk_out), .D(D_0), .Q(\d触发器_带使能端_61_q ));
  \D触发器_带使能端  \d触发器_带使能端_62  (.EN(and_6_out), .RESET(RESET), .clk(clk_out), .D(D_0), .Q(\d触发器_带使能端_62_q ));
  \D触发器_带使能端  \d触发器_带使能端_63  (.EN(and_7_out), .RESET(RESET), .clk(clk_out), .D(D_0), .Q(\d触发器_带使能端_63_q ));
  \D触发器_带使能端  \d触发器_带使能端_64  (.EN(and_8_out), .RESET(RESET), .clk(clk_out), .D(D_0), .Q(\d触发器_带使能端_64_q ));
  and and_65 (and_65_out, decoder_1_out0, \d触发器_带使能端_57_q );
  and and_66 (and_66_out, decoder_1_out1, \d触发器_带使能端_58_q );
  and and_67 (and_67_out, decoder_1_out2, \d触发器_带使能端_59_q );
  and and_68 (and_68_out, decoder_1_out3, \d触发器_带使能端_60_q );
  and and_69 (and_69_out, decoder_1_out4, \d触发器_带使能端_61_q );
  and and_70 (and_70_out, decoder_1_out5, \d触发器_带使能端_62_q );
  and and_71 (and_71_out, decoder_1_out6, \d触发器_带使能端_63_q );
  and and_72 (and_72_out, decoder_1_out7, \d触发器_带使能端_64_q );
  or or_8 (or_8_out, and_72_out, and_71_out, and_70_out, and_69_out, and_68_out, and_67_out, and_66_out, and_65_out);
endmodule

module sCPU (
  input  RESET,
  input  D_7,
  input  D_6,
  input  D_5,
  input  D_4,
  input  D_3,
  input  D_2,
  input  D_1,
  input  D_0,
  input  EN_CHANGE,
  input  RESET_2,
  input  EN,
  input  RESET_3
);

  wire adder_1_cout, adder_1_out, adder_2_cout, adder_2_out, adder_3_out, adder_4_cout, adder_4_out,
       adder_5_cout, adder_5_out, adder_6_out, and_1_out, and_2_out, and_3_out, and_4_out, and_5_out,
       and_6_out, and_7_out, and_8_out, and_9_out, and_10_out, and_11_out, and_12_out, and_13_out,
       and_14_out, and_15_out, and_16_out, and_17_out, and_18_out, and_19_out, and_20_out, and_21_out,
       and_22_out, and_23_out, and_24_out, and_25_out, and_26_out, and_27_out, and_28_out, and_29_out,
       and_30_out, and_31_out, and_32_out, and_33_out, and_34_out, and_35_out, and_36_out, and_37_out,
       and_38_out, and_39_out, and_40_out, and_41_out, and_45_out, and_46_out, and_47_out, and_48_out,
       and_49_out, and_50_out, and_51_out, and_52_out, and_57_out, and_58_out, and_59_out, and_60_out,
       and_61_out, and_62_out, and_63_out, and_64_out, and_67_out, and_68_out, and_69_out, and_70_out,
       and_71_out, and_72_out, and_73_out, and_74_out, and_75_out, and_76_out, and_77_out, and_78_out,
       and_79_out, and_80_out, and_81_out, and_82_out, clk_out, comparator_1_eq, decoder_1_out0,
       decoder_1_out1, decoder_1_out2, decoder_1_out3, decoder_1_out4, decoder_1_out5, decoder_1_out6,
       decoder_1_out7, decoder_2_out0, decoder_2_out1, decoder_2_out2, decoder_2_out3, decoder_3_out0,
       decoder_3_out2, decoder_3_out3, \d触发器_带使能端_1_q , \d触发器_带使能端_2_q , \d触发器_带使能端_3_q , \d触发器_带使能端_4_q ,
       \d触发器_带使能端_5_q , \d触发器_带使能端_6_q , \d触发器_带使能端_7_q , \d触发器_带使能端_8_q , \d触发器_带使能端_9_q , \d触发器_带使能端_10_q ,
       \d触发器_带使能端_11_q , \d触发器_带使能端_12_q , \d触发器_带使能端_13_q , \d触发器_带使能端_14_q , \d触发器_带使能端_15_q ,
       \d触发器_带使能端_16_q , \d触发器_带使能端_17_q , \d触发器_带使能端_18_q , \d触发器_带使能端_19_q , \d触发器_带使能端_20_q ,
       \d触发器_带使能端_21_q , \d触发器_带使能端_22_q , \d触发器_带使能端_23_q , \d触发器_带使能端_24_q , \d触发器_带使能端_25_q ,
       \d触发器_带使能端_26_q , \d触发器_带使能端_27_q , \d触发器_带使能端_28_q , \d触发器_带使能端_29_q , \d触发器_带使能端_30_q ,
       \d触发器_带使能端_31_q , \d触发器_带使能端_32_q , \d触发器_带使能端_33_q , \d触发器_带使能端_34_q , \d触发器_带使能端_35_q ,
       \d触发器_带使能端_36_q , \d触发器_带使能端_37_q , \d触发器_带使能端_38_q , \d触发器_带使能端_39_q , \d触发器_带使能端_40_q ,
       \d触发器_带使能端_41_q , \d触发器_带使能端_42_q , \d触发器_带使能端_43_q , \d触发器_带使能端_44_q , \d触发器_带使能端_45_q ,
       \d触发器_带使能端_46_q , \d触发器_带使能端_47_q , \d触发器_带使能端_48_q , \d触发器_带使能端_49_q , \d触发器_带使能端_50_q ,
       \d触发器_带使能端_51_q , \d触发器_带使能端_52_q , \d触发器_带使能端_53_q , \d触发器_带使能端_54_q , \d触发器_带使能端_55_q ,
       \d触发器_带使能端_56_q , \d触发器_带使能端_57_q , \d触发器_带使能端_58_q , \d触发器_带使能端_59_q , \d触发器_带使能端_60_q ,
       \d触发器_带使能端_61_q , \d触发器_带使能端_62_q , \d触发器_带使能端_63_q , \d触发器_带使能端_64_q , multiplexer_2_out,
       multiplexer_3_out, multiplexer_4_out, \n4位寄存器_1_q_0 , not_1_out, or_3_out, or_6_out, or_7_out,
       or_8_out, or_9_out;
  wire [1:0] and_65_out, and_83_out, and_86_out, or_2_out, or_5_out;
  wire [2:0] and_44_out, multiplexer_1_out, \n4位寄存器_1_q_3 , register_1_q;
  wire [3:0] and_56_out, multiplexer_5_out;
  wire [7:0] adder_7_out, multiplexer_6_out, multiplexer_7_out, multiplexer_8_out, register_2_q,
       register_3_q, register_4_q, register_5_q;
  wire [7:4] multiplexer_5_out_2;

  Hex_Digit_Display hex_digit_display_1 (.value({1'b0, \n4位寄存器_1_q_3 }));  // open: dp
  Hex_Digit_Display hex_digit_display_2 (.value({1'b0, and_44_out}));  // open: dp
  and and_1 (and_1_out, decoder_3_out3, not_1_out);
  \_4位寄存器  \u_4位寄存器_1  (
    .EN(EN), .RESET(RESET), .clk(clk_out), .D_0(\n4位寄存器_1_q_0 ), .D_1(multiplexer_2_out),
    .D_2(multiplexer_3_out), .D_3(multiplexer_4_out), .Q_0(\n4位寄存器_1_q_0 ), .Q_1(\n4位寄存器_1_q_3 [2]),
    .Q_2(\n4位寄存器_1_q_3 [1]), .Q_3(\n4位寄存器_1_q_3 [0]));
  Multiplexer #(.width(3), .enable("false")) multiplexer_1 (
    .in0(\n4位寄存器_1_q_3 ), .in1(and_44_out), .out(multiplexer_1_out), .sel(and_1_out));
  Multiplexer #(.enable("false")) multiplexer_2 (
    .in0(adder_3_out), .in1(adder_6_out), .out(multiplexer_2_out), .sel(and_1_out));
  Multiplexer #(.enable("false")) multiplexer_3 (
    .in0(adder_2_out), .in1(adder_5_out), .out(multiplexer_3_out), .sel(and_1_out));
  Multiplexer #(.enable("false")) multiplexer_4 (
    .in0(adder_1_out), .in1(adder_4_out), .out(multiplexer_4_out), .sel(and_1_out));
  Clock clk (.out(clk_out));
  Hex_Digit_Display hex_digit_display_3 (.value({1'b0, register_1_q}));  // open: dp
  not not_1 (not_1_out, comparator_1_eq);
  Adder #(.width(1)) adder_1 (.a(\n4位寄存器_1_q_3 [0]), .b(1'b1), .out(adder_1_out), .cin(1'b0), .cout(adder_1_cout));
  Adder #(.width(1)) adder_2 (
    .a(\n4位寄存器_1_q_3 [1]), .b(1'b0), .out(adder_2_out), .cin(adder_1_cout), .cout(adder_2_cout));
  Adder #(.width(1)) adder_3 (.a(\n4位寄存器_1_q_3 [2]), .b(1'b0), .out(adder_3_out), .cin(adder_2_cout));  // open: cout
  Decoder #(.select(3), .enable("false")) decoder_1 (
    .out0(decoder_1_out0), .out1(decoder_1_out1), .out2(decoder_1_out2), .out3(decoder_1_out3),
    .out4(decoder_1_out4), .out5(decoder_1_out5), .out6(decoder_1_out6), .out7(decoder_1_out7),
    .sel(register_1_q));
  Register #(.width(3)) register_1 (.D(multiplexer_1_out), .en(EN), .Q(register_1_q), .clk(clk_out), .clr(RESET));
  Adder #(.width(1)) adder_4 (.a(multiplexer_1_out[0]), .b(1'b1), .out(adder_4_out), .cin(1'b0), .cout(adder_4_cout));
  Adder #(.width(1)) adder_5 (
    .a(multiplexer_1_out[1]), .b(1'b0), .out(adder_5_out), .cin(adder_4_cout), .cout(adder_5_cout));
  Adder #(.width(1)) adder_6 (.a(multiplexer_1_out[2]), .b(1'b0), .out(adder_6_out), .cin(adder_5_cout));  // open: cout
  and and_2 (and_2_out, decoder_1_out0, EN_CHANGE);
  and and_3 (and_3_out, decoder_1_out1, EN_CHANGE);
  and and_4 (and_4_out, decoder_1_out2, EN_CHANGE);
  and and_5 (and_5_out, decoder_1_out3, EN_CHANGE);
  and and_6 (and_6_out, decoder_1_out4, EN_CHANGE);
  and and_7 (and_7_out, decoder_1_out5, EN_CHANGE);
  and and_8 (and_8_out, decoder_1_out6, EN_CHANGE);
  and and_9 (and_9_out, decoder_1_out7, EN_CHANGE);
  and and_10 (and_10_out, decoder_1_out0, \d触发器_带使能端_1_q );
  \D触发器_带使能端  \d触发器_带使能端_1  (.EN(and_2_out), .RESET(RESET_2), .clk(clk_out), .D(D_7), .Q(\d触发器_带使能端_1_q ));
  and and_11 (and_11_out, decoder_1_out1, \d触发器_带使能端_2_q );
  \D触发器_带使能端  \d触发器_带使能端_2  (.EN(and_3_out), .RESET(RESET_2), .clk(clk_out), .D(D_7), .Q(\d触发器_带使能端_2_q ));
  and and_12 (and_12_out, decoder_1_out2, \d触发器_带使能端_3_q );
  \D触发器_带使能端  \d触发器_带使能端_3  (.EN(and_4_out), .RESET(RESET_2), .clk(clk_out), .D(D_7), .Q(\d触发器_带使能端_3_q ));
  and and_13 (and_13_out, decoder_1_out3, \d触发器_带使能端_4_q );
  \D触发器_带使能端  \d触发器_带使能端_4  (.EN(and_5_out), .RESET(RESET_2), .clk(clk_out), .D(D_7), .Q(\d触发器_带使能端_4_q ));
  and and_14 (and_14_out, decoder_1_out4, \d触发器_带使能端_5_q );
  \D触发器_带使能端  \d触发器_带使能端_5  (.EN(and_6_out), .RESET(RESET_2), .clk(clk_out), .D(D_7), .Q(\d触发器_带使能端_5_q ));
  and and_15 (and_15_out, decoder_1_out5, \d触发器_带使能端_6_q );
  \D触发器_带使能端  \d触发器_带使能端_6  (.EN(and_7_out), .RESET(RESET_2), .clk(clk_out), .D(D_7), .Q(\d触发器_带使能端_6_q ));
  and and_16 (and_16_out, decoder_1_out6, \d触发器_带使能端_7_q );
  \D触发器_带使能端  \d触发器_带使能端_7  (.EN(and_8_out), .RESET(RESET_2), .clk(clk_out), .D(D_7), .Q(\d触发器_带使能端_7_q ));
  and and_17 (and_17_out, decoder_1_out7, \d触发器_带使能端_8_q );
  \D触发器_带使能端  \d触发器_带使能端_8  (.EN(and_9_out), .RESET(RESET_2), .clk(clk_out), .D(D_7), .Q(\d触发器_带使能端_8_q ));
  or or_1 (or_2_out[1], and_17_out, and_16_out, and_15_out, and_14_out, and_13_out, and_12_out, and_11_out, and_10_out);
  Decoder #(.select(2), .enable("false")) decoder_2 (
    .out0(decoder_2_out0), .out1(decoder_2_out1), .out2(decoder_2_out2), .out3(decoder_2_out3), .sel(or_5_out));
  Decoder #(.select(2), .enable("false")) decoder_3 (
    .out0(decoder_3_out0), .out2(decoder_3_out2), .out3(decoder_3_out3), .sel(or_2_out));  // open: out1
  \D触发器_带使能端  \d触发器_带使能端_9  (.EN(and_2_out), .RESET(RESET_2), .clk(clk_out), .D(D_6), .Q(\d触发器_带使能端_9_q ));
  \D触发器_带使能端  \d触发器_带使能端_10  (.EN(and_3_out), .RESET(RESET_2), .clk(clk_out), .D(D_6), .Q(\d触发器_带使能端_10_q ));
  \D触发器_带使能端  \d触发器_带使能端_11  (.EN(and_4_out), .RESET(RESET_2), .clk(clk_out), .D(D_6), .Q(\d触发器_带使能端_11_q ));
  \D触发器_带使能端  \d触发器_带使能端_12  (.EN(and_5_out), .RESET(RESET_2), .clk(clk_out), .D(D_6), .Q(\d触发器_带使能端_12_q ));
  \D触发器_带使能端  \d触发器_带使能端_13  (.EN(and_6_out), .RESET(RESET_2), .clk(clk_out), .D(D_6), .Q(\d触发器_带使能端_13_q ));
  \D触发器_带使能端  \d触发器_带使能端_14  (.EN(and_7_out), .RESET(RESET_2), .clk(clk_out), .D(D_6), .Q(\d触发器_带使能端_14_q ));
  \D触发器_带使能端  \d触发器_带使能端_15  (.EN(and_8_out), .RESET(RESET_2), .clk(clk_out), .D(D_6), .Q(\d触发器_带使能端_15_q ));
  \D触发器_带使能端  \d触发器_带使能端_16  (.EN(and_9_out), .RESET(RESET_2), .clk(clk_out), .D(D_6), .Q(\d触发器_带使能端_16_q ));
  Hex_Digit_Display hex_digit_display_4 (.value(multiplexer_5_out));  // open: dp
  and and_18 (and_18_out, decoder_1_out0, \d触发器_带使能端_9_q );
  and and_19 (and_19_out, decoder_1_out1, \d触发器_带使能端_10_q );
  and and_20 (and_20_out, decoder_1_out2, \d触发器_带使能端_11_q );
  and and_21 (and_21_out, decoder_1_out3, \d触发器_带使能端_12_q );
  and and_22 (and_22_out, decoder_1_out4, \d触发器_带使能端_13_q );
  and and_23 (and_23_out, decoder_1_out5, \d触发器_带使能端_14_q );
  and and_24 (and_24_out, decoder_1_out6, \d触发器_带使能端_15_q );
  and and_25 (and_25_out, decoder_1_out7, \d触发器_带使能端_16_q );
  or or_2 (or_2_out[0], and_25_out, and_24_out, and_23_out, and_22_out, and_21_out, and_20_out, and_19_out, and_18_out);
  Multiplexer #(.width(8)) multiplexer_5 (
    .in0({4'b0000, and_56_out}), .in1(adder_7_out), .out({multiplexer_5_out_2, multiplexer_5_out}),
    .sel(decoder_3_out0), .en(or_3_out));
  Register register_2 (
    .D({multiplexer_5_out_2, multiplexer_5_out}), .en(decoder_2_out0), .Q(register_2_q), .clk(clk_out),
    .clr(RESET_3));
  Register register_3 (
    .D({multiplexer_5_out_2, multiplexer_5_out}), .en(decoder_2_out1), .Q(register_3_q), .clk(clk_out),
    .clr(RESET_3));
  Register register_4 (
    .D({multiplexer_5_out_2, multiplexer_5_out}), .en(decoder_2_out2), .Q(register_4_q), .clk(clk_out),
    .clr(RESET_3));
  Register register_5 (
    .D({multiplexer_5_out_2, multiplexer_5_out}), .en(decoder_2_out3), .Q(register_5_q), .clk(clk_out),
    .clr(RESET_3));
  or or_3 (or_3_out, decoder_3_out0, decoder_3_out2);
  \D触发器_带使能端  \d触发器_带使能端_17  (.EN(and_2_out), .RESET(RESET_2), .clk(clk_out), .D(D_5), .Q(\d触发器_带使能端_17_q ));
  \D触发器_带使能端  \d触发器_带使能端_18  (.EN(and_3_out), .RESET(RESET_2), .clk(clk_out), .D(D_5), .Q(\d触发器_带使能端_18_q ));
  \D触发器_带使能端  \d触发器_带使能端_19  (.EN(and_4_out), .RESET(RESET_2), .clk(clk_out), .D(D_5), .Q(\d触发器_带使能端_19_q ));
  \D触发器_带使能端  \d触发器_带使能端_20  (.EN(and_5_out), .RESET(RESET_2), .clk(clk_out), .D(D_5), .Q(\d触发器_带使能端_20_q ));
  \D触发器_带使能端  \d触发器_带使能端_21  (.EN(and_6_out), .RESET(RESET_2), .clk(clk_out), .D(D_5), .Q(\d触发器_带使能端_21_q ));
  \D触发器_带使能端  \d触发器_带使能端_22  (.EN(and_7_out), .RESET(RESET_2), .clk(clk_out), .D(D_5), .Q(\d触发器_带使能端_22_q ));
  \D触发器_带使能端  \d触发器_带使能端_23  (.EN(and_8_out), .RESET(RESET_2), .clk(clk_out), .D(D_5), .Q(\d触发器_带使能端_23_q ));
  \D触发器_带使能端  \d触发器_带使能端_24  (.EN(and_9_out), .RESET(RESET_2), .clk(clk_out), .D(D_5), .Q(\d触发器_带使能端_24_q ));
  Hex_Digit_Display hex_digit_display_5 (.value(register_3_q[3:0]));  // open: dp
  Multiplexer #(.select(2), .width(8), .enable("false")) multiplexer_6 (
    .in0(register_2_q), .in1(register_3_q), .in2(register_4_q), .in3(register_5_q), .out(multiplexer_6_out),
    .sel(and_86_out));
  and and_26 (and_26_out, decoder_1_out0, \d触发器_带使能端_17_q );
  and and_27 (and_27_out, decoder_1_out1, \d触发器_带使能端_18_q );
  and and_28 (and_28_out, decoder_1_out2, \d触发器_带使能端_19_q );
  and and_29 (and_29_out, decoder_1_out3, \d触发器_带使能端_20_q );
  and and_30 (and_30_out, decoder_1_out4, \d触发器_带使能端_21_q );
  and and_31 (and_31_out, decoder_1_out5, \d触发器_带使能端_22_q );
  and and_32 (and_32_out, decoder_1_out6, \d触发器_带使能端_23_q );
  and and_33 (and_33_out, decoder_1_out7, \d触发器_带使能端_24_q );
  or or_4 (or_5_out[1], and_33_out, and_32_out, and_31_out, and_30_out, and_29_out, and_28_out, and_27_out, and_26_out);
  Multiplexer #(.select(2), .width(8)) multiplexer_7 (
    .in0(register_2_q), .in1(register_3_q), .in2(register_4_q), .in3(register_5_q), .out(multiplexer_7_out),
    .sel(and_65_out), .en(decoder_3_out0));
  Multiplexer #(.select(2), .width(8)) multiplexer_8 (
    .in0(register_2_q), .in1(register_3_q), .in2(register_4_q), .in3(register_5_q), .out(multiplexer_8_out),
    .sel(and_83_out), .en(decoder_3_out0));
  Comparator comparator_1 (.a(register_2_q), .b(multiplexer_6_out), .eq(comparator_1_eq));  // open: gt, lt
  Adder adder_7 (.a(multiplexer_7_out), .b(multiplexer_8_out), .out(adder_7_out));  // open: cin, cout
  Hex_Digit_Display hex_digit_display_6 (.value(register_3_q[3:0]));  // open: dp
  \D触发器_带使能端  \d触发器_带使能端_25  (.EN(and_2_out), .RESET(RESET_2), .clk(clk_out), .D(D_4), .Q(\d触发器_带使能端_25_q ));
  \D触发器_带使能端  \d触发器_带使能端_26  (.EN(and_3_out), .RESET(RESET_2), .clk(clk_out), .D(D_4), .Q(\d触发器_带使能端_26_q ));
  \D触发器_带使能端  \d触发器_带使能端_27  (.EN(and_4_out), .RESET(RESET_2), .clk(clk_out), .D(D_4), .Q(\d触发器_带使能端_27_q ));
  \D触发器_带使能端  \d触发器_带使能端_28  (.EN(and_5_out), .RESET(RESET_2), .clk(clk_out), .D(D_4), .Q(\d触发器_带使能端_28_q ));
  \D触发器_带使能端  \d触发器_带使能端_29  (.EN(and_6_out), .RESET(RESET_2), .clk(clk_out), .D(D_4), .Q(\d触发器_带使能端_29_q ));
  \D触发器_带使能端  \d触发器_带使能端_30  (.EN(and_7_out), .RESET(RESET_2), .clk(clk_out), .D(D_4), .Q(\d触发器_带使能端_30_q ));
  \D触发器_带使能端  \d触发器_带使能端_31  (.EN(and_8_out), .RESET(RESET_2), .clk(clk_out), .D(D_4), .Q(\d触发器_带使能端_31_q ));
  \D触发器_带使能端  \d触发器_带使能端_32  (.EN(and_9_out), .RESET(RESET_2), .clk(clk_out), .D(D_4), .Q(\d触发器_带使能端_32_q ));
  Hex_Digit_Display hex_digit_display_7 (.value(register_5_q[3:0]));  // open: dp
  and and_34 (and_34_out, decoder_1_out0, \d触发器_带使能端_25_q );
  and and_35 (and_35_out, decoder_1_out1, \d触发器_带使能端_26_q );
  and and_36 (and_36_out, decoder_1_out2, \d触发器_带使能端_27_q );
  and and_37 (and_37_out, decoder_1_out3, \d触发器_带使能端_28_q );
  and and_38 (and_38_out, decoder_1_out4, \d触发器_带使能端_29_q );
  and and_39 (and_39_out, decoder_1_out5, \d触发器_带使能端_30_q );
  and and_40 (and_40_out, decoder_1_out6, \d触发器_带使能端_31_q );
  and and_41 (and_41_out, decoder_1_out7, \d触发器_带使能端_32_q );
  or or_5 (or_5_out[0], and_41_out, and_40_out, and_39_out, and_38_out, and_37_out, and_36_out, and_35_out, and_34_out);
  Hex_Digit_Display hex_digit_display_8 (.value(multiplexer_7_out[3:0]));  // open: dp
  Hex_Digit_Display hex_digit_display_9 (.value(multiplexer_8_out[3:0]));  // open: dp
  and and_42 (and_44_out[2], decoder_3_out3, or_5_out[0]);
  and and_43 (and_44_out[1], decoder_3_out3, or_6_out);
  \D触发器_带使能端  \d触发器_带使能端_33  (.EN(and_2_out), .RESET(RESET_2), .clk(clk_out), .D(D_3), .Q(\d触发器_带使能端_33_q ));
  \D触发器_带使能端  \d触发器_带使能端_34  (.EN(and_3_out), .RESET(RESET_2), .clk(clk_out), .D(D_3), .Q(\d触发器_带使能端_34_q ));
  \D触发器_带使能端  \d触发器_带使能端_35  (.EN(and_4_out), .RESET(RESET_2), .clk(clk_out), .D(D_3), .Q(\d触发器_带使能端_35_q ));
  \D触发器_带使能端  \d触发器_带使能端_36  (.EN(and_5_out), .RESET(RESET_2), .clk(clk_out), .D(D_3), .Q(\d触发器_带使能端_36_q ));
  \D触发器_带使能端  \d触发器_带使能端_37  (.EN(and_6_out), .RESET(RESET_2), .clk(clk_out), .D(D_3), .Q(\d触发器_带使能端_37_q ));
  \D触发器_带使能端  \d触发器_带使能端_38  (.EN(and_7_out), .RESET(RESET_2), .clk(clk_out), .D(D_3), .Q(\d触发器_带使能端_38_q ));
  \D触发器_带使能端  \d触发器_带使能端_39  (.EN(and_8_out), .RESET(RESET_2), .clk(clk_out), .D(D_3), .Q(\d触发器_带使能端_39_q ));
  \D触发器_带使能端  \d触发器_带使能端_40  (.EN(and_9_out), .RESET(RESET_2), .clk(clk_out), .D(D_3), .Q(\d触发器_带使能端_40_q ));
  and and_44 (and_44_out[0], decoder_3_out3, or_7_out);
  and and_45 (and_45_out, decoder_1_out0, \d触发器_带使能端_33_q );
  and and_46 (and_46_out, decoder_1_out1, \d触发器_带使能端_34_q );
  and and_47 (and_47_out, decoder_1_out2, \d触发器_带使能端_35_q );
  and and_48 (and_48_out, decoder_1_out3, \d触发器_带使能端_36_q );
  and and_49 (and_49_out, decoder_1_out4, \d触发器_带使能端_37_q );
  and and_50 (and_50_out, decoder_1_out5, \d触发器_带使能端_38_q );
  and and_51 (and_51_out, decoder_1_out6, \d触发器_带使能端_39_q );
  and and_52 (and_52_out, decoder_1_out7, \d触发器_带使能端_40_q );
  and and_53 (and_56_out[3], decoder_3_out2, or_6_out);
  and and_54 (and_56_out[2], decoder_3_out2, or_7_out);
  or or_6 (or_6_out, and_52_out, and_51_out, and_50_out, and_49_out, and_48_out, and_47_out, and_46_out, and_45_out);
  and and_55 (and_56_out[1], decoder_3_out2, or_8_out);
  and and_56 (and_56_out[0], decoder_3_out2, or_9_out);
  \D触发器_带使能端  \d触发器_带使能端_41  (.EN(and_2_out), .RESET(RESET_2), .clk(clk_out), .D(D_2), .Q(\d触发器_带使能端_41_q ));
  \D触发器_带使能端  \d触发器_带使能端_42  (.EN(and_3_out), .RESET(RESET_2), .clk(clk_out), .D(D_2), .Q(\d触发器_带使能端_42_q ));
  \D触发器_带使能端  \d触发器_带使能端_43  (.EN(and_4_out), .RESET(RESET_2), .clk(clk_out), .D(D_2), .Q(\d触发器_带使能端_43_q ));
  \D触发器_带使能端  \d触发器_带使能端_44  (.EN(and_5_out), .RESET(RESET_2), .clk(clk_out), .D(D_2), .Q(\d触发器_带使能端_44_q ));
  \D触发器_带使能端  \d触发器_带使能端_45  (.EN(and_6_out), .RESET(RESET_2), .clk(clk_out), .D(D_2), .Q(\d触发器_带使能端_45_q ));
  \D触发器_带使能端  \d触发器_带使能端_46  (.EN(and_7_out), .RESET(RESET_2), .clk(clk_out), .D(D_2), .Q(\d触发器_带使能端_46_q ));
  \D触发器_带使能端  \d触发器_带使能端_47  (.EN(and_8_out), .RESET(RESET_2), .clk(clk_out), .D(D_2), .Q(\d触发器_带使能端_47_q ));
  \D触发器_带使能端  \d触发器_带使能端_48  (.EN(decoder_1_out7), .RESET(RESET_2), .clk(clk_out), .D(D_2), .Q(\d触发器_带使能端_48_q ));
  and and_57 (and_57_out, decoder_1_out0, \d触发器_带使能端_41_q );
  and and_58 (and_58_out, decoder_1_out1, \d触发器_带使能端_42_q );
  and and_59 (and_59_out, decoder_1_out2, \d触发器_带使能端_43_q );
  and and_60 (and_60_out, decoder_1_out3, \d触发器_带使能端_44_q );
  and and_61 (and_61_out, decoder_1_out4, \d触发器_带使能端_45_q );
  and and_62 (and_62_out, decoder_1_out5, \d触发器_带使能端_46_q );
  and and_63 (and_63_out, decoder_1_out6, \d触发器_带使能端_47_q );
  and and_64 (and_64_out, decoder_1_out7, \d触发器_带使能端_48_q );
  and and_65 (and_65_out[0], decoder_3_out0, or_7_out);
  and and_66 (and_65_out[1], decoder_3_out0, or_6_out);
  or or_7 (or_7_out, and_64_out, and_63_out, and_62_out, and_61_out, and_60_out, and_59_out, and_58_out, and_57_out);
  \D触发器_带使能端  \d触发器_带使能端_49  (.EN(and_2_out), .RESET(RESET_2), .clk(clk_out), .D(D_1), .Q(\d触发器_带使能端_49_q ));
  \D触发器_带使能端  \d触发器_带使能端_50  (.EN(and_3_out), .RESET(RESET_2), .clk(clk_out), .D(D_1), .Q(\d触发器_带使能端_50_q ));
  \D触发器_带使能端  \d触发器_带使能端_51  (.EN(and_4_out), .RESET(RESET_2), .clk(clk_out), .D(D_1), .Q(\d触发器_带使能端_51_q ));
  \D触发器_带使能端  \d触发器_带使能端_52  (.EN(and_5_out), .RESET(RESET_2), .clk(clk_out), .D(D_1), .Q(\d触发器_带使能端_52_q ));
  \D触发器_带使能端  \d触发器_带使能端_53  (.EN(and_6_out), .RESET(RESET_2), .clk(clk_out), .D(D_1), .Q(\d触发器_带使能端_53_q ));
  \D触发器_带使能端  \d触发器_带使能端_54  (.EN(and_7_out), .RESET(RESET_2), .clk(clk_out), .D(D_1), .Q(\d触发器_带使能端_54_q ));
  \D触发器_带使能端  \d触发器_带使能端_55  (.EN(and_8_out), .RESET(RESET_2), .clk(clk_out), .D(D_1), .Q(\d触发器_带使能端_55_q ));
  \D触发器_带使能端  \d触发器_带使能端_56  (.EN(and_9_out), .RESET(RESET_2), .clk(clk_out), .D(D_1), .Q(\d触发器_带使能端_56_q ));
  and and_67 (and_67_out, decoder_1_out0, \d触发器_带使能端_49_q );
  and and_68 (and_68_out, decoder_1_out1, \d触发器_带使能端_50_q );
  and and_69 (and_69_out, decoder_1_out2, \d触发器_带使能端_51_q );
  and and_70 (and_70_out, decoder_1_out3, \d触发器_带使能端_52_q );
  and and_71 (and_71_out, decoder_1_out4, \d触发器_带使能端_53_q );
  and and_72 (and_72_out, decoder_1_out5, \d触发器_带使能端_54_q );
  and and_73 (and_73_out, decoder_1_out6, \d触发器_带使能端_55_q );
  and and_74 (and_74_out, decoder_1_out7, \d触发器_带使能端_56_q );
  or or_8 (or_8_out, and_74_out, and_73_out, and_72_out, and_71_out, and_70_out, and_69_out, and_68_out, and_67_out);
  and and_75 (and_75_out, decoder_1_out0, \d触发器_带使能端_57_q );
  \D触发器_带使能端  \d触发器_带使能端_57  (.EN(and_2_out), .RESET(RESET_2), .clk(clk_out), .D(D_0), .Q(\d触发器_带使能端_57_q ));
  and and_76 (and_76_out, decoder_1_out1, \d触发器_带使能端_58_q );
  \D触发器_带使能端  \d触发器_带使能端_58  (.EN(and_3_out), .RESET(RESET_2), .clk(clk_out), .D(D_0), .Q(\d触发器_带使能端_58_q ));
  and and_77 (and_77_out, decoder_1_out2, \d触发器_带使能端_59_q );
  \D触发器_带使能端  \d触发器_带使能端_59  (.EN(and_4_out), .RESET(RESET_2), .clk(clk_out), .D(D_0), .Q(\d触发器_带使能端_59_q ));
  and and_78 (and_78_out, decoder_1_out3, \d触发器_带使能端_60_q );
  \D触发器_带使能端  \d触发器_带使能端_60  (.EN(and_5_out), .RESET(RESET_2), .clk(clk_out), .D(D_0), .Q(\d触发器_带使能端_60_q ));
  and and_79 (and_79_out, decoder_1_out4, \d触发器_带使能端_61_q );
  \D触发器_带使能端  \d触发器_带使能端_61  (.EN(and_6_out), .RESET(RESET_2), .clk(clk_out), .D(D_0), .Q(\d触发器_带使能端_61_q ));
  and and_80 (and_80_out, decoder_1_out5, \d触发器_带使能端_62_q );
  \D触发器_带使能端  \d触发器_带使能端_62  (.EN(and_7_out), .RESET(RESET_2), .clk(clk_out), .D(D_0), .Q(\d触发器_带使能端_62_q ));
  and and_81 (and_81_out, decoder_1_out6, \d触发器_带使能端_63_q );
  \D触发器_带使能端  \d触发器_带使能端_63  (.EN(and_8_out), .RESET(RESET_2), .clk(clk_out), .D(D_0), .Q(\d触发器_带使能端_63_q ));
  and and_82 (and_82_out, decoder_1_out7, \d触发器_带使能端_64_q );
  \D触发器_带使能端  \d触发器_带使能端_64  (.EN(and_9_out), .RESET(RESET_2), .clk(clk_out), .D(D_0), .Q(\d触发器_带使能端_64_q ));
  and and_83 (and_83_out[0], decoder_3_out0, or_9_out);
  and and_84 (and_83_out[1], decoder_3_out0, or_8_out);
  and and_85 (and_86_out[1], decoder_3_out3, or_8_out);
  or or_9 (or_9_out, and_82_out, and_81_out, and_80_out, and_79_out, and_78_out, and_77_out, and_76_out, and_75_out);
  and and_86 (and_86_out[0], decoder_3_out3, or_9_out);

  // Notes on the sheet:
  //   数列求和
  //   1+2+...+10
  //   PC
endmodule

module \sCPU_奇数  (
  input  RESET,
  input  D_7,
  input  D_6,
  input  D_5,
  input  D_4,
  input  D_3,
  input  D_2,
  input  D_1,
  input  D_0,
  input  EN_CHANGE,
  input  RESET_2,
  input  EN,
  input  RESET_3
);

  wire adder_1_cout, adder_1_out, adder_2_cout, adder_2_out, adder_3_out, adder_4_cout, adder_4_out,
       adder_5_cout, adder_5_out, adder_6_out, and_1_out, and_2_out, and_3_out, and_4_out, and_5_out,
       and_6_out, and_7_out, and_8_out, and_9_out, and_10_out, and_11_out, and_12_out, and_13_out,
       and_14_out, and_15_out, and_16_out, and_17_out, and_18_out, and_19_out, and_20_out, and_21_out,
       and_22_out, and_23_out, and_24_out, and_25_out, and_26_out, and_27_out, and_28_out, and_29_out,
       and_30_out, and_31_out, and_32_out, and_33_out, and_34_out, and_35_out, and_36_out, and_37_out,
       and_38_out, and_39_out, and_40_out, and_41_out, and_45_out, and_46_out, and_47_out, and_48_out,
       and_49_out, and_50_out, and_51_out, and_52_out, and_57_out, and_58_out, and_59_out, and_60_out,
       and_61_out, and_62_out, and_63_out, and_64_out, and_67_out, and_68_out, and_69_out, and_70_out,
       and_71_out, and_72_out, and_73_out, and_74_out, and_75_out, and_76_out, and_77_out, and_78_out,
       and_79_out, and_80_out, and_81_out, and_82_out, clk_out, comparator_1_eq, decoder_1_out0,
       decoder_1_out1, decoder_1_out2, decoder_1_out3, decoder_1_out4, decoder_1_out5, decoder_1_out6,
       decoder_1_out7, decoder_2_out0, decoder_2_out2, decoder_2_out3, decoder_3_out0, decoder_3_out1,
       decoder_3_out2, decoder_3_out3, \d触发器_带使能端_1_q , \d触发器_带使能端_2_q , \d触发器_带使能端_3_q , \d触发器_带使能端_4_q ,
       \d触发器_带使能端_5_q , \d触发器_带使能端_6_q , \d触发器_带使能端_7_q , \d触发器_带使能端_8_q , \d触发器_带使能端_9_q , \d触发器_带使能端_10_q ,
       \d触发器_带使能端_11_q , \d触发器_带使能端_12_q , \d触发器_带使能端_13_q , \d触发器_带使能端_14_q , \d触发器_带使能端_15_q ,
       \d触发器_带使能端_16_q , \d触发器_带使能端_17_q , \d触发器_带使能端_18_q , \d触发器_带使能端_19_q , \d触发器_带使能端_20_q ,
       \d触发器_带使能端_21_q , \d触发器_带使能端_22_q , \d触发器_带使能端_23_q , \d触发器_带使能端_24_q , \d触发器_带使能端_25_q ,
       \d触发器_带使能端_26_q , \d触发器_带使能端_27_q , \d触发器_带使能端_28_q , \d触发器_带使能端_29_q , \d触发器_带使能端_30_q ,
       \d触发器_带使能端_31_q , \d触发器_带使能端_32_q , \d触发器_带使能端_33_q , \d触发器_带使能端_34_q , \d触发器_带使能端_35_q ,
       \d触发器_带使能端_36_q , \d触发器_带使能端_37_q , \d触发器_带使能端_38_q , \d触发器_带使能端_39_q , \d触发器_带使能端_40_q ,
       \d触发器_带使能端_41_q , \d触发器_带使能端_42_q , \d触发器_带使能端_43_q , \d触发器_带使能端_44_q , \d触发器_带使能端_45_q ,
       \d触发器_带使能端_46_q , \d触发器_带使能端_47_q , \d触发器_带使能端_48_q , \d触发器_带使能端_49_q , \d触发器_带使能端_50_q ,
       \d触发器_带使能端_51_q , \d触发器_带使能端_52_q , \d触发器_带使能端_53_q , \d触发器_带使能端_54_q , \d触发器_带使能端_55_q ,
       \d触发器_带使能端_56_q , \d触发器_带使能端_57_q , \d触发器_带使能端_58_q , \d触发器_带使能端_59_q , \d触发器_带使能端_60_q ,
       \d触发器_带使能端_61_q , \d触发器_带使能端_62_q , \d触发器_带使能端_63_q , \d触发器_带使能端_64_q , multiplexer_2_out,
       multiplexer_3_out, multiplexer_4_out, \n4位寄存器_1_q_0 , not_1_out, or_3_out, or_6_out, or_7_out,
       or_8_out, or_9_out;
  wire [1:0] and_66_out, and_83_out, and_86_out, or_2_out, or_5_out;
  wire [2:0] and_44_out, multiplexer_1_out, \n4位寄存器_1_q_3 , register_1_q;
  wire [3:0] and_56_out;
  wire [7:0] adder_7_out, multiplexer_5_out, multiplexer_6_out, multiplexer_7_out, multiplexer_8_out,
       register_2_q, register_3_q, register_4_q, register_5_q;

  Hex_Digit_Display hex_digit_display_1 (.value({1'b0, \n4位寄存器_1_q_3 }));  // open: dp
  Hex_Digit_Display hex_digit_display_2 (.value({1'b0, and_44_out}));  // open: dp
  and and_1 (and_1_out, decoder_2_out3, not_1_out);
  \_4位寄存器  \u_4位寄存器_1  (
    .EN(EN), .RESET(RESET), .clk(clk_out), .D_0(\n4位寄存器_1_q_0 ), .D_1(multiplexer_2_out),
    .D_2(multiplexer_3_out), .D_3(multiplexer_4_out), .Q_0(\n4位寄存器_1_q_0 ), .Q_1(\n4位寄存器_1_q_3 [2]),
    .Q_2(\n4位寄存器_1_q_3 [1]), .Q_3(\n4位寄存器_1_q_3 [0]));
  Multiplexer #(.width(3), .enable("false")) multiplexer_1 (
    .in0(\n4位寄存器_1_q_3 ), .in1(and_44_out), .out(multiplexer_1_out), .sel(and_1_out));
  Multiplexer #(.enable("false")) multiplexer_2 (
    .in0(adder_3_out), .in1(adder_6_out), .out(multiplexer_2_out), .sel(and_1_out));
  Multiplexer #(.enable("false")) multiplexer_3 (
    .in0(adder_2_out), .in1(adder_5_out), .out(multiplexer_3_out), .sel(and_1_out));
  Multiplexer #(.enable("false")) multiplexer_4 (
    .in0(adder_1_out), .in1(adder_4_out), .out(multiplexer_4_out), .sel(and_1_out));
  Clock clk (.out(clk_out));
  Hex_Digit_Display hex_digit_display_3 (.value({1'b0, register_1_q}));  // open: dp
  not not_1 (not_1_out, comparator_1_eq);
  Adder #(.width(1)) adder_1 (.a(\n4位寄存器_1_q_3 [0]), .b(1'b1), .out(adder_1_out), .cin(1'b0), .cout(adder_1_cout));
  Adder #(.width(1)) adder_2 (
    .a(\n4位寄存器_1_q_3 [1]), .b(1'b0), .out(adder_2_out), .cin(adder_1_cout), .cout(adder_2_cout));
  Adder #(.width(1)) adder_3 (.a(\n4位寄存器_1_q_3 [2]), .b(1'b0), .out(adder_3_out), .cin(adder_2_cout));  // open: cout
  Decoder #(.select(3), .enable("false")) decoder_1 (
    .out0(decoder_1_out0), .out1(decoder_1_out1), .out2(decoder_1_out2), .out3(decoder_1_out3),
    .out4(decoder_1_out4), .out5(decoder_1_out5), .out6(decoder_1_out6), .out7(decoder_1_out7),
    .sel(register_1_q));
  Register #(.width(3)) register_1 (.D(multiplexer_1_out), .en(EN), .Q(register_1_q), .clk(clk_out), .clr(RESET));
  Adder #(.width(1)) adder_4 (.a(multiplexer_1_out[0]), .b(1'b1), .out(adder_4_out), .cin(1'b0), .cout(adder_4_cout));
  Adder #(.width(1)) adder_5 (
    .a(multiplexer_1_out[1]), .b(1'b0), .out(adder_5_out), .cin(adder_4_cout), .cout(adder_5_cout));
  Adder #(.width(1)) adder_6 (.a(multiplexer_1_out[2]), .b(1'b0), .out(adder_6_out), .cin(adder_5_cout));  // open: cout
  and and_2 (and_2_out, decoder_1_out0, EN_CHANGE);
  and and_3 (and_3_out, decoder_1_out1, EN_CHANGE);
  and and_4 (and_4_out, decoder_1_out2, EN_CHANGE);
  and and_5 (and_5_out, decoder_1_out3, EN_CHANGE);
  and and_6 (and_6_out, decoder_1_out4, EN_CHANGE);
  and and_7 (and_7_out, decoder_1_out5, EN_CHANGE);
  and and_8 (and_8_out, decoder_1_out6, EN_CHANGE);
  and and_9 (and_9_out, decoder_1_out7, EN_CHANGE);
  \D触发器_带使能端  \d触发器_带使能端_1  (.EN(and_2_out), .RESET(RESET_2), .clk(clk_out), .D(D_7), .Q(\d触发器_带使能端_1_q ));
  \D触发器_带使能端  \d触发器_带使能端_2  (.EN(and_3_out), .RESET(RESET_2), .clk(clk_out), .D(D_7), .Q(\d触发器_带使能端_2_q ));
  \D触发器_带使能端  \d触发器_带使能端_3  (.EN(and_4_out), .RESET(RESET_2), .clk(clk_out), .D(D_7), .Q(\d触发器_带使能端_3_q ));
  \D触发器_带使能端  \d触发器_带使能端_4  (.EN(and_5_out), .RESET(RESET_2), .clk(clk_out), .D(D_7), .Q(\d触发器_带使能端_4_q ));
  \D触发器_带使能端  \d触发器_带使能端_5  (.EN(and_6_out), .RESET(RESET_2), .clk(clk_out), .D(D_7), .Q(\d触发器_带使能端_5_q ));
  \D触发器_带使能端  \d触发器_带使能端_6  (.EN(and_7_out), .RESET(RESET_2), .clk(clk_out), .D(D_7), .Q(\d触发器_带使能端_6_q ));
  \D触发器_带使能端  \d触发器_带使能端_7  (.EN(and_8_out), .RESET(RESET_2), .clk(clk_out), .D(D_7), .Q(\d触发器_带使能端_7_q ));
  \D触发器_带使能端  \d触发器_带使能端_8  (.EN(and_9_out), .RESET(RESET_2), .clk(clk_out), .D(D_7), .Q(\d触发器_带使能端_8_q ));
  and and_10 (and_10_out, decoder_1_out0, \d触发器_带使能端_1_q );
  and and_11 (and_11_out, decoder_1_out1, \d触发器_带使能端_2_q );
  and and_12 (and_12_out, decoder_1_out2, \d触发器_带使能端_3_q );
  and and_13 (and_13_out, decoder_1_out3, \d触发器_带使能端_4_q );
  and and_14 (and_14_out, decoder_1_out4, \d触发器_带使能端_5_q );
  and and_15 (and_15_out, decoder_1_out5, \d触发器_带使能端_6_q );
  and and_16 (and_16_out, decoder_1_out6, \d触发器_带使能端_7_q );
  and and_17 (and_17_out, decoder_1_out7, \d触发器_带使能端_8_q );
  or or_1 (or_2_out[1], and_17_out, and_16_out, and_15_out, and_14_out, and_13_out, and_12_out, and_11_out, and_10_out);
  Decoder #(.select(2), .enable("false")) decoder_2 (
    .out0(decoder_2_out0), .out2(decoder_2_out2), .out3(decoder_2_out3), .sel(or_2_out));  // open: out1
  \D触发器_带使能端  \d触发器_带使能端_9  (.EN(and_2_out), .RESET(RESET_2), .clk(clk_out), .D(D_6), .Q(\d触发器_带使能端_9_q ));
  \D触发器_带使能端  \d触发器_带使能端_10  (.EN(and_3_out), .RESET(RESET_2), .clk(clk_out), .D(D_6), .Q(\d触发器_带使能端_10_q ));
  \D触发器_带使能端  \d触发器_带使能端_11  (.EN(and_4_out), .RESET(RESET_2), .clk(clk_out), .D(D_6), .Q(\d触发器_带使能端_11_q ));
  \D触发器_带使能端  \d触发器_带使能端_12  (.EN(and_5_out), .RESET(RESET_2), .clk(clk_out), .D(D_6), .Q(\d触发器_带使能端_12_q ));
  \D触发器_带使能端  \d触发器_带使能端_13  (.EN(and_6_out), .RESET(RESET_2), .clk(clk_out), .D(D_6), .Q(\d触发器_带使能端_13_q ));
  \D触发器_带使能端  \d触发器_带使能端_14  (.EN(and_7_out), .RESET(RESET_2), .clk(clk_out), .D(D_6), .Q(\d触发器_带使能端_14_q ));
  \D触发器_带使能端  \d触发器_带使能端_15  (.EN(and_8_out), .RESET(RESET_2), .clk(clk_out), .D(D_6), .Q(\d触发器_带使能端_15_q ));
  \D触发器_带使能端  \d触发器_带使能端_16  (.EN(and_9_out), .RESET(RESET_2), .clk(clk_out), .D(D_6), .Q(\d触发器_带使能端_16_q ));
  Decoder #(.select(2), .enable("false")) decoder_3 (
    .out0(decoder_3_out0), .out1(decoder_3_out1), .out2(decoder_3_out2), .out3(decoder_3_out3), .sel(or_5_out));
  Hex_Digit_Display hex_digit_display_4 (.value(multiplexer_5_out[3:0]));  // open: dp
  and and_18 (and_18_out, decoder_1_out0, \d触发器_带使能端_9_q );
  and and_19 (and_19_out, decoder_1_out1, \d触发器_带使能端_10_q );
  and and_20 (and_20_out, decoder_1_out2, \d触发器_带使能端_11_q );
  and and_21 (and_21_out, decoder_1_out3, \d触发器_带使能端_12_q );
  and and_22 (and_22_out, decoder_1_out4, \d触发器_带使能端_13_q );
  and and_23 (and_23_out, decoder_1_out5, \d触发器_带使能端_14_q );
  and and_24 (and_24_out, decoder_1_out6, \d触发器_带使能端_15_q );
  and and_25 (and_25_out, decoder_1_out7, \d触发器_带使能端_16_q );
  or or_2 (or_2_out[0], and_25_out, and_24_out, and_23_out, and_22_out, and_21_out, and_20_out, and_19_out, and_18_out);
  Multiplexer #(.width(8)) multiplexer_5 (
    .in0({4'b0000, and_56_out}), .in1(adder_7_out), .out(multiplexer_5_out), .sel(decoder_2_out0),
    .en(or_3_out));
  Register register_2 (.D(multiplexer_5_out), .en(decoder_3_out0), .Q(register_2_q), .clk(clk_out), .clr(RESET_3));
  Register register_3 (.D(multiplexer_5_out), .en(decoder_3_out1), .Q(register_3_q), .clk(clk_out), .clr(RESET_3));
  Register register_4 (.D(multiplexer_5_out), .en(decoder_3_out2), .Q(register_4_q), .clk(clk_out), .clr(RESET_3));
  Register register_5 (.D(multiplexer_5_out), .en(decoder_3_out3), .Q(register_5_q), .clk(clk_out), .clr(RESET_3));
  or or_3 (or_3_out, decoder_2_out0, decoder_2_out2);
  \D触发器_带使能端  \d触发器_带使能端_17  (.EN(and_2_out), .RESET(RESET_2), .clk(clk_out), .D(D_5), .Q(\d触发器_带使能端_17_q ));
  \D触发器_带使能端  \d触发器_带使能端_18  (.EN(and_3_out), .RESET(RESET_2), .clk(clk_out), .D(D_5), .Q(\d触发器_带使能端_18_q ));
  \D触发器_带使能端  \d触发器_带使能端_19  (.EN(and_4_out), .RESET(RESET_2), .clk(clk_out), .D(D_5), .Q(\d触发器_带使能端_19_q ));
  \D触发器_带使能端  \d触发器_带使能端_20  (.EN(and_5_out), .RESET(RESET_2), .clk(clk_out), .D(D_5), .Q(\d触发器_带使能端_20_q ));
  \D触发器_带使能端  \d触发器_带使能端_21  (.EN(and_6_out), .RESET(RESET_2), .clk(clk_out), .D(D_5), .Q(\d触发器_带使能端_21_q ));
  \D触发器_带使能端  \d触发器_带使能端_22  (.EN(and_7_out), .RESET(RESET_2), .clk(clk_out), .D(D_5), .Q(\d触发器_带使能端_22_q ));
  \D触发器_带使能端  \d触发器_带使能端_23  (.EN(and_8_out), .RESET(RESET_2), .clk(clk_out), .D(D_5), .Q(\d触发器_带使能端_23_q ));
  \D触发器_带使能端  \d触发器_带使能端_24  (.EN(and_9_out), .RESET(RESET_2), .clk(clk_out), .D(D_5), .Q(\d触发器_带使能端_24_q ));
  Hex_Digit_Display hex_digit_display_5 (.value(register_3_q[3:0]));  // open: dp
  Multiplexer #(.select(2), .width(8), .enable("false")) multiplexer_6 (
    .in0(register_2_q), .in1(register_3_q), .in2(register_4_q), .in3(register_5_q), .out(multiplexer_6_out),
    .sel(and_86_out));
  and and_26 (and_26_out, decoder_1_out0, \d触发器_带使能端_17_q );
  and and_27 (and_27_out, decoder_1_out1, \d触发器_带使能端_18_q );
  and and_28 (and_28_out, decoder_1_out2, \d触发器_带使能端_19_q );
  and and_29 (and_29_out, decoder_1_out3, \d触发器_带使能端_20_q );
  and and_30 (and_30_out, decoder_1_out4, \d触发器_带使能端_21_q );
  and and_31 (and_31_out, decoder_1_out5, \d触发器_带使能端_22_q );
  and and_32 (and_32_out, decoder_1_out6, \d触发器_带使能端_23_q );
  and and_33 (and_33_out, decoder_1_out7, \d触发器_带使能端_24_q );
  or or_4 (or_5_out[1], and_33_out, and_32_out, and_31_out, and_30_out, and_29_out, and_28_out, and_27_out, and_26_out);
  Multiplexer #(.select(2), .width(8)) multiplexer_7 (
    .in0(register_2_q), .in1(register_3_q), .in2(register_4_q), .in3(register_5_q), .out(multiplexer_7_out),
    .sel(and_66_out), .en(decoder_2_out0));
  Multiplexer #(.select(2), .width(8)) multiplexer_8 (
    .in0(register_2_q), .in1(register_3_q), .in2(register_4_q), .in3(register_5_q), .out(multiplexer_8_out),
    .sel(and_83_out), .en(decoder_2_out0));
  Adder adder_7 (.a(multiplexer_7_out), .b(multiplexer_8_out), .out(adder_7_out));  // open: cin, cout
  Hex_Digit_Display hex_digit_display_6 (.value(register_3_q[3:0]));  // open: dp
  \D触发器_带使能端  \d触发器_带使能端_25  (.EN(and_2_out), .RESET(RESET_2), .clk(clk_out), .D(D_4), .Q(\d触发器_带使能端_25_q ));
  \D触发器_带使能端  \d触发器_带使能端_26  (.EN(and_3_out), .RESET(RESET_2), .clk(clk_out), .D(D_4), .Q(\d触发器_带使能端_26_q ));
  \D触发器_带使能端  \d触发器_带使能端_27  (.EN(and_4_out), .RESET(RESET_2), .clk(clk_out), .D(D_4), .Q(\d触发器_带使能端_27_q ));
  \D触发器_带使能端  \d触发器_带使能端_28  (.EN(and_5_out), .RESET(RESET_2), .clk(clk_out), .D(D_4), .Q(\d触发器_带使能端_28_q ));
  \D触发器_带使能端  \d触发器_带使能端_29  (.EN(and_6_out), .RESET(RESET_2), .clk(clk_out), .D(D_4), .Q(\d触发器_带使能端_29_q ));
  \D触发器_带使能端  \d触发器_带使能端_30  (.EN(and_7_out), .RESET(RESET_2), .clk(clk_out), .D(D_4), .Q(\d触发器_带使能端_30_q ));
  \D触发器_带使能端  \d触发器_带使能端_31  (.EN(and_8_out), .RESET(RESET_2), .clk(clk_out), .D(D_4), .Q(\d触发器_带使能端_31_q ));
  \D触发器_带使能端  \d触发器_带使能端_32  (.EN(and_9_out), .RESET(RESET_2), .clk(clk_out), .D(D_4), .Q(\d触发器_带使能端_32_q ));
  Comparator comparator_1 (.a(register_2_q), .b(multiplexer_6_out), .eq(comparator_1_eq));  // open: gt, lt
  Hex_Digit_Display hex_digit_display_7 (.value(register_5_q[3:0]));  // open: dp
  and and_34 (and_34_out, decoder_1_out0, \d触发器_带使能端_25_q );
  and and_35 (and_35_out, decoder_1_out1, \d触发器_带使能端_26_q );
  and and_36 (and_36_out, decoder_1_out2, \d触发器_带使能端_27_q );
  and and_37 (and_37_out, decoder_1_out3, \d触发器_带使能端_28_q );
  and and_38 (and_38_out, decoder_1_out4, \d触发器_带使能端_29_q );
  and and_39 (and_39_out, decoder_1_out5, \d触发器_带使能端_30_q );
  and and_40 (and_40_out, decoder_1_out6, \d触发器_带使能端_31_q );
  and and_41 (and_41_out, decoder_1_out7, \d触发器_带使能端_32_q );
  Hex_Digit_Display hex_digit_display_8 (.value(multiplexer_7_out[3:0]));  // open: dp
  or or_5 (or_5_out[0], and_41_out, and_40_out, and_39_out, and_38_out, and_37_out, and_36_out, and_35_out, and_34_out);
  Hex_Digit_Display hex_digit_display_9 (.value(multiplexer_8_out[3:0]));  // open: dp
  and and_42 (and_44_out[2], decoder_2_out3, or_5_out[0]);
  and and_43 (and_44_out[1], decoder_2_out3, or_6_out);
  \D触发器_带使能端  \d触发器_带使能端_33  (.EN(and_2_out), .RESET(RESET_2), .clk(clk_out), .D(D_3), .Q(\d触发器_带使能端_33_q ));
  \D触发器_带使能端  \d触发器_带使能端_34  (.EN(and_3_out), .RESET(RESET_2), .clk(clk_out), .D(D_3), .Q(\d触发器_带使能端_34_q ));
  \D触发器_带使能端  \d触发器_带使能端_35  (.EN(and_4_out), .RESET(RESET_2), .clk(clk_out), .D(D_3), .Q(\d触发器_带使能端_35_q ));
  \D触发器_带使能端  \d触发器_带使能端_36  (.EN(and_5_out), .RESET(RESET_2), .clk(clk_out), .D(D_3), .Q(\d触发器_带使能端_36_q ));
  \D触发器_带使能端  \d触发器_带使能端_37  (.EN(and_6_out), .RESET(RESET_2), .clk(clk_out), .D(D_3), .Q(\d触发器_带使能端_37_q ));
  \D触发器_带使能端  \d触发器_带使能端_38  (.EN(and_7_out), .RESET(RESET_2), .clk(clk_out), .D(D_3), .Q(\d触发器_带使能端_38_q ));
  \D触发器_带使能端  \d触发器_带使能端_39  (.EN(and_8_out), .RESET(RESET_2), .clk(clk_out), .D(D_3), .Q(\d触发器_带使能端_39_q ));
  \D触发器_带使能端  \d触发器_带使能端_40  (.EN(and_9_out), .RESET(RESET_2), .clk(clk_out), .D(D_3), .Q(\d触发器_带使能端_40_q ));
  and and_44 (and_44_out[0], decoder_2_out3, or_7_out);
  and and_45 (and_45_out, decoder_1_out0, \d触发器_带使能端_33_q );
  and and_46 (and_46_out, decoder_1_out1, \d触发器_带使能端_34_q );
  and and_47 (and_47_out, decoder_1_out2, \d触发器_带使能端_35_q );
  and and_48 (and_48_out, decoder_1_out3, \d触发器_带使能端_36_q );
  and and_49 (and_49_out, decoder_1_out4, \d触发器_带使能端_37_q );
  and and_50 (and_50_out, decoder_1_out5, \d触发器_带使能端_38_q );
  and and_51 (and_51_out, decoder_1_out6, \d触发器_带使能端_39_q );
  and and_52 (and_52_out, decoder_1_out7, \d触发器_带使能端_40_q );
  and and_53 (and_56_out[3], decoder_2_out2, or_6_out);
  and and_54 (and_56_out[2], decoder_2_out2, or_7_out);
  or or_6 (or_6_out, and_52_out, and_51_out, and_50_out, and_49_out, and_48_out, and_47_out, and_46_out, and_45_out);
  and and_55 (and_56_out[1], decoder_2_out2, or_8_out);
  and and_56 (and_56_out[0], decoder_2_out2, or_9_out);
  \D触发器_带使能端  \d触发器_带使能端_41  (.EN(and_2_out), .RESET(RESET_2), .clk(clk_out), .D(D_2), .Q(\d触发器_带使能端_41_q ));
  \D触发器_带使能端  \d触发器_带使能端_42  (.EN(and_3_out), .RESET(RESET_2), .clk(clk_out), .D(D_2), .Q(\d触发器_带使能端_42_q ));
  \D触发器_带使能端  \d触发器_带使能端_43  (.EN(and_4_out), .RESET(RESET_2), .clk(clk_out), .D(D_2), .Q(\d触发器_带使能端_43_q ));
  \D触发器_带使能端  \d触发器_带使能端_44  (.EN(and_5_out), .RESET(RESET_2), .clk(clk_out), .D(D_2), .Q(\d触发器_带使能端_44_q ));
  \D触发器_带使能端  \d触发器_带使能端_45  (.EN(and_6_out), .RESET(RESET_2), .clk(clk_out), .D(D_2), .Q(\d触发器_带使能端_45_q ));
  \D触发器_带使能端  \d触发器_带使能端_46  (.EN(and_7_out), .RESET(RESET_2), .clk(clk_out), .D(D_2), .Q(\d触发器_带使能端_46_q ));
  \D触发器_带使能端  \d触发器_带使能端_47  (.EN(and_8_out), .RESET(RESET_2), .clk(clk_out), .D(D_2), .Q(\d触发器_带使能端_47_q ));
  \D触发器_带使能端  \d触发器_带使能端_48  (.EN(decoder_1_out7), .RESET(RESET_2), .clk(clk_out), .D(D_2), .Q(\d触发器_带使能端_48_q ));
  and and_57 (and_57_out, decoder_1_out0, \d触发器_带使能端_41_q );
  and and_58 (and_58_out, decoder_1_out1, \d触发器_带使能端_42_q );
  and and_59 (and_59_out, decoder_1_out2, \d触发器_带使能端_43_q );
  and and_60 (and_60_out, decoder_1_out3, \d触发器_带使能端_44_q );
  and and_61 (and_61_out, decoder_1_out4, \d触发器_带使能端_45_q );
  and and_62 (and_62_out, decoder_1_out5, \d触发器_带使能端_46_q );
  and and_63 (and_63_out, decoder_1_out6, \d触发器_带使能端_47_q );
  and and_64 (and_64_out, decoder_1_out7, \d触发器_带使能端_48_q );
  and and_65 (and_66_out[1], decoder_2_out0, or_6_out);
  or or_7 (or_7_out, and_64_out, and_63_out, and_62_out, and_61_out, and_60_out, and_59_out, and_58_out, and_57_out);
  and and_66 (and_66_out[0], decoder_2_out0, or_7_out);
  and and_67 (and_67_out, decoder_1_out0, \d触发器_带使能端_49_q );
  \D触发器_带使能端  \d触发器_带使能端_49  (.EN(and_2_out), .RESET(RESET_2), .clk(clk_out), .D(D_1), .Q(\d触发器_带使能端_49_q ));
  and and_68 (and_68_out, decoder_1_out1, \d触发器_带使能端_50_q );
  \D触发器_带使能端  \d触发器_带使能端_50  (.EN(and_3_out), .RESET(RESET_2), .clk(clk_out), .D(D_1), .Q(\d触发器_带使能端_50_q ));
  and and_69 (and_69_out, decoder_1_out2, \d触发器_带使能端_51_q );
  \D触发器_带使能端  \d触发器_带使能端_51  (.EN(and_4_out), .RESET(RESET_2), .clk(clk_out), .D(D_1), .Q(\d触发器_带使能端_51_q ));
  and and_70 (and_70_out, decoder_1_out3, \d触发器_带使能端_52_q );
  \D触发器_带使能端  \d触发器_带使能端_52  (.EN(and_5_out), .RESET(RESET_2), .clk(clk_out), .D(D_1), .Q(\d触发器_带使能端_52_q ));
  and and_71 (and_71_out, decoder_1_out4, \d触发器_带使能端_53_q );
  \D触发器_带使能端  \d触发器_带使能端_53  (.EN(and_6_out), .RESET(RESET_2), .clk(clk_out), .D(D_1), .Q(\d触发器_带使能端_53_q ));
  and and_72 (and_72_out, decoder_1_out5, \d触发器_带使能端_54_q );
  \D触发器_带使能端  \d触发器_带使能端_54  (.EN(and_7_out), .RESET(RESET_2), .clk(clk_out), .D(D_1), .Q(\d触发器_带使能端_54_q ));
  and and_73 (and_73_out, decoder_1_out6, \d触发器_带使能端_55_q );
  \D触发器_带使能端  \d触发器_带使能端_55  (.EN(and_8_out), .RESET(RESET_2), .clk(clk_out), .D(D_1), .Q(\d触发器_带使能端_55_q ));
  and and_74 (and_74_out, decoder_1_out7, \d触发器_带使能端_56_q );
  \D触发器_带使能端  \d触发器_带使能端_56  (.EN(and_9_out), .RESET(RESET_2), .clk(clk_out), .D(D_1), .Q(\d触发器_带使能端_56_q ));
  or or_8 (or_8_out, and_74_out, and_73_out, and_72_out, and_71_out, and_70_out, and_69_out, and_68_out, and_67_out);
  and and_75 (and_75_out, decoder_1_out0, \d触发器_带使能端_57_q );
  \D触发器_带使能端  \d触发器_带使能端_57  (.EN(and_2_out), .RESET(RESET_2), .clk(clk_out), .D(D_0), .Q(\d触发器_带使能端_57_q ));
  and and_76 (and_76_out, decoder_1_out1, \d触发器_带使能端_58_q );
  \D触发器_带使能端  \d触发器_带使能端_58  (.EN(and_3_out), .RESET(RESET_2), .clk(clk_out), .D(D_0), .Q(\d触发器_带使能端_58_q ));
  and and_77 (and_77_out, decoder_1_out2, \d触发器_带使能端_59_q );
  \D触发器_带使能端  \d触发器_带使能端_59  (.EN(and_4_out), .RESET(RESET_2), .clk(clk_out), .D(D_0), .Q(\d触发器_带使能端_59_q ));
  and and_78 (and_78_out, decoder_1_out3, \d触发器_带使能端_60_q );
  \D触发器_带使能端  \d触发器_带使能端_60  (.EN(and_5_out), .RESET(RESET_2), .clk(clk_out), .D(D_0), .Q(\d触发器_带使能端_60_q ));
  and and_79 (and_79_out, decoder_1_out4, \d触发器_带使能端_61_q );
  \D触发器_带使能端  \d触发器_带使能端_61  (.EN(and_6_out), .RESET(RESET_2), .clk(clk_out), .D(D_0), .Q(\d触发器_带使能端_61_q ));
  and and_80 (and_80_out, decoder_1_out5, \d触发器_带使能端_62_q );
  \D触发器_带使能端  \d触发器_带使能端_62  (.EN(and_7_out), .RESET(RESET_2), .clk(clk_out), .D(D_0), .Q(\d触发器_带使能端_62_q ));
  and and_81 (and_81_out, decoder_1_out6, \d触发器_带使能端_63_q );
  \D触发器_带使能端  \d触发器_带使能端_63  (.EN(and_8_out), .RESET(RESET_2), .clk(clk_out), .D(D_0), .Q(\d触发器_带使能端_63_q ));
  and and_82 (and_82_out, decoder_1_out7, \d触发器_带使能端_64_q );
  \D触发器_带使能端  \d触发器_带使能端_64  (.EN(and_9_out), .RESET(RESET_2), .clk(clk_out), .D(D_0), .Q(\d触发器_带使能端_64_q ));
  and and_83 (and_83_out[0], decoder_2_out0, or_9_out);
  and and_84 (and_83_out[1], decoder_2_out0, or_8_out);
  and and_85 (and_86_out[1], decoder_2_out3, or_8_out);
  or or_9 (or_9_out, and_82_out, and_81_out, and_80_out, and_79_out, and_78_out, and_77_out, and_76_out, and_75_out);
  and and_86 (and_86_out[0], decoder_2_out3, or_9_out);

  // Notes on the sheet:
  //   奇数数列求和
  //   1+3+5+7+9
  //   PC
endmodule

module \sCPU_out指令  (
  input  RESET,
  input  D_7,
  input  D_6,
  input  D_5,
  input  D_4,
  input  D_3,
  input  D_2,
  input  D_1,
  input  D_0,
  input  EN_CHANGE,
  input  RESET_2,
  input  EN,
  input  RESET_3,
  input  [7:0] in_14
);

  wire adder_1_cout, adder_1_out, adder_2_cout, adder_2_out, adder_3_out, adder_4_cout, adder_4_out,
       adder_5_cout, adder_5_out, adder_6_out, and_1_out, and_2_out, and_3_out, and_4_out, and_5_out,
       and_6_out, and_7_out, and_8_out, and_9_out, and_10_out, and_11_out, and_12_out, and_13_out,
       and_14_out, and_15_out, and_16_out, and_17_out, and_18_out, and_19_out, and_20_out, and_21_out,
       and_22_out, and_23_out, and_24_out, and_25_out, and_26_out, and_27_out, and_28_out, and_29_out,
       and_30_out, and_31_out, and_32_out, and_33_out, and_34_out, and_35_out, and_36_out, and_37_out,
       and_38_out, and_39_out, and_40_out, and_41_out, and_45_out, and_46_out, and_47_out, and_48_out,
       and_49_out, and_50_out, and_51_out, and_52_out, and_57_out, and_58_out, and_59_out, and_60_out,
       and_61_out, and_62_out, and_63_out, and_64_out, and_67_out, and_68_out, and_69_out, and_70_out,
       and_71_out, and_72_out, and_73_out, and_74_out, and_75_out, and_76_out, and_77_out, and_78_out,
       and_79_out, and_80_out, and_81_out, and_82_out, clk_out, comparator_1_eq, decoder_1_out0,
       decoder_1_out1, decoder_1_out2, decoder_1_out3, decoder_1_out4, decoder_1_out5, decoder_1_out6,
       decoder_1_out7, decoder_2_out0, decoder_2_out1, decoder_2_out2, decoder_2_out3, decoder_3_out0,
       decoder_3_out1, decoder_3_out2, decoder_3_out3, \d触发器_带使能端_1_q , \d触发器_带使能端_2_q , \d触发器_带使能端_3_q ,
       \d触发器_带使能端_4_q , \d触发器_带使能端_5_q , \d触发器_带使能端_6_q , \d触发器_带使能端_7_q , \d触发器_带使能端_8_q , \d触发器_带使能端_9_q ,
       \d触发器_带使能端_10_q , \d触发器_带使能端_11_q , \d触发器_带使能端_12_q , \d触发器_带使能端_13_q , \d触发器_带使能端_14_q ,
       \d触发器_带使能端_15_q , \d触发器_带使能端_16_q , \d触发器_带使能端_17_q , \d触发器_带使能端_18_q , \d触发器_带使能端_19_q ,
       \d触发器_带使能端_20_q , \d触发器_带使能端_21_q , \d触发器_带使能端_22_q , \d触发器_带使能端_23_q , \d触发器_带使能端_24_q ,
       \d触发器_带使能端_25_q , \d触发器_带使能端_26_q , \d触发器_带使能端_27_q , \d触发器_带使能端_28_q , \d触发器_带使能端_29_q ,
       \d触发器_带使能端_30_q , \d触发器_带使能端_31_q , \d触发器_带使能端_32_q , \d触发器_带使能端_33_q , \d触发器_带使能端_34_q ,
       \d触发器_带使能端_35_q , \d触发器_带使能端_36_q , \d触发器_带使能端_37_q , \d触发器_带使能端_38_q , \d触发器_带使能端_39_q ,
       \d触发器_带使能端_40_q , \d触发器_带使能端_41_q , \d触发器_带使能端_42_q , \d触发器_带使能端_43_q , \d触发器_带使能端_44_q ,
       \d触发器_带使能端_45_q , \d触发器_带使能端_46_q , \d触发器_带使能端_47_q , \d触发器_带使能端_48_q , \d触发器_带使能端_49_q ,
       \d触发器_带使能端_50_q , \d触发器_带使能端_51_q , \d触发器_带使能端_52_q , \d触发器_带使能端_53_q , \d触发器_带使能端_54_q ,
       \d触发器_带使能端_55_q , \d触发器_带使能端_56_q , \d触发器_带使能端_57_q , \d触发器_带使能端_58_q , \d触发器_带使能端_59_q ,
       \d触发器_带使能端_60_q , \d触发器_带使能端_61_q , \d触发器_带使能端_62_q , \d触发器_带使能端_63_q , \d触发器_带使能端_64_q ,
       multiplexer_2_out, multiplexer_3_out, multiplexer_4_out, \n4位寄存器_1_q_0 , not_1_out, or_3_out,
       or_6_out, or_7_out, or_8_out, or_9_out;
  wire [1:0] and_66_out, and_83_out, and_86_out, or_2_out, or_5_out;
  wire [2:0] and_44_out, multiplexer_1_out, \n4位寄存器_1_q_3 , register_1_q;
  wire [3:0] and_56_out;
  wire [7:0] adder_7_out, multiplexer_5_out, multiplexer_6_out, multiplexer_7_out, multiplexer_8_out,
       multiplexer_9_out, multiplexer_10_out, register_2_q, register_3_q, register_4_q, register_5_q;

  Hex_Digit_Display hex_digit_display_1 (.value({1'b0, \n4位寄存器_1_q_3 }));  // open: dp
  Hex_Digit_Display hex_digit_display_2 (.value({1'b0, and_44_out}));  // open: dp
  and and_1 (and_1_out, decoder_2_out3, not_1_out);
  \_4位寄存器  \u_4位寄存器_1  (
    .EN(EN), .RESET(RESET), .clk(clk_out), .D_0(\n4位寄存器_1_q_0 ), .D_1(multiplexer_2_out),
    .D_2(multiplexer_3_out), .D_3(multiplexer_4_out), .Q_0(\n4位寄存器_1_q_0 ), .Q_1(\n4位寄存器_1_q_3 [2]),
    .Q_2(\n4位寄存器_1_q_3 [1]), .Q_3(\n4位寄存器_1_q_3 [0]));
  Multiplexer #(.width(3), .enable("false")) multiplexer_1 (
    .in0(\n4位寄存器_1_q_3 ), .in1(and_44_out), .out(multiplexer_1_out), .sel(and_1_out));
  Multiplexer #(.enable("false")) multiplexer_2 (
    .in0(adder_3_out), .in1(adder_6_out), .out(multiplexer_2_out), .sel(and_1_out));
  Multiplexer #(.enable("false")) multiplexer_3 (
    .in0(adder_2_out), .in1(adder_5_out), .out(multiplexer_3_out), .sel(and_1_out));
  Multiplexer #(.enable("false")) multiplexer_4 (
    .in0(adder_1_out), .in1(adder_4_out), .out(multiplexer_4_out), .sel(and_1_out));
  Clock clk (.out(clk_out));
  Hex_Digit_Display hex_digit_display_3 (.value({1'b0, register_1_q}));  // open: dp
  not not_1 (not_1_out, comparator_1_eq);
  Adder #(.width(1)) adder_1 (.a(\n4位寄存器_1_q_3 [0]), .b(1'b1), .out(adder_1_out), .cin(1'b0), .cout(adder_1_cout));
  Adder #(.width(1)) adder_2 (
    .a(\n4位寄存器_1_q_3 [1]), .b(1'b0), .out(adder_2_out), .cin(adder_1_cout), .cout(adder_2_cout));
  Adder #(.width(1)) adder_3 (.a(\n4位寄存器_1_q_3 [2]), .b(1'b0), .out(adder_3_out), .cin(adder_2_cout));  // open: cout
  Decoder #(.select(3), .enable("false")) decoder_1 (
    .out0(decoder_1_out0), .out1(decoder_1_out1), .out2(decoder_1_out2), .out3(decoder_1_out3),
    .out4(decoder_1_out4), .out5(decoder_1_out5), .out6(decoder_1_out6), .out7(decoder_1_out7),
    .sel(register_1_q));
  Register #(.width(3)) register_1 (.D(multiplexer_1_out), .en(EN), .Q(register_1_q), .clk(clk_out), .clr(RESET));
  Adder #(.width(1)) adder_4 (.a(multiplexer_1_out[0]), .b(1'b1), .out(adder_4_out), .cin(1'b0), .cout(adder_4_cout));
  Adder #(.width(1)) adder_5 (
    .a(multiplexer_1_out[1]), .b(1'b0), .out(adder_5_out), .cin(adder_4_cout), .cout(adder_5_cout));
  Adder #(.width(1)) adder_6 (.a(multiplexer_1_out[2]), .b(1'b0), .out(adder_6_out), .cin(adder_5_cout));  // open: cout
  and and_2 (and_2_out, decoder_1_out0, EN_CHANGE);
  and and_3 (and_3_out, decoder_1_out1, EN_CHANGE);
  and and_4 (and_4_out, decoder_1_out2, EN_CHANGE);
  and and_5 (and_5_out, decoder_1_out3, EN_CHANGE);
  and and_6 (and_6_out, decoder_1_out4, EN_CHANGE);
  and and_7 (and_7_out, decoder_1_out5, EN_CHANGE);
  and and_8 (and_8_out, decoder_1_out6, EN_CHANGE);
  and and_9 (and_9_out, decoder_1_out7, EN_CHANGE);
  \D触发器_带使能端  \d触发器_带使能端_1  (.EN(and_2_out), .RESET(RESET_2), .clk(clk_out), .D(D_7), .Q(\d触发器_带使能端_1_q ));
  \D触发器_带使能端  \d触发器_带使能端_2  (.EN(and_3_out), .RESET(RESET_2), .clk(clk_out), .D(D_7), .Q(\d触发器_带使能端_2_q ));
  \D触发器_带使能端  \d触发器_带使能端_3  (.EN(and_4_out), .RESET(RESET_2), .clk(clk_out), .D(D_7), .Q(\d触发器_带使能端_3_q ));
  \D触发器_带使能端  \d触发器_带使能端_4  (.EN(and_5_out), .RESET(RESET_2), .clk(clk_out), .D(D_7), .Q(\d触发器_带使能端_4_q ));
  \D触发器_带使能端  \d触发器_带使能端_5  (.EN(and_6_out), .RESET(RESET_2), .clk(clk_out), .D(D_7), .Q(\d触发器_带使能端_5_q ));
  \D触发器_带使能端  \d触发器_带使能端_6  (.EN(and_7_out), .RESET(RESET_2), .clk(clk_out), .D(D_7), .Q(\d触发器_带使能端_6_q ));
  \D触发器_带使能端  \d触发器_带使能端_7  (.EN(and_8_out), .RESET(RESET_2), .clk(clk_out), .D(D_7), .Q(\d触发器_带使能端_7_q ));
  \D触发器_带使能端  \d触发器_带使能端_8  (.EN(and_9_out), .RESET(RESET_2), .clk(clk_out), .D(D_7), .Q(\d触发器_带使能端_8_q ));
  and and_10 (and_10_out, decoder_1_out0, \d触发器_带使能端_1_q );
  and and_11 (and_11_out, decoder_1_out1, \d触发器_带使能端_2_q );
  and and_12 (and_12_out, decoder_1_out2, \d触发器_带使能端_3_q );
  and and_13 (and_13_out, decoder_1_out3, \d触发器_带使能端_4_q );
  and and_14 (and_14_out, decoder_1_out4, \d触发器_带使能端_5_q );
  and and_15 (and_15_out, decoder_1_out5, \d触发器_带使能端_6_q );
  and and_16 (and_16_out, decoder_1_out6, \d触发器_带使能端_7_q );
  and and_17 (and_17_out, decoder_1_out7, \d触发器_带使能端_8_q );
  or or_1 (or_2_out[1], and_17_out, and_16_out, and_15_out, and_14_out, and_13_out, and_12_out, and_11_out, and_10_out);
  Decoder #(.select(2), .enable("false")) decoder_2 (
    .out0(decoder_2_out0), .out1(decoder_2_out1), .out2(decoder_2_out2), .out3(decoder_2_out3), .sel(or_2_out));
  \D触发器_带使能端  \d触发器_带使能端_9  (.EN(and_2_out), .RESET(RESET_2), .clk(clk_out), .D(D_6), .Q(\d触发器_带使能端_9_q ));
  \D触发器_带使能端  \d触发器_带使能端_10  (.EN(and_3_out), .RESET(RESET_2), .clk(clk_out), .D(D_6), .Q(\d触发器_带使能端_10_q ));
  \D触发器_带使能端  \d触发器_带使能端_11  (.EN(and_4_out), .RESET(RESET_2), .clk(clk_out), .D(D_6), .Q(\d触发器_带使能端_11_q ));
  \D触发器_带使能端  \d触发器_带使能端_12  (.EN(and_5_out), .RESET(RESET_2), .clk(clk_out), .D(D_6), .Q(\d触发器_带使能端_12_q ));
  \D触发器_带使能端  \d触发器_带使能端_13  (.EN(and_6_out), .RESET(RESET_2), .clk(clk_out), .D(D_6), .Q(\d触发器_带使能端_13_q ));
  \D触发器_带使能端  \d触发器_带使能端_14  (.EN(and_7_out), .RESET(RESET_2), .clk(clk_out), .D(D_6), .Q(\d触发器_带使能端_14_q ));
  \D触发器_带使能端  \d触发器_带使能端_15  (.EN(and_8_out), .RESET(RESET_2), .clk(clk_out), .D(D_6), .Q(\d触发器_带使能端_15_q ));
  \D触发器_带使能端  \d触发器_带使能端_16  (.EN(and_9_out), .RESET(RESET_2), .clk(clk_out), .D(D_6), .Q(\d触发器_带使能端_16_q ));
  Decoder #(.select(2), .enable("false")) decoder_3 (
    .out0(decoder_3_out0), .out1(decoder_3_out1), .out2(decoder_3_out2), .out3(decoder_3_out3), .sel(or_5_out));
  Hex_Digit_Display hex_digit_display_4 (.value(multiplexer_5_out[3:0]));  // open: dp
  and and_18 (and_18_out, decoder_1_out0, \d触发器_带使能端_9_q );
  and and_19 (and_19_out, decoder_1_out1, \d触发器_带使能端_10_q );
  and and_20 (and_20_out, decoder_1_out2, \d触发器_带使能端_11_q );
  and and_21 (and_21_out, decoder_1_out3, \d触发器_带使能端_12_q );
  and and_22 (and_22_out, decoder_1_out4, \d触发器_带使能端_13_q );
  and and_23 (and_23_out, decoder_1_out5, \d触发器_带使能端_14_q );
  and and_24 (and_24_out, decoder_1_out6, \d触发器_带使能端_15_q );
  and and_25 (and_25_out, decoder_1_out7, \d触发器_带使能端_16_q );
  or or_2 (or_2_out[0], and_25_out, and_24_out, and_23_out, and_22_out, and_21_out, and_20_out, and_19_out, and_18_out);
  Multiplexer #(.width(8)) multiplexer_5 (
    .in0({4'b0000, and_56_out}), .in1(adder_7_out), .out(multiplexer_5_out), .sel(decoder_2_out0),
    .en(or_3_out));
  Register register_2 (.D(multiplexer_5_out), .en(decoder_3_out0), .Q(register_2_q), .clk(clk_out), .clr(RESET_3));
  Register register_3 (.D(multiplexer_5_out), .en(decoder_3_out1), .Q(register_3_q), .clk(clk_out), .clr(RESET_3));
  Register register_4 (.D(multiplexer_5_out), .en(decoder_3_out2), .Q(register_4_q), .clk(clk_out), .clr(RESET_3));
  Register register_5 (.D(multiplexer_5_out), .en(decoder_3_out3), .Q(register_5_q), .clk(clk_out), .clr(RESET_3));
  or or_3 (or_3_out, decoder_2_out0, decoder_2_out2);
  \D触发器_带使能端  \d触发器_带使能端_17  (.EN(and_2_out), .RESET(RESET_2), .clk(clk_out), .D(D_5), .Q(\d触发器_带使能端_17_q ));
  \D触发器_带使能端  \d触发器_带使能端_18  (.EN(and_3_out), .RESET(RESET_2), .clk(clk_out), .D(D_5), .Q(\d触发器_带使能端_18_q ));
  \D触发器_带使能端  \d触发器_带使能端_19  (.EN(and_4_out), .RESET(RESET_2), .clk(clk_out), .D(D_5), .Q(\d触发器_带使能端_19_q ));
  \D触发器_带使能端  \d触发器_带使能端_20  (.EN(and_5_out), .RESET(RESET_2), .clk(clk_out), .D(D_5), .Q(\d触发器_带使能端_20_q ));
  \D触发器_带使能端  \d触发器_带使能端_21  (.EN(and_6_out), .RESET(RESET_2), .clk(clk_out), .D(D_5), .Q(\d触发器_带使能端_21_q ));
  \D触发器_带使能端  \d触发器_带使能端_22  (.EN(and_7_out), .RESET(RESET_2), .clk(clk_out), .D(D_5), .Q(\d触发器_带使能端_22_q ));
  \D触发器_带使能端  \d触发器_带使能端_23  (.EN(and_8_out), .RESET(RESET_2), .clk(clk_out), .D(D_5), .Q(\d触发器_带使能端_23_q ));
  \D触发器_带使能端  \d触发器_带使能端_24  (.EN(and_9_out), .RESET(RESET_2), .clk(clk_out), .D(D_5), .Q(\d触发器_带使能端_24_q ));
  Hex_Digit_Display hex_digit_display_5 (.value(register_3_q[3:0]));  // open: dp
  Multiplexer #(.select(2), .width(8), .enable("false")) multiplexer_6 (
    .in0(register_2_q), .in1(register_3_q), .in2(register_4_q), .in3(register_5_q), .out(multiplexer_6_out),
    .sel(and_86_out));
  and and_26 (and_26_out, decoder_1_out0, \d触发器_带使能端_17_q );
  and and_27 (and_27_out, decoder_1_out1, \d触发器_带使能端_18_q );
  and and_28 (and_28_out, decoder_1_out2, \d触发器_带使能端_19_q );
  and and_29 (and_29_out, decoder_1_out3, \d触发器_带使能端_20_q );
  and and_30 (and_30_out, decoder_1_out4, \d触发器_带使能端_21_q );
  and and_31 (and_31_out, decoder_1_out5, \d触发器_带使能端_22_q );
  and and_32 (and_32_out, decoder_1_out6, \d触发器_带使能端_23_q );
  and and_33 (and_33_out, decoder_1_out7, \d触发器_带使能端_24_q );
  or or_4 (or_5_out[1], and_33_out, and_32_out, and_31_out, and_30_out, and_29_out, and_28_out, and_27_out, and_26_out);
  Multiplexer #(.select(2), .width(8)) multiplexer_7 (
    .in0(register_2_q), .in1(register_3_q), .in2(register_4_q), .in3(register_5_q), .out(multiplexer_7_out),
    .sel(and_66_out), .en(decoder_2_out0));
  Multiplexer #(.select(2), .width(8)) multiplexer_8 (
    .in0(register_2_q), .in1(register_3_q), .in2(register_4_q), .in3(register_5_q), .out(multiplexer_8_out),
    .sel(and_83_out), .en(decoder_2_out0));
  Multiplexer #(.select(2), .width(8)) multiplexer_9 (
    .in0(register_2_q), .in1(register_3_q), .in2(register_4_q), .in3(register_5_q), .out(multiplexer_9_out),
    .sel(or_5_out), .en(decoder_2_out1));
  Adder adder_7 (.a(multiplexer_7_out), .b(multiplexer_8_out), .out(adder_7_out));  // open: cin, cout
  Hex_Digit_Display hex_digit_display_6 (.value(register_3_q[3:0]));  // open: dp
  Multiplexer #(.width(8)) multiplexer_10 (
    .in0(in_14), .in1(multiplexer_9_out), .out(multiplexer_10_out), .sel(decoder_2_out1), .en(decoder_2_out1));
  \D触发器_带使能端  \d触发器_带使能端_25  (.EN(and_2_out), .RESET(RESET_2), .clk(clk_out), .D(D_4), .Q(\d触发器_带使能端_25_q ));
  \D触发器_带使能端  \d触发器_带使能端_26  (.EN(and_3_out), .RESET(RESET_2), .clk(clk_out), .D(D_4), .Q(\d触发器_带使能端_26_q ));
  \D触发器_带使能端  \d触发器_带使能端_27  (.EN(and_4_out), .RESET(RESET_2), .clk(clk_out), .D(D_4), .Q(\d触发器_带使能端_27_q ));
  \D触发器_带使能端  \d触发器_带使能端_28  (.EN(and_5_out), .RESET(RESET_2), .clk(clk_out), .D(D_4), .Q(\d触发器_带使能端_28_q ));
  \D触发器_带使能端  \d触发器_带使能端_29  (.EN(and_6_out), .RESET(RESET_2), .clk(clk_out), .D(D_4), .Q(\d触发器_带使能端_29_q ));
  \D触发器_带使能端  \d触发器_带使能端_30  (.EN(and_7_out), .RESET(RESET_2), .clk(clk_out), .D(D_4), .Q(\d触发器_带使能端_30_q ));
  \D触发器_带使能端  \d触发器_带使能端_31  (.EN(and_8_out), .RESET(RESET_2), .clk(clk_out), .D(D_4), .Q(\d触发器_带使能端_31_q ));
  \D触发器_带使能端  \d触发器_带使能端_32  (.EN(and_9_out), .RESET(RESET_2), .clk(clk_out), .D(D_4), .Q(\d触发器_带使能端_32_q ));
  Comparator comparator_1 (.a(register_2_q), .b(multiplexer_6_out), .eq(comparator_1_eq));  // open: gt, lt
  Hex_Digit_Display hex_digit_display_7 (.value(register_5_q[3:0]));  // open: dp
  Hex_Digit_Display hex_digit_display_8 (.value(multiplexer_10_out[3:0]));  // open: dp
  and and_34 (and_34_out, decoder_1_out0, \d触发器_带使能端_25_q );
  and and_35 (and_35_out, decoder_1_out1, \d触发器_带使能端_26_q );
  and and_36 (and_36_out, decoder_1_out2, \d触发器_带使能端_27_q );
  and and_37 (and_37_out, decoder_1_out3, \d触发器_带使能端_28_q );
  and and_38 (and_38_out, decoder_1_out4, \d触发器_带使能端_29_q );
  and and_39 (and_39_out, decoder_1_out5, \d触发器_带使能端_30_q );
  and and_40 (and_40_out, decoder_1_out6, \d触发器_带使能端_31_q );
  and and_41 (and_41_out, decoder_1_out7, \d触发器_带使能端_32_q );
  Hex_Digit_Display hex_digit_display_9 (.value(multiplexer_7_out[3:0]));  // open: dp
  or or_5 (or_5_out[0], and_41_out, and_40_out, and_39_out, and_38_out, and_37_out, and_36_out, and_35_out, and_34_out);
  Hex_Digit_Display hex_digit_display_10 (.value(multiplexer_8_out[3:0]));  // open: dp
  and and_42 (and_44_out[2], decoder_2_out3, or_5_out[0]);
  and and_43 (and_44_out[1], decoder_2_out3, or_6_out);
  \D触发器_带使能端  \d触发器_带使能端_33  (.EN(and_2_out), .RESET(RESET_2), .clk(clk_out), .D(D_3), .Q(\d触发器_带使能端_33_q ));
  \D触发器_带使能端  \d触发器_带使能端_34  (.EN(and_3_out), .RESET(RESET_2), .clk(clk_out), .D(D_3), .Q(\d触发器_带使能端_34_q ));
  \D触发器_带使能端  \d触发器_带使能端_35  (.EN(and_4_out), .RESET(RESET_2), .clk(clk_out), .D(D_3), .Q(\d触发器_带使能端_35_q ));
  \D触发器_带使能端  \d触发器_带使能端_36  (.EN(and_5_out), .RESET(RESET_2), .clk(clk_out), .D(D_3), .Q(\d触发器_带使能端_36_q ));
  \D触发器_带使能端  \d触发器_带使能端_37  (.EN(and_6_out), .RESET(RESET_2), .clk(clk_out), .D(D_3), .Q(\d触发器_带使能端_37_q ));
  \D触发器_带使能端  \d触发器_带使能端_38  (.EN(and_7_out), .RESET(RESET_2), .clk(clk_out), .D(D_3), .Q(\d触发器_带使能端_38_q ));
  \D触发器_带使能端  \d触发器_带使能端_39  (.EN(and_8_out), .RESET(RESET_2), .clk(clk_out), .D(D_3), .Q(\d触发器_带使能端_39_q ));
  \D触发器_带使能端  \d触发器_带使能端_40  (.EN(and_9_out), .RESET(RESET_2), .clk(clk_out), .D(D_3), .Q(\d触发器_带使能端_40_q ));
  and and_44 (and_44_out[0], decoder_2_out3, or_7_out);
  and and_45 (and_45_out, decoder_1_out0, \d触发器_带使能端_33_q );
  and and_46 (and_46_out, decoder_1_out1, \d触发器_带使能端_34_q );
  and and_47 (and_47_out, decoder_1_out2, \d触发器_带使能端_35_q );
  and and_48 (and_48_out, decoder_1_out3, \d触发器_带使能端_36_q );
  and and_49 (and_49_out, decoder_1_out4, \d触发器_带使能端_37_q );
  and and_50 (and_50_out, decoder_1_out5, \d触发器_带使能端_38_q );
  and and_51 (and_51_out, decoder_1_out6, \d触发器_带使能端_39_q );
  and and_52 (and_52_out, decoder_1_out7, \d触发器_带使能端_40_q );
  and and_53 (and_56_out[3], decoder_2_out2, or_6_out);
  and and_54 (and_56_out[2], decoder_2_out2, or_7_out);
  or or_6 (or_6_out, and_52_out, and_51_out, and_50_out, and_49_out, and_48_out, and_47_out, and_46_out, and_45_out);
  and and_55 (and_56_out[1], decoder_2_out2, or_8_out);
  and and_56 (and_56_out[0], decoder_2_out2, or_9_out);
  \D触发器_带使能端  \d触发器_带使能端_41  (.EN(and_2_out), .RESET(RESET_2), .clk(clk_out), .D(D_2), .Q(\d触发器_带使能端_41_q ));
  \D触发器_带使能端  \d触发器_带使能端_42  (.EN(and_3_out), .RESET(RESET_2), .clk(clk_out), .D(D_2), .Q(\d触发器_带使能端_42_q ));
  \D触发器_带使能端  \d触发器_带使能端_43  (.EN(and_4_out), .RESET(RESET_2), .clk(clk_out), .D(D_2), .Q(\d触发器_带使能端_43_q ));
  \D触发器_带使能端  \d触发器_带使能端_44  (.EN(and_5_out), .RESET(RESET_2), .clk(clk_out), .D(D_2), .Q(\d触发器_带使能端_44_q ));
  \D触发器_带使能端  \d触发器_带使能端_45  (.EN(and_6_out), .RESET(RESET_2), .clk(clk_out), .D(D_2), .Q(\d触发器_带使能端_45_q ));
  \D触发器_带使能端  \d触发器_带使能端_46  (.EN(and_7_out), .RESET(RESET_2), .clk(clk_out), .D(D_2), .Q(\d触发器_带使能端_46_q ));
  \D触发器_带使能端  \d触发器_带使能端_47  (.EN(and_8_out), .RESET(RESET_2), .clk(clk_out), .D(D_2), .Q(\d触发器_带使能端_47_q ));
  \D触发器_带使能端  \d触发器_带使能端_48  (.EN(decoder_1_out7), .RESET(RESET_2), .clk(clk_out), .D(D_2), .Q(\d触发器_带使能端_48_q ));
  and and_57 (and_57_out, decoder_1_out0, \d触发器_带使能端_41_q );
  and and_58 (and_58_out, decoder_1_out1, \d触发器_带使能端_42_q );
  and and_59 (and_59_out, decoder_1_out2, \d触发器_带使能端_43_q );
  and and_60 (and_60_out, decoder_1_out3, \d触发器_带使能端_44_q );
  and and_61 (and_61_out, decoder_1_out4, \d触发器_带使能端_45_q );
  and and_62 (and_62_out, decoder_1_out5, \d触发器_带使能端_46_q );
  and and_63 (and_63_out, decoder_1_out6, \d触发器_带使能端_47_q );
  and and_64 (and_64_out, decoder_1_out7, \d触发器_带使能端_48_q );
  and and_65 (and_66_out[1], decoder_2_out0, or_6_out);
  or or_7 (or_7_out, and_64_out, and_63_out, and_62_out, and_61_out, and_60_out, and_59_out, and_58_out, and_57_out);
  and and_66 (and_66_out[0], decoder_2_out0, or_7_out);
  and and_67 (and_67_out, decoder_1_out0, \d触发器_带使能端_49_q );
  \D触发器_带使能端  \d触发器_带使能端_49  (.EN(and_2_out), .RESET(RESET_2), .clk(clk_out), .D(D_1), .Q(\d触发器_带使能端_49_q ));
  and and_68 (and_68_out, decoder_1_out1, \d触发器_带使能端_50_q );
  \D触发器_带使能端  \d触发器_带使能端_50  (.EN(and_3_out), .RESET(RESET_2), .clk(clk_out), .D(D_1), .Q(\d触发器_带使能端_50_q ));
  and and_69 (and_69_out, decoder_1_out2, \d触发器_带使能端_51_q );
  \D触发器_带使能端  \d触发器_带使能端_51  (.EN(and_4_out), .RESET(RESET_2), .clk(clk_out), .D(D_1), .Q(\d触发器_带使能端_51_q ));
  and and_70 (and_70_out, decoder_1_out3, \d触发器_带使能端_52_q );
  \D触发器_带使能端  \d触发器_带使能端_52  (.EN(and_5_out), .RESET(RESET_2), .clk(clk_out), .D(D_1), .Q(\d触发器_带使能端_52_q ));
  and and_71 (and_71_out, decoder_1_out4, \d触发器_带使能端_53_q );
  \D触发器_带使能端  \d触发器_带使能端_53  (.EN(and_6_out), .RESET(RESET_2), .clk(clk_out), .D(D_1), .Q(\d触发器_带使能端_53_q ));
  and and_72 (and_72_out, decoder_1_out5, \d触发器_带使能端_54_q );
  \D触发器_带使能端  \d触发器_带使能端_54  (.EN(and_7_out), .RESET(RESET_2), .clk(clk_out), .D(D_1), .Q(\d触发器_带使能端_54_q ));
  and and_73 (and_73_out, decoder_1_out6, \d触发器_带使能端_55_q );
  \D触发器_带使能端  \d触发器_带使能端_55  (.EN(and_8_out), .RESET(RESET_2), .clk(clk_out), .D(D_1), .Q(\d触发器_带使能端_55_q ));
  and and_74 (and_74_out, decoder_1_out7, \d触发器_带使能端_56_q );
  \D触发器_带使能端  \d触发器_带使能端_56  (.EN(and_9_out), .RESET(RESET_2), .clk(clk_out), .D(D_1), .Q(\d触发器_带使能端_56_q ));
  or or_8 (or_8_out, and_74_out, and_73_out, and_72_out, and_71_out, and_70_out, and_69_out, and_68_out, and_67_out);
  and and_75 (and_75_out, decoder_1_out0, \d触发器_带使能端_57_q );
  \D触发器_带使能端  \d触发器_带使能端_57  (.EN(and_2_out), .RESET(RESET_2), .clk(clk_out), .D(D_0), .Q(\d触发器_带使能端_57_q ));
  and and_76 (and_76_out, decoder_1_out1, \d触发器_带使能端_58_q );
  \D触发器_带使能端  \d触发器_带使能端_58  (.EN(and_3_out), .RESET(RESET_2), .clk(clk_out), .D(D_0), .Q(\d触发器_带使能端_58_q ));
  and and_77 (and_77_out, decoder_1_out2, \d触发器_带使能端_59_q );
  \D触发器_带使能端  \d触发器_带使能端_59  (.EN(and_4_out), .RESET(RESET_2), .clk(clk_out), .D(D_0), .Q(\d触发器_带使能端_59_q ));
  and and_78 (and_78_out, decoder_1_out3, \d触发器_带使能端_60_q );
  \D触发器_带使能端  \d触发器_带使能端_60  (.EN(and_5_out), .RESET(RESET_2), .clk(clk_out), .D(D_0), .Q(\d触发器_带使能端_60_q ));
  and and_79 (and_79_out, decoder_1_out4, \d触发器_带使能端_61_q );
  \D触发器_带使能端  \d触发器_带使能端_61  (.EN(and_6_out), .RESET(RESET_2), .clk(clk_out), .D(D_0), .Q(\d触发器_带使能端_61_q ));
  and and_80 (and_80_out, decoder_1_out5, \d触发器_带使能端_62_q );
  \D触发器_带使能端  \d触发器_带使能端_62  (.EN(and_7_out), .RESET(RESET_2), .clk(clk_out), .D(D_0), .Q(\d触发器_带使能端_62_q ));
  and and_81 (and_81_out, decoder_1_out6, \d触发器_带使能端_63_q );
  \D触发器_带使能端  \d触发器_带使能端_63  (.EN(and_8_out), .RESET(RESET_2), .clk(clk_out), .D(D_0), .Q(\d触发器_带使能端_63_q ));
  and and_82 (and_82_out, decoder_1_out7, \d触发器_带使能端_64_q );
  \D触发器_带使能端  \d触发器_带使能端_64  (.EN(and_9_out), .RESET(RESET_2), .clk(clk_out), .D(D_0), .Q(\d触发器_带使能端_64_q ));
  and and_83 (and_83_out[0], decoder_2_out0, or_9_out);
  and and_84 (and_83_out[1], decoder_2_out0, or_8_out);
  and and_85 (and_86_out[1], decoder_2_out3, or_8_out);
  or or_9 (or_9_out, and_82_out, and_81_out, and_80_out, and_79_out, and_78_out, and_77_out, and_76_out, and_75_out);
  and and_86 (and_86_out[0], decoder_2_out3, or_9_out);

  // Notes on the sheet:
  //   添加新指令out
  //   PC
  //   抛开循环部分已经实现，需要再加一行指令用来实现循环
endmodule
