// Logisim project 时序逻辑电路.circ as structural Verilog: 14 circuits, main circuit SR锁存器(NOR)
module \SR锁存器_NOR  (
  input  R,
  input  in_2,
  input  S,
  output out_4,
  output out_5
);

  wire and_1_out, and_2_out;

  and and_1 (and_1_out, R, in_2);
  and and_2 (and_2_out, in_2, S);
  nor nor_1 (out_4, and_1_out, out_5);
  nor nor_2 (out_5, out_4, and_2_out);
endmodule

module \S_R锁存器_NAND  (
  input  in_1,
  input  in_2,
  output out_3,
  output out_4
);

  nand nand_1 (out_3, in_1, out_4);
  nand nand_2 (out_4, out_3, in_2);
endmodule

module \D锁存器  (
  input  RESET,
  input  WE,
  input  D,
  output out_4,
  output Q
);

  wire and_1_out, and_2_out, not_1_out, not_2_out, or_1_out;

  not not_1 (not_1_out, D);
  not not_2 (not_2_out, RESET);
  and and_1 (and_1_out, not_2_out, D, WE);
  and and_2 (and_2_out, WE, not_1_out);
  or or_1 (or_1_out, and_2_out, RESET);
  nor nor_1 (out_4, and_1_out, Q);
  nor nor_2 (Q, out_4, or_1_out);

  // Notes on the sheet:
  //   S
  //   R
endmodule

module \D锁存器位翻转功能  (
  input  in_1,
  input  in_2
);

  wire \d锁存器_1_q , not_1_out;

  \D锁存器  \d锁存器_1  (.RESET(in_1), .WE(in_2), .D(not_1_out), .Q(\d锁存器_1_q ));  // open: out_4
  not not_1 (not_1_out, \d锁存器_1_q );
endmodule

module \D触发器_上升沿触发  (
  input  RESET,
  input  clk,
  input  D,
  output Q
);

  wire \d锁存器_1_q , not_1_out;

  not not_1 (not_1_out, clk);
  \D锁存器  \d锁存器_1  (.RESET(RESET), .WE(not_1_out), .D(D), .Q(\d锁存器_1_q ));  // open: out_4
  \D锁存器  \d锁存器_2  (.RESET(RESET), .WE(clk), .D(\d锁存器_1_q ), .Q(Q));  // open: out_4
endmodule

module \D触发器实现位翻转功能  (
  input  RESET,
  input  clk
);

  wire \d触发器_上升沿触发_1_q , not_1_out;

  \D触发器_上升沿触发  \d触发器_上升沿触发_1  (.RESET(RESET), .clk(clk), .D(not_1_out), .Q(\d触发器_上升沿触发_1_q ));
  not not_1 (not_1_out, \d触发器_上升沿触发_1_q );
endmodule

module \D触发器_下降沿触发  (
  input  RESET,
  input  clk,
  input  D,
  output Q
);

  wire \d锁存器_1_q , not_1_out, not_2_out;

  not not_1 (not_1_out, clk);
  not not_2 (not_2_out, not_1_out);
  \D锁存器  \d锁存器_1  (.RESET(RESET), .WE(not_2_out), .D(D), .Q(\d锁存器_1_q ));  // open: out_4
  \D锁存器  \d锁存器_2  (.RESET(RESET), .WE(not_1_out), .D(\d锁存器_1_q ), .Q(Q));  // open: out_4
endmodule

module \D触发器_带使能端  (
  input  EN,
  input  RESET,
  input  clk,
  input  D,
  output Q
);

  wire and_1_out, and_2_out, \d锁存器_1_q , not_1_out;

  not not_1 (not_1_out, clk);
  and and_1 (and_1_out, EN, clk);
  and and_2 (and_2_out, EN, not_1_out);
  \D锁存器  \d锁存器_1  (.RESET(RESET), .WE(and_2_out), .D(D), .Q(\d锁存器_1_q ));  // open: out_4
  \D锁存器  \d锁存器_2  (.RESET(RESET), .WE(and_1_out), .D(\d锁存器_1_q ), .Q(Q));  // open: out_4
endmodule

module \_4位寄存器  (
  input  D_0,
  input  D_1,
  input  D_2,
  input  D_3,
  input  EN,
  input  RESET,
  input  clk,
  output Q_0,
  output Q_1,
  output Q_2,
  output Q_3
);

  \D触发器_带使能端  \d触发器_带使能端_1  (.EN(EN), .RESET(RESET), .clk(clk), .D(D_0), .Q(Q_0));
  \D触发器_带使能端  \d触发器_带使能端_2  (.EN(EN), .RESET(RESET), .clk(clk), .D(D_1), .Q(Q_1));
  \D触发器_带使能端  \d触发器_带使能端_3  (.EN(EN), .RESET(RESET), .clk(clk), .D(D_2), .Q(Q_2));
  \D触发器_带使能端  \d触发器_带使能端_4  (.EN(EN), .RESET(RESET), .clk(clk), .D(D_3), .Q(Q_3));
endmodule

module \_4位计数器  (
  input  EN,
  input  RESET,
  input  clk,
  output [3:0] out_4
);

  wire adder_1_cout, adder_1_out, adder_2_cout, adder_2_out, adder_3_cout, adder_3_out, adder_4_out;

  \_4位寄存器  \u_4位寄存器_1  (
    .EN(EN), .RESET(RESET), .clk(clk), .D_0(adder_4_out), .D_1(adder_3_out), .D_2(adder_2_out),
    .D_3(adder_1_out), .Q_0(out_4[3]), .Q_1(out_4[2]), .Q_2(out_4[1]), .Q_3(out_4[0]));
  Adder #(.width(1)) adder_1 (.a(out_4[0]), .b(1'b1), .out(adder_1_out), .cin(1'b0), .cout(adder_1_cout));
  Adder #(.width(1)) adder_2 (.a(out_4[1]), .b(1'b0), .out(adder_2_out), .cin(adder_1_cout), .cout(adder_2_cout));
  Adder #(.width(1)) adder_3 (.a(out_4[2]), .b(1'b0), .out(adder_3_out), .cin(adder_2_cout), .cout(adder_3_cout));
  Adder #(.width(1)) adder_4 (.a(out_4[3]), .b(1'b0), .out(adder_4_out), .cin(adder_3_cout));  // open: cout
  Hex_Digit_Display hex_digit_display_1 (.value(out_4));  // open: dp
endmodule

module \_8位寄存器  (
  input  D_0,
  input  D_1,
  input  D_2,
  input  D_3,
  input  D_4,
  input  D_5,
  input  D_6,
  input  D_7,
  input  EN,
  input  RESET,
  input  clk,
  output Q_0,
  output Q_1,
  output Q_2,
  output Q_3,
  output Q_4,
  output Q_5,
  output Q_6,
  output Q_7
);

  \D触发器_带使能端  \d触发器_带使能端_1  (.EN(EN), .RESET(RESET), .clk(clk), .D(D_0), .Q(Q_0));
  \D触发器_带使能端  \d触发器_带使能端_2  (.EN(EN), .RESET(RESET), .clk(clk), .D(D_1), .Q(Q_1));
  \D触发器_带使能端  \d触发器_带使能端_3  (.EN(EN), .RESET(RESET), .clk(clk), .D(D_2), .Q(Q_2));
  \D触发器_带使能端  \d触发器_带使能端_4  (.EN(EN), .RESET(RESET), .clk(clk), .D(D_3), .Q(Q_3));
  \D触发器_带使能端  \d触发器_带使能端_5  (.EN(EN), .RESET(RESET), .clk(clk), .D(D_4), .Q(Q_4));
  \D触发器_带使能端  \d触发器_带使能端_6  (.EN(EN), .RESET(RESET), .clk(clk), .D(D_5), .Q(Q_5));
  \D触发器_带使能端  \d触发器_带使能端_7  (.EN(EN), .RESET(RESET), .clk(clk), .D(D_6), .Q(Q_6));
  \D触发器_带使能端  \d触发器_带使能端_8  (.EN(EN), .RESET(RESET), .clk(clk), .D(D_7), .Q(Q_7));
endmodule

module \数列求和电路  (
  input  EN,
  input  RESET,
  input  clk
);

  wire adder_1_cout, adder_1_out, adder_2_cout, adder_2_out, adder_3_cout, adder_3_out, adder_4_cout,
       adder_4_out, adder_5_cout, adder_5_out, adder_6_cout, adder_6_out, adder_7_cout, adder_7_out,
       adder_8_out, \n8位寄存器_1_q_0 , \n8位寄存器_1_q_1 , \n8位寄存器_1_q_2 , \n8位寄存器_1_q_3 , \n8位寄存器_1_q_4 ,
       \n8位寄存器_1_q_5 , \n8位寄存器_1_q_6 , \n8位寄存器_1_q_7 ;
  wire [3:0] \n4位计数器_1_out_4 ;

  \_4位计数器  \u_4位计数器_1  (.EN(EN), .RESET(RESET), .clk(clk), .out_4(\n4位计数器_1_out_4 ));
  Hex_Digit_Display hex_digit_display_1 (.value(\n4位计数器_1_out_4 ));  // open: dp
  \_8位寄存器  \u_8位寄存器_1  (
    .EN(EN), .RESET(RESET), .clk(clk), .D_0(adder_8_out), .D_1(adder_7_out), .D_2(adder_6_out),
    .D_3(adder_5_out), .D_4(adder_4_out), .D_5(adder_3_out), .D_6(adder_2_out), .D_7(adder_1_out),
    .Q_0(\n8位寄存器_1_q_0 ), .Q_1(\n8位寄存器_1_q_1 ), .Q_2(\n8位寄存器_1_q_2 ), .Q_3(\n8位寄存器_1_q_3 ),
    .Q_4(\n8位寄存器_1_q_4 ), .Q_5(\n8位寄存器_1_q_5 ), .Q_6(\n8位寄存器_1_q_6 ), .Q_7(\n8位寄存器_1_q_7 ));
  Adder #(.width(1)) adder_1 (
    .a(\n8位寄存器_1_q_7 ), .b(\n4位计数器_1_out_4 [0]), .out(adder_1_out), .cin(1'b0), .cout(adder_1_cout));
  Adder #(.width(1)) adder_2 (
    .a(\n8位寄存器_1_q_6 ), .b(\n4位计数器_1_out_4 [1]), .out(adder_2_out), .cin(adder_1_cout), .cout(adder_2_cout));
  Adder #(.width(1)) adder_3 (
    .a(\n8位寄存器_1_q_5 ), .b(\n4位计数器_1_out_4 [2]), .out(adder_3_out), .cin(adder_2_cout), .cout(adder_3_cout));
  Adder #(.width(1)) adder_4 (
    .a(\n8位寄存器_1_q_4 ), .b(\n4位计数器_1_out_4 [3]), .out(adder_4_out), .cin(adder_3_cout), .cout(adder_4_cout));
  Adder #(.width(1)) adder_5 (.a(\n8位寄存器_1_q_3 ), .b(1'b0), .out(adder_5_out), .cin(adder_4_cout), .cout(adder_5_cout));
  Adder #(.width(1)) adder_6 (.a(\n8位寄存器_1_q_2 ), .b(1'b0), .out(adder_6_out), .cin(adder_5_cout), .cout(adder_6_cout));
  Adder #(.width(1)) adder_7 (.a(\n8位寄存器_1_q_1 ), .b(1'b0), .out(adder_7_out), .cin(adder_6_cout), .cout(adder_7_cout));
  Adder #(.width(1)) adder_8 (.a(\n8位寄存器_1_q_0 ), .b(1'b0), .out(adder_8_out), .cin(adder_7_cout));  // open: cout
endmodule

module \电子时钟  (
  input  RESET,
  input  EN
);

  wire adder_1_cout, adder_1_out, adder_2_cout, adder_2_out, adder_3_cout, adder_3_out, adder_4_out,
       adder_5_cout, adder_5_out, adder_6_cout, adder_6_out, adder_7_cout, adder_7_out, adder_8_out,
       adder_9_cout, adder_9_out, adder_10_cout, adder_10_out, adder_11_cout, adder_11_out, adder_12_out,
       adder_13_cout, adder_13_out, adder_14_cout, adder_14_out, adder_15_cout, adder_15_out, adder_16_out,
       and_1_out, and_2_out, and_3_out, and_4_out, clk_out, \n4位寄存器_1_q_0 , \n4位寄存器_1_q_1 , \n4位寄存器_1_q_2 ,
       \n4位寄存器_1_q_3 , \n4位寄存器_2_q_0 , \n4位寄存器_2_q_1 , \n4位寄存器_2_q_2 , \n4位寄存器_2_q_3 , \n4位寄存器_3_q_0 ,
       \n4位寄存器_3_q_1 , \n4位寄存器_3_q_2 , \n4位寄存器_3_q_3 , \n4位寄存器_4_q_0 , \n4位寄存器_4_q_1 , \n4位寄存器_4_q_2 ,
       \n4位寄存器_4_q_3 , or_1_out, or_2_out, or_3_out, or_4_out, \七段数码管0_9_1_out_5 , \七段数码管0_9_1_out_6 ,
       \七段数码管0_9_1_out_7 , \七段数码管0_9_1_out_8 , \七段数码管0_9_1_out_9 , \七段数码管0_9_1_out_10 , \七段数码管0_9_1_out_11 ,
       \七段数码管0_9_2_out_5 , \七段数码管0_9_2_out_6 , \七段数码管0_9_2_out_7 , \七段数码管0_9_2_out_8 , \七段数码管0_9_2_out_9 ,
       \七段数码管0_9_2_out_10 , \七段数码管0_9_2_out_11 , \七段数码管0_9_3_out_5 , \七段数码管0_9_3_out_6 , \七段数码管0_9_3_out_7 ,
       \七段数码管0_9_3_out_8 , \七段数码管0_9_3_out_9 , \七段数码管0_9_3_out_10 , \七段数码管0_9_3_out_11 , \七段数码管0_9_4_out_5 ,
       \七段数码管0_9_4_out_6 , \七段数码管0_9_4_out_7 , \七段数码管0_9_4_out_8 , \七段数码管0_9_4_out_9 , \七段数码管0_9_4_out_10 ,
       \七段数码管0_9_4_out_11 ;

  and and_1 (and_1_out, \n4位寄存器_1_q_1 , \n4位寄存器_1_q_2 );
  \_4位寄存器  \u_4位寄存器_1  (
    .EN(EN), .RESET(or_1_out), .clk(and_2_out), .D_0(adder_4_out), .D_1(adder_3_out), .D_2(adder_2_out),
    .D_3(adder_1_out), .Q_0(\n4位寄存器_1_q_0 ), .Q_1(\n4位寄存器_1_q_1 ), .Q_2(\n4位寄存器_1_q_2 ), .Q_3(\n4位寄存器_1_q_3 ));
  or or_1 (or_1_out, RESET, and_1_out);
  \七段数码管0_9  \u_七段数码管0_9_1  (
    .in_1(\n4位寄存器_1_q_3 ), .in_2(\n4位寄存器_1_q_2 ), .in_3(\n4位寄存器_1_q_1 ), .in_4(\n4位寄存器_1_q_0 ),
    .out_5(\七段数码管0_9_1_out_5 ), .out_6(\七段数码管0_9_1_out_6 ), .out_7(\七段数码管0_9_1_out_7 ),
    .out_8(\七段数码管0_9_1_out_8 ), .out_9(\七段数码管0_9_1_out_9 ), .out_10(\七段数码管0_9_1_out_10 ),
    .out_11(\七段数码管0_9_1_out_11 ));
  Adder #(.width(1)) adder_1 (.a(\n4位寄存器_1_q_3 ), .b(1'b1), .out(adder_1_out), .cin(1'b0), .cout(adder_1_cout));
  Adder #(.width(1)) adder_2 (.a(\n4位寄存器_1_q_2 ), .b(1'b0), .out(adder_2_out), .cin(adder_1_cout), .cout(adder_2_cout));
  Adder #(.width(1)) adder_3 (.a(\n4位寄存器_1_q_1 ), .b(1'b0), .out(adder_3_out), .cin(adder_2_cout), .cout(adder_3_cout));
  Adder #(.width(1)) adder_4 (.a(\n4位寄存器_1_q_0 ), .b(1'b0), .out(adder_4_out), .cin(adder_3_cout));  // open: cout
  _7_Segment_Display u_7_segment_display_1 (
    .g(\七段数码管0_9_1_out_5 ), .f(\七段数码管0_9_1_out_6 ), .a(\七段数码管0_9_1_out_7 ), .b(\七段数码管0_9_1_out_8 ),
    .e(\七段数码管0_9_1_out_9 ), .d(\七段数码管0_9_1_out_10 ), .c(\七段数码管0_9_1_out_11 ));  // open: dp
  and and_2 (and_2_out, \n4位寄存器_2_q_0 , \n4位寄存器_2_q_2 );
  or or_2 (or_2_out, RESET, and_2_out);
  \_4位寄存器  \u_4位寄存器_2  (
    .EN(EN), .RESET(or_2_out), .clk(and_3_out), .D_0(adder_8_out), .D_1(adder_7_out), .D_2(adder_6_out),
    .D_3(adder_5_out), .Q_0(\n4位寄存器_2_q_0 ), .Q_1(\n4位寄存器_2_q_1 ), .Q_2(\n4位寄存器_2_q_2 ), .Q_3(\n4位寄存器_2_q_3 ));
  \七段数码管0_9  \u_七段数码管0_9_2  (
    .in_1(\n4位寄存器_2_q_3 ), .in_2(\n4位寄存器_2_q_2 ), .in_3(\n4位寄存器_2_q_1 ), .in_4(\n4位寄存器_2_q_0 ),
    .out_5(\七段数码管0_9_2_out_5 ), .out_6(\七段数码管0_9_2_out_6 ), .out_7(\七段数码管0_9_2_out_7 ),
    .out_8(\七段数码管0_9_2_out_8 ), .out_9(\七段数码管0_9_2_out_9 ), .out_10(\七段数码管0_9_2_out_10 ),
    .out_11(\七段数码管0_9_2_out_11 ));
  Adder #(.width(1)) adder_5 (.a(\n4位寄存器_2_q_3 ), .b(1'b1), .out(adder_5_out), .cin(1'b0), .cout(adder_5_cout));
  Adder #(.width(1)) adder_6 (.a(\n4位寄存器_2_q_2 ), .b(1'b0), .out(adder_6_out), .cin(adder_5_cout), .cout(adder_6_cout));
  Adder #(.width(1)) adder_7 (.a(\n4位寄存器_2_q_1 ), .b(1'b0), .out(adder_7_out), .cin(adder_6_cout), .cout(adder_7_cout));
  Adder #(.width(1)) adder_8 (.a(\n4位寄存器_2_q_0 ), .b(1'b0), .out(adder_8_out), .cin(adder_7_cout));  // open: cout
  _7_Segment_Display u_7_segment_display_2 (
    .g(\七段数码管0_9_2_out_5 ), .f(\七段数码管0_9_2_out_6 ), .a(\七段数码管0_9_2_out_7 ), .b(\七段数码管0_9_2_out_8 ),
    .e(\七段数码管0_9_2_out_9 ), .d(\七段数码管0_9_2_out_10 ), .c(\七段数码管0_9_2_out_11 ));  // open: dp
  and and_3 (and_3_out, \n4位寄存器_3_q_1 , \n4位寄存器_3_q_2 );
  \_4位寄存器  \u_4位寄存器_3  (
    .EN(EN), .RESET(or_3_out), .clk(and_4_out), .D_0(adder_12_out), .D_1(adder_11_out), .D_2(adder_10_out),
    .D_3(adder_9_out), .Q_0(\n4位寄存器_3_q_0 ), .Q_1(\n4位寄存器_3_q_1 ), .Q_2(\n4位寄存器_3_q_2 ), .Q_3(\n4位寄存器_3_q_3 ));
  or or_3 (or_3_out, RESET, and_3_out);
  \七段数码管0_9  \u_七段数码管0_9_3  (
    .in_1(\n4位寄存器_3_q_3 ), .in_2(\n4位寄存器_3_q_2 ), .in_3(\n4位寄存器_3_q_1 ), .in_4(\n4位寄存器_3_q_0 ),
    .out_5(\七段数码管0_9_3_out_5 ), .out_6(\七段数码管0_9_3_out_6 ), .out_7(\七段数码管0_9_3_out_7 ),
    .out_8(\七段数码管0_9_3_out_8 ), .out_9(\七段数码管0_9_3_out_9 ), .out_10(\七段数码管0_9_3_out_10 ),
    .out_11(\七段数码管0_9_3_out_11 ));
  Adder #(.width(1)) adder_9 (.a(\n4位寄存器_3_q_3 ), .b(1'b1), .out(adder_9_out), .cin(1'b0), .cout(adder_9_cout));
  Adder #(.width(1)) adder_10 (
    .a(\n4位寄存器_3_q_2 ), .b(1'b0), .out(adder_10_out), .cin(adder_9_cout), .cout(adder_10_cout));
  Adder #(.width(1)) adder_11 (
    .a(\n4位寄存器_3_q_1 ), .b(1'b0), .out(adder_11_out), .cin(adder_10_cout), .cout(adder_11_cout));
  Adder #(.width(1)) adder_12 (.a(\n4位寄存器_3_q_0 ), .b(1'b0), .out(adder_12_out), .cin(adder_11_cout));  // open: cout
  _7_Segment_Display u_7_segment_display_3 (
    .g(\七段数码管0_9_3_out_5 ), .f(\七段数码管0_9_3_out_6 ), .a(\七段数码管0_9_3_out_7 ), .b(\七段数码管0_9_3_out_8 ),
    .e(\七段数码管0_9_3_out_9 ), .d(\七段数码管0_9_3_out_10 ), .c(\七段数码管0_9_3_out_11 ));  // open: dp
  or or_4 (or_4_out, RESET, and_4_out);
  Clock clk (.out(clk_out));
  and and_4 (and_4_out, \n4位寄存器_4_q_0 , \n4位寄存器_4_q_2 );
  \_4位寄存器  \u_4位寄存器_4  (
    .EN(EN), .RESET(or_4_out), .clk(clk_out), .D_0(adder_16_out), .D_1(adder_15_out), .D_2(adder_14_out),
    .D_3(adder_13_out), .Q_0(\n4位寄存器_4_q_0 ), .Q_1(\n4位寄存器_4_q_1 ), .Q_2(\n4位寄存器_4_q_2 ), .Q_3(\n4位寄存器_4_q_3 ));
  \七段数码管0_9  \u_七段数码管0_9_4  (
    .in_1(\n4位寄存器_4_q_3 ), .in_2(\n4位寄存器_4_q_2 ), .in_3(\n4位寄存器_4_q_1 ), .in_4(\n4位寄存器_4_q_0 ),
    .out_5(\七段数码管0_9_4_out_5 ), .out_6(\七段数码管0_9_4_out_6 ), .out_7(\七段数码管0_9_4_out_7 ),
    .out_8(\七段数码管0_9_4_out_8 ), .out_9(\七段数码管0_9_4_out_9 ), .out_10(\七段数码管0_9_4_out_10 ),
    .out_11(\七段数码管0_9_4_out_11 ));
  _7_Segment_Display u_7_segment_display_4 (
    .g(\七段数码管0_9_4_out_5 ), .f(\七段数码管0_9_4_out_6 ), .a(\七段数码管0_9_4_out_7 ), .b(\七段数码管0_9_4_out_8 ),
    .e(\七段数码管0_9_4_out_9 ), .d(\七段数码管0_9_4_out_10 ), .c(\七段数码管0_9_4_out_11 ));  // open: dp
  Adder #(.width(1)) adder_13 (.a(\n4位寄存器_4_q_3 ), .b(1'b1), .out(adder_13_out), .cin(1'b0), .cout(adder_13_cout));
  Adder #(.width(1)) adder_14 (
    .a(\n4位寄存器_4_q_2 ), .b(1'b0), .out(adder_14_out), .cin(adder_13_cout), .cout(adder_14_cout));
  Adder #(.width(1)) adder_15 (
    .a(\n4位寄存器_4_q_1 ), .b(1'b0), .out(adder_15_out), .cin(adder_14_cout), .cout(adder_15_cout));
  Adder #(.width(1)) adder_16 (.a(\n4位寄存器_4_q_0 ), .b(1'b0), .out(adder_16_out), .cin(adder_15_cout));  // open: cout
endmodule

module \七段数码管0_9  (
  input  in_1,
  input  in_2,
  input  in_3,
  input  in_4,
  output out_5,
  output out_6,
  output out_7,
  output out_8,
  output out_9,
  output out_10,
  output out_11
);

  wire decoder_1_out0, decoder_1_out1, decoder_1_out2, decoder_1_out3, decoder_1_out4, decoder_1_out5,
       decoder_1_out6, decoder_1_out7, decoder_1_out8, decoder_1_out9;

  Decoder #(.select(4), .enable("false")) decoder_1 (
    .out0(decoder_1_out0), .out1(decoder_1_out1), .out2(decoder_1_out2), .out3(decoder_1_out3),
    .out4(decoder_1_out4), .out5(decoder_1_out5), .out6(decoder_1_out6), .out7(decoder_1_out7),
    .out8(decoder_1_out8), .out9(decoder_1_out9), .sel({in_4, in_3, in_2, in_1}));  // open: out10, out11, out12, out13, out14, out15
  or or_1 (out_5, decoder_1_out2, decoder_1_out3, decoder_1_out4, decoder_1_out5, decoder_1_out6, decoder_1_out8, decoder_1_out9);
  or or_2 (out_6, decoder_1_out0, decoder_1_out4, decoder_1_out5, decoder_1_out6, decoder_1_out8, decoder_1_out9);
  or or_3 (out_7, decoder_1_out0, decoder_1_out2, decoder_1_out3, decoder_1_out5, decoder_1_out6, decoder_1_out7, decoder_1_out8, decoder_1_out9);
  or or_4 (out_8, decoder_1_out0, decoder_1_out1, decoder_1_out2, decoder_1_out3, decoder_1_out4, decoder_1_out7, decoder_1_out8, decoder_1_out9);
  or or_5 (out_9, decoder_1_out0, decoder_1_out2, decoder_1_out6, decoder_1_out8);
  or or_6 (out_10, decoder_1_out0, decoder_1_out2, decoder_1_out3, decoder_1_out5, decoder_1_out6, decoder_1_out8, decoder_1_out9);
  or or_7 (out_11, decoder_1_out0, decoder_1_out1, decoder_1_out3, decoder_1_out4, decoder_1_out5, decoder_1_out6, decoder_1_out7, decoder_1_out8, decoder_1_out9);
  _7_Segment_Display u_7_segment_display_1 (
    .g(out_5), .f(out_6), .a(out_7), .b(out_8), .e(out_9), .d(out_10), .c(out_11));  // open: dp
endmodule
