// Logisim project 编码器.circ as structural Verilog: 2 circuits, main circuit 16-4 encoder
module _16_4_encoder (
  input  _0,
  input  _1,
  input  _2,
  input  _3,
  input  _4,
  input  _5,
  input  _6,
  input  _7,
  input  _8,
  input  _9,
  input  _10,
  input  _11,
  input  _12,
  input  _13,
  input  _14,
  input  _15
);

  wire or_1_out, or_2_out, or_3_out, or_4_out, or_5_out;

  or or_1 (or_1_out, _0, _1, _2, _3, _4, _5, _6, _7, _8, _9, _10, _11, _12, _13, _14, _15);
  or or_2 (or_2_out, _0, _2, _4, _6, _8, _10, _12, _14);
  or or_3 (or_3_out, _0, _1, _4, _5, _8, _9, _12, _13);
  or or_4 (or_4_out, _0, _1, _2, _10, _8, _9, _3, _11);
  or or_5 (or_5_out, _0, _1, _2, _3, _4, _5, _6, _7);
  _7_Segment_Display u_7_segment_display_1 (
    .f(or_5_out), .a(or_5_out), .b(or_1_out), .e(or_5_out), .d(or_5_out), .c(or_1_out));  // open: g, dp
  _7_Segment_Display u_7_segment_display_2 (
    .f(or_4_out), .a(or_4_out), .b(or_1_out), .e(or_4_out), .d(or_4_out), .c(or_1_out));  // open: g, dp
  _7_Segment_Display u_7_segment_display_3 (
    .f(or_3_out), .a(or_3_out), .b(or_1_out), .e(or_3_out), .d(or_3_out), .c(or_1_out));  // open: g, dp
  _7_Segment_Display u_7_segment_display_4 (
    .f(or_2_out), .a(or_2_out), .b(or_1_out), .e(or_2_out), .d(or_2_out), .c(or_1_out));  // open: g, dp
endmodule

module _4_2_priority_encoder (
  input  in_1,
  input  in_2,
  input  in_3,
  input  in_4,
  output out_5,
  output out_6
);

  wire and_1_out, and_2_out, not_1_out, not_2_out, undriven;

  not not_1 (not_1_out, in_3);
  not not_2 (not_2_out, in_4);
  and and_1 (and_1_out, in_2, not_1_out, not_2_out);
  and and_2 (and_2_out, in_3, not_2_out);
  or or_1 (out_6, and_1_out, in_4);
  or or_2 (out_5, and_2_out, in_4);
  _7_Segment_Display u_7_segment_display_1 (
    .g(undriven), .f(undriven), .a(undriven), .b(undriven), .e(undriven), .d(undriven), .c(undriven));  // open: dp
  _7_Segment_Display u_7_segment_display_2 (
    .f(undriven), .a(undriven), .b(undriven), .e(undriven), .d(undriven), .c(undriven), .dp(undriven));  // open: g
endmodule
