// Logisim project 译码器.circ as structural Verilog: 5 circuits, main circuit 2-4 decoder
module _2_4_decoder (
  input  A0,
  input  A1,
  output out_3,
  output out_4,
  output out_5,
  output out_6
);

  wire not_1_out, not_2_out;

  not not_1 (not_1_out, A0);
  not not_2 (not_2_out, A1);
  and and_1 (out_3, not_1_out, not_2_out);
  and and_2 (out_4, A0, not_2_out);
  and and_3 (out_5, not_1_out, A1);
  and and_4 (out_6, A0, A1);
endmodule

module _3_8_decoder (
  input  A0,
  input  A1,
  input  A2,
  output out_4,
  output out_5,
  output out_6,
  output out_7,
  output out_8,
  output out_9,
  output out_10,
  output out_11
);

  wire n2_4_decoder_1_out_3, n2_4_decoder_1_out_4, n2_4_decoder_1_out_5, n2_4_decoder_1_out_6,
       n2_4_decoder_2_out_3, n2_4_decoder_2_out_4, n2_4_decoder_2_out_5, n2_4_decoder_2_out_6, not_1_out;

  _2_4_decoder u_2_4_decoder_1 (
    .A0(A0), .A1(A1), .out_3(n2_4_decoder_1_out_3), .out_4(n2_4_decoder_1_out_4),
    .out_5(n2_4_decoder_1_out_5), .out_6(n2_4_decoder_1_out_6));
  _2_4_decoder u_2_4_decoder_2 (
    .A0(A0), .A1(A1), .out_3(n2_4_decoder_2_out_3), .out_4(n2_4_decoder_2_out_4),
    .out_5(n2_4_decoder_2_out_5), .out_6(n2_4_decoder_2_out_6));
  not not_1 (not_1_out, A2);
  and and_1 (out_4, n2_4_decoder_1_out_3, not_1_out);
  and and_2 (out_5, n2_4_decoder_1_out_4, not_1_out);
  and and_3 (out_6, n2_4_decoder_1_out_5, not_1_out);
  and and_4 (out_7, n2_4_decoder_1_out_6, not_1_out);
  and and_5 (out_8, n2_4_decoder_2_out_3, A2);
  and and_6 (out_9, n2_4_decoder_2_out_4, A2);
  and and_7 (out_10, n2_4_decoder_2_out_5, A2);
  and and_8 (out_11, n2_4_decoder_2_out_6, A2);
endmodule

module _4_16_decoder (
  input  A0,
  input  A1,
  input  A2,
  input  A3,
  output out_5,
  output out_6,
  output out_7,
  output out_8,
  output out_9,
  output out_10,
  output out_11,
  output out_12,
  output out_13,
  output out_14,
  output out_15,
  output out_16,
  output out_17,
  output out_18,
  output out_19,
  output out_20
);

  wire n3_8_decoder_1_out_4, n3_8_decoder_1_out_5, n3_8_decoder_1_out_6, n3_8_decoder_1_out_7,
       n3_8_decoder_1_out_8, n3_8_decoder_1_out_9, n3_8_decoder_1_out_10, n3_8_decoder_1_out_11,
       n3_8_decoder_2_out_4, n3_8_decoder_2_out_5, n3_8_decoder_2_out_6, n3_8_decoder_2_out_7,
       n3_8_decoder_2_out_8, n3_8_decoder_2_out_9, n3_8_decoder_2_out_10, n3_8_decoder_2_out_11, not_1_out;

  not not_1 (not_1_out, A3);
  _3_8_decoder u_3_8_decoder_1 (
    .A0(A0), .A1(A1), .A2(A2), .out_4(n3_8_decoder_1_out_4), .out_5(n3_8_decoder_1_out_5),
    .out_6(n3_8_decoder_1_out_6), .out_7(n3_8_decoder_1_out_7), .out_8(n3_8_decoder_1_out_8),
    .out_9(n3_8_decoder_1_out_9), .out_10(n3_8_decoder_1_out_10), .out_11(n3_8_decoder_1_out_11));
  _3_8_decoder u_3_8_decoder_2 (
    .A0(A0), .A1(A1), .A2(A2), .out_4(n3_8_decoder_2_out_4), .out_5(n3_8_decoder_2_out_5),
    .out_6(n3_8_decoder_2_out_6), .out_7(n3_8_decoder_2_out_7), .out_8(n3_8_decoder_2_out_8),
    .out_9(n3_8_decoder_2_out_9), .out_10(n3_8_decoder_2_out_10), .out_11(n3_8_decoder_2_out_11));
  and and_1 (out_5, n3_8_decoder_1_out_4, not_1_out);
  and and_2 (out_6, n3_8_decoder_1_out_5, not_1_out);
  and and_3 (out_7, n3_8_decoder_1_out_6, not_1_out);
  and and_4 (out_8, n3_8_decoder_1_out_7, not_1_out);
  and and_5 (out_9, n3_8_decoder_1_out_8, not_1_out);
  and and_6 (out_10, n3_8_decoder_1_out_9, not_1_out);
  and and_7 (out_11, n3_8_decoder_1_out_10, not_1_out);
  and and_8 (out_12, n3_8_decoder_1_out_11, not_1_out);
  and and_9 (out_13, n3_8_decoder_2_out_4, A3);
  and and_10 (out_14, n3_8_decoder_2_out_5, A3);
  and and_11 (out_15, n3_8_decoder_2_out_6, A3);
  and and_12 (out_16, n3_8_decoder_2_out_7, A3);
  and and_13 (out_17, n3_8_decoder_2_out_8, A3);
  and and_14 (out_18, n3_8_decoder_2_out_9, A3);
  and and_15 (out_19, n3_8_decoder_2_out_10, A3);
  and and_16 (out_20, n3_8_decoder_2_out_11, A3);
endmodule

module \七段数码管_0_9  (
  input  in_1,
  input  in_2,
  input  in_3,
  input  in_4
);

  wire n4_16_decoder_1_out_5, n4_16_decoder_1_out_6, n4_16_decoder_1_out_7, n4_16_decoder_1_out_8,
       n4_16_decoder_1_out_9, n4_16_decoder_1_out_10, n4_16_decoder_1_out_11, n4_16_decoder_1_out_12,
       n4_16_decoder_1_out_13, n4_16_decoder_1_out_14, or_1_out, or_2_out, or_3_out, or_4_out, or_5_out,
       or_6_out, or_7_out;

  _4_16_decoder u_4_16_decoder_1 (
    .A0(in_1), .A1(in_2), .A2(in_3), .A3(in_4), .out_5(n4_16_decoder_1_out_5), .out_6(n4_16_decoder_1_out_6),
    .out_7(n4_16_decoder_1_out_7), .out_8(n4_16_decoder_1_out_8), .out_9(n4_16_decoder_1_out_9),
    .out_10(n4_16_decoder_1_out_10), .out_11(n4_16_decoder_1_out_11), .out_12(n4_16_decoder_1_out_12),
    .out_13(n4_16_decoder_1_out_13), .out_14(n4_16_decoder_1_out_14));  // open: out_15, out_16, out_17, out_18, out_19, out_20
  or or_1 (or_1_out, n4_16_decoder_1_out_7, n4_16_decoder_1_out_8, n4_16_decoder_1_out_9, n4_16_decoder_1_out_10, n4_16_decoder_1_out_11, n4_16_decoder_1_out_13, n4_16_decoder_1_out_14);
  or or_2 (or_2_out, n4_16_decoder_1_out_5, n4_16_decoder_1_out_9, n4_16_decoder_1_out_10, n4_16_decoder_1_out_11, n4_16_decoder_1_out_13, n4_16_decoder_1_out_14);
  or or_3 (or_3_out, n4_16_decoder_1_out_5, n4_16_decoder_1_out_7, n4_16_decoder_1_out_8, n4_16_decoder_1_out_10, n4_16_decoder_1_out_11, n4_16_decoder_1_out_12, n4_16_decoder_1_out_13, n4_16_decoder_1_out_14);
  or or_4 (or_4_out, n4_16_decoder_1_out_5, n4_16_decoder_1_out_6, n4_16_decoder_1_out_7, n4_16_decoder_1_out_8, n4_16_decoder_1_out_9, n4_16_decoder_1_out_12, n4_16_decoder_1_out_13, n4_16_decoder_1_out_14);
  or or_5 (or_5_out, n4_16_decoder_1_out_5, n4_16_decoder_1_out_7, n4_16_decoder_1_out_11, n4_16_decoder_1_out_13);
  or or_6 (or_6_out, n4_16_decoder_1_out_5, n4_16_decoder_1_out_7, n4_16_decoder_1_out_8, n4_16_decoder_1_out_10, n4_16_decoder_1_out_11, n4_16_decoder_1_out_13, n4_16_decoder_1_out_14);
  or or_7 (or_7_out, n4_16_decoder_1_out_5, n4_16_decoder_1_out_6, n4_16_decoder_1_out_8, n4_16_decoder_1_out_9, n4_16_decoder_1_out_10, n4_16_decoder_1_out_11, n4_16_decoder_1_out_12, n4_16_decoder_1_out_13, n4_16_decoder_1_out_14);
  _7_Segment_Display u_7_segment_display_1 (
    .g(or_1_out), .f(or_2_out), .a(or_3_out), .b(or_4_out), .e(or_5_out), .d(or_6_out), .c(or_7_out));  // open: dp
endmodule

module \七段数码管_10_15  (
  input  in_1,
  input  in_2,
  input  in_3,
  input  in_4
);

  wire n4_16_decoder_1_out_15, n4_16_decoder_1_out_16, n4_16_decoder_1_out_17, n4_16_decoder_1_out_18,
       n4_16_decoder_1_out_19, n4_16_decoder_1_out_20, or_1_out, or_2_out, or_3_out, or_4_out, or_5_out,
       or_6_out, or_7_out;

  _4_16_decoder u_4_16_decoder_1 (
    .A0(in_1), .A1(in_2), .A2(in_3), .A3(in_4), .out_15(n4_16_decoder_1_out_15),
    .out_16(n4_16_decoder_1_out_16), .out_17(n4_16_decoder_1_out_17), .out_18(n4_16_decoder_1_out_18),
    .out_19(n4_16_decoder_1_out_19), .out_20(n4_16_decoder_1_out_20));  // open: out_5, out_6, out_7, out_8, out_9, out_10, out_11, out_12, out_13, out_14
  or or_1 (or_1_out, n4_16_decoder_1_out_15, n4_16_decoder_1_out_16, n4_16_decoder_1_out_18, n4_16_decoder_1_out_19, n4_16_decoder_1_out_20);
  or or_2 (or_2_out, n4_16_decoder_1_out_15, n4_16_decoder_1_out_16, n4_16_decoder_1_out_17, n4_16_decoder_1_out_19, n4_16_decoder_1_out_20);
  or or_3 (or_3_out, n4_16_decoder_1_out_15, n4_16_decoder_1_out_17, n4_16_decoder_1_out_19, n4_16_decoder_1_out_20);
  or or_4 (or_4_out, n4_16_decoder_1_out_15, n4_16_decoder_1_out_18);
  or or_5 (or_5_out, n4_16_decoder_1_out_15, n4_16_decoder_1_out_16, n4_16_decoder_1_out_17, n4_16_decoder_1_out_18, n4_16_decoder_1_out_19, n4_16_decoder_1_out_20);
  or or_6 (or_6_out, n4_16_decoder_1_out_16, n4_16_decoder_1_out_17, n4_16_decoder_1_out_18, n4_16_decoder_1_out_19);
  or or_7 (or_7_out, n4_16_decoder_1_out_15, n4_16_decoder_1_out_16, n4_16_decoder_1_out_18);
  _7_Segment_Display u_7_segment_display_1 (
    .g(or_1_out), .f(or_2_out), .a(or_3_out), .b(or_4_out), .e(or_5_out), .d(or_6_out), .c(or_7_out));  // open: dp
endmodule
